// Logisim project ALU.circ as structural Verilog: 6 circuits, main circuit ALU
module ALU (
  input  [15:0] A,
  input  [15:0] B,
  input  F0,
  input  F1,
  input  F2,
  output [7:0] Result,
  output C,
  output Z
);

  wire adder_1_c_out, controlled_buffer_1_out, multiplication_1_c, or_2_out, or_3_out, subtractor_1_c_out;
  wire [1:0] multiplexer_2_out;
  wire [7:0] adder_1_result, AND_out, multiplication_1_r, NOT_out, OR_out, subtractor_1_result, XOR_out;

  Adder adder_1 (.A(A[7:0]), .B(B[7:0]), .C_in(1'b0), .C_out(adder_1_c_out), .Result(adder_1_result));
  Subtractor subtractor_1 (
    .A(A[7:0]), .B(B[7:0]), .C_in(1'b0), .C_out(subtractor_1_c_out), .Result(subtractor_1_result));
  Multiplication multiplication_1 (.A(A[7:0]), .B(B[7:0]), .R(multiplication_1_r), .C(multiplication_1_c));
  assign AND_out = A[7:0] & B[7:0];  // AND_Gate AND, 8 bits wide
  assign OR_out = A[7:0] | B[7:0];  // OR_Gate OR, 8 bits wide
  assign NOT_out = ~A[7:0];  // NOT_Gate NOT, 8 bits wide
  assign XOR_out = A[7:0] ^ B[7:0];  // XOR_Gate XOR, 8 bits wide
  Multiplexer #(.select(3), .width(8)) multiplexer_1 (
    .in0(A[7:0]), .in1(adder_1_result), .in2(subtractor_1_result), .in3(multiplication_1_r), .in4(AND_out),
    .in5(OR_out), .in6(NOT_out), .in7(XOR_out), .out(Result), .sel({F2, F1, F0}));  // open: en
  Multiplexer #(.select(3)) multiplexer_2 (
    .in0(1'b0), .in1(adder_1_c_out), .in2(subtractor_1_c_out), .in3(multiplication_1_c), .in4(1'b0),
    .in5(1'b0), .in6(1'b0), .in7(1'b0), .out(multiplexer_2_out[0]), .sel({F2, F1, F0}));  // open: en
  or or_2 (or_2_out, Result[0], Result[1], Result[2], Result[3], Result[4], Result[5], Result[6], Result[7]);
  not not_2 (multiplexer_2_out[1], or_2_out);
  assign controlled_buffer_1_out = or_3_out ? 1'b1 : 1'bz;  // Controlled_Buffer controlled_buffer_1
  or or_3 (or_3_out, F0, F1, F2);
  Register #(.width(2), .trigger("high")) register_1 (
    .D(multiplexer_2_out), .Q({Z, C}), .clk(controlled_buffer_1_out));  // open: en, clr
endmodule

// +
module Adder (
  input  [7:0] A,
  input  [7:0] B,
  input  C_in,
  output C_out,
  output [7:0] Result
);

  wire full_adder_1_c_out, full_adder_2_c_out, full_adder_3_c_out, full_adder_4_c_out, full_adder_5_c_out,
       full_adder_6_c_out, full_adder_7_c_out;

  Full_adder full_adder_1 (.A(A[0]), .B(B[0]), .C_in(C_in), .Sum(Result[0]), .C_out(full_adder_1_c_out));
  Full_adder full_adder_2 (.A(A[1]), .B(B[1]), .C_in(full_adder_1_c_out), .Sum(Result[1]), .C_out(full_adder_2_c_out));
  Full_adder full_adder_3 (.A(A[2]), .B(B[2]), .C_in(full_adder_2_c_out), .Sum(Result[2]), .C_out(full_adder_3_c_out));
  Full_adder full_adder_4 (.A(A[3]), .B(B[3]), .C_in(full_adder_3_c_out), .Sum(Result[3]), .C_out(full_adder_4_c_out));
  Full_adder full_adder_5 (.A(A[4]), .B(B[4]), .C_in(full_adder_4_c_out), .Sum(Result[4]), .C_out(full_adder_5_c_out));
  Full_adder full_adder_6 (.A(A[5]), .B(B[5]), .C_in(full_adder_5_c_out), .Sum(Result[5]), .C_out(full_adder_6_c_out));
  Full_adder full_adder_7 (.A(A[6]), .B(B[6]), .C_in(full_adder_6_c_out), .Sum(Result[6]), .C_out(full_adder_7_c_out));
  Full_adder full_adder_8 (.A(A[7]), .B(B[7]), .C_in(full_adder_7_c_out), .Sum(Result[7]), .C_out(C_out));
endmodule

// -
module Subtractor (
  input  [7:0] A,
  input  [7:0] B,
  input  C_in,
  output C_out,
  output [7:0] Result
);

  wire and_1_out, and_2_out, and_3_out, and_4_out, and_5_out, and_6_out, and_7_out, and_8_out, and_9_out,
       and_10_out, and_11_out, and_12_out, and_13_out, and_14_out, and_15_out, and_16_out, not_1_out,
       not_2_out, not_3_out, not_4_out, not_5_out, not_6_out, not_7_out, not_8_out, not_9_out, not_10_out,
       not_11_out, not_12_out, not_13_out, not_14_out, not_15_out, not_16_out, or_1_out, or_2_out, or_3_out,
       or_4_out, or_5_out, or_6_out, or_7_out, xor_1_out, xor_3_out, xor_5_out, xor_7_out, xor_9_out,
       xor_11_out, xor_13_out, xor_15_out;

  xor xor_1 (xor_1_out, A[0], B[0]);
  not not_1 (not_1_out, xor_1_out);
  not not_2 (not_2_out, A[0]);
  and and_1 (and_1_out, not_1_out, C_in);
  and and_2 (and_2_out, not_2_out, B[0]);
  xor xor_2 (Result[0], xor_1_out, C_in);
  or or_1 (or_1_out, and_1_out, and_2_out);
  xor xor_3 (xor_3_out, A[1], B[1]);
  not not_3 (not_3_out, A[1]);
  not not_4 (not_4_out, xor_3_out);
  xor xor_4 (Result[1], xor_3_out, or_1_out);
  and and_3 (and_3_out, not_4_out, or_1_out);
  and and_4 (and_4_out, not_3_out, B[1]);
  or or_2 (or_2_out, and_3_out, and_4_out);
  xor xor_5 (xor_5_out, A[2], B[2]);
  not not_5 (not_5_out, xor_5_out);
  not not_6 (not_6_out, A[2]);
  xor xor_6 (Result[2], xor_5_out, or_2_out);
  and and_5 (and_5_out, not_5_out, or_2_out);
  and and_6 (and_6_out, not_6_out, B[2]);
  or or_3 (or_3_out, and_5_out, and_6_out);
  xor xor_7 (xor_7_out, A[3], B[3]);
  not not_7 (not_7_out, xor_7_out);
  not not_8 (not_8_out, A[3]);
  xor xor_8 (Result[3], xor_7_out, or_3_out);
  and and_7 (and_7_out, not_7_out, or_3_out);
  and and_8 (and_8_out, not_8_out, B[3]);
  or or_4 (or_4_out, and_7_out, and_8_out);
  xor xor_9 (xor_9_out, A[4], B[4]);
  not not_9 (not_9_out, A[4]);
  not not_10 (not_10_out, xor_9_out);
  xor xor_10 (Result[4], xor_9_out, or_4_out);
  and and_9 (and_9_out, not_10_out, or_4_out);
  and and_10 (and_10_out, not_9_out, B[4]);
  or or_5 (or_5_out, and_9_out, and_10_out);
  xor xor_11 (xor_11_out, A[5], B[5]);
  not not_11 (not_11_out, A[5]);
  not not_12 (not_12_out, xor_11_out);
  xor xor_12 (Result[5], xor_11_out, or_5_out);
  and and_11 (and_11_out, not_12_out, or_5_out);
  and and_12 (and_12_out, not_11_out, B[5]);
  or or_6 (or_6_out, and_11_out, and_12_out);
  xor xor_13 (xor_13_out, A[6], B[6]);
  not not_13 (not_13_out, A[6]);
  not not_14 (not_14_out, xor_13_out);
  xor xor_14 (Result[6], xor_13_out, or_6_out);
  and and_13 (and_13_out, not_14_out, or_6_out);
  and and_14 (and_14_out, not_13_out, B[6]);
  or or_7 (or_7_out, and_13_out, and_14_out);
  xor xor_15 (xor_15_out, A[7], B[7]);
  not not_15 (not_15_out, A[7]);
  not not_16 (not_16_out, xor_15_out);
  and and_15 (and_15_out, not_16_out, or_7_out);
  and and_16 (and_16_out, not_15_out, B[7]);
  xor xor_16 (Result[7], xor_15_out, or_7_out);
  or or_8 (C_out, and_15_out, and_16_out);
endmodule

// X
module Multiplication (
  input  [7:0] A,
  input  [7:0] B,
  output [7:0] R,
  output C
);

  wire and_2_out, and_3_out, and_4_out, and_5_out, and_6_out, and_7_out, and_8_out, and_9_out, and_10_out,
       and_11_out, and_12_out, and_13_out, and_14_out, and_15_out, and_16_out, and_17_out, and_18_out,
       and_19_out, and_20_out, and_21_out, and_22_out, and_23_out, and_24_out, and_25_out, and_26_out,
       and_27_out, and_28_out, and_29_out, and_30_out, and_31_out, and_32_out, and_33_out, and_34_out,
       and_35_out, and_36_out, and_37_out, and_38_out, and_39_out, and_40_out, and_41_out, and_42_out,
       and_43_out, and_44_out, and_45_out, and_46_out, and_47_out, and_48_out, and_49_out, and_50_out,
       and_51_out, and_52_out, and_53_out, and_54_out, and_55_out, and_56_out, and_57_out, and_58_out,
       and_59_out, and_60_out, and_61_out, and_62_out, and_63_out, and_64_out, full_adder_1_c_out,
       full_adder_1_sum, full_adder_2_c_out, full_adder_2_sum, full_adder_3_c_out, full_adder_3_sum,
       full_adder_4_c_out, full_adder_4_sum, full_adder_5_c_out, full_adder_5_sum, full_adder_6_c_out,
       full_adder_6_sum, full_adder_7_c_out, full_adder_7_sum, full_adder_8_c_out, full_adder_8_sum,
       full_adder_9_c_out, full_adder_9_sum, full_adder_10_c_out, full_adder_10_sum, full_adder_11_c_out,
       full_adder_11_sum, full_adder_12_c_out, full_adder_12_sum, full_adder_13_c_out, full_adder_13_sum,
       full_adder_14_c_out, full_adder_14_sum, full_adder_15_c_out, full_adder_15_sum, full_adder_16_c_out,
       full_adder_16_sum, full_adder_17_c_out, full_adder_17_sum, full_adder_18_c_out, full_adder_18_sum,
       full_adder_19_c_out, full_adder_19_sum, full_adder_20_c_out, full_adder_20_sum, full_adder_21_c_out,
       full_adder_21_sum, full_adder_22_c_out, full_adder_22_sum, full_adder_23_c_out, full_adder_23_sum,
       full_adder_24_c_out, full_adder_24_sum, full_adder_25_c_out, full_adder_25_sum, full_adder_26_c_out,
       full_adder_26_sum, full_adder_27_c_out, full_adder_27_sum, full_adder_28_c_out, full_adder_28_sum,
       full_adder_29_c_out, full_adder_29_sum, full_adder_30_c_out, full_adder_30_sum, full_adder_31_c_out,
       full_adder_31_sum, full_adder_32_c_out, full_adder_32_sum, full_adder_33_c_out, full_adder_33_sum,
       full_adder_34_c_out, full_adder_34_sum, full_adder_35_c_out, full_adder_35_sum, full_adder_36_c_out,
       full_adder_36_sum, full_adder_37_c_out, full_adder_37_sum, full_adder_38_c_out, full_adder_38_sum,
       full_adder_39_c_out, full_adder_39_sum, full_adder_40_c_out, full_adder_40_sum, full_adder_41_c_out,
       full_adder_41_sum, full_adder_42_c_out, full_adder_42_sum, full_adder_43_c_out, full_adder_43_sum,
       full_adder_44_c_out, full_adder_44_sum, full_adder_45_c_out, full_adder_45_sum, full_adder_46_c_out,
       full_adder_46_sum, full_adder_47_c_out, full_adder_47_sum, full_adder_48_c_out, full_adder_48_sum,
       full_adder_49_sum, half_adder_1_c_out, half_adder_2_c_out, half_adder_3_c_out, half_adder_4_c_out,
       half_adder_5_c_out, half_adder_6_c_out, half_adder_7_c_out;

  and and_1 (R[0], A[0], B[0]);
  and and_2 (and_2_out, A[0], B[1]);
  and and_3 (and_3_out, A[0], B[2]);
  and and_4 (and_4_out, A[0], B[3]);
  and and_5 (and_5_out, A[0], B[4]);
  and and_6 (and_6_out, A[0], B[5]);
  and and_7 (and_7_out, A[0], B[6]);
  and and_8 (and_8_out, A[0], B[7]);
  and and_9 (and_9_out, B[0], A[1]);
  and and_10 (and_10_out, B[1], A[1]);
  and and_11 (and_11_out, B[2], A[1]);
  and and_12 (and_12_out, B[3], A[1]);
  and and_13 (and_13_out, B[4], A[1]);
  and and_14 (and_14_out, B[5], A[1]);
  and and_15 (and_15_out, B[6], A[1]);
  and and_16 (and_16_out, B[7], A[1]);
  Half_adder half_adder_1 (.in_1(and_9_out), .in_2(and_2_out), .Sum(R[1]), .C_out(half_adder_1_c_out));
  Full_adder full_adder_1 (
    .A(and_10_out), .B(and_3_out), .C_in(half_adder_1_c_out), .Sum(full_adder_1_sum),
    .C_out(full_adder_1_c_out));
  Full_adder full_adder_2 (
    .A(and_11_out), .B(and_4_out), .C_in(full_adder_1_c_out), .Sum(full_adder_2_sum),
    .C_out(full_adder_2_c_out));
  Full_adder full_adder_3 (
    .A(and_12_out), .B(and_5_out), .C_in(full_adder_2_c_out), .Sum(full_adder_3_sum),
    .C_out(full_adder_3_c_out));
  Full_adder full_adder_4 (
    .A(and_13_out), .B(and_6_out), .C_in(full_adder_3_c_out), .Sum(full_adder_4_sum),
    .C_out(full_adder_4_c_out));
  Full_adder full_adder_5 (
    .A(and_14_out), .B(and_7_out), .C_in(full_adder_4_c_out), .Sum(full_adder_5_sum),
    .C_out(full_adder_5_c_out));
  Full_adder full_adder_6 (
    .A(and_15_out), .B(and_8_out), .C_in(full_adder_5_c_out), .Sum(full_adder_6_sum),
    .C_out(full_adder_6_c_out));
  Full_adder full_adder_7 (
    .A(and_16_out), .B(1'b0), .C_in(full_adder_6_c_out), .Sum(full_adder_7_sum), .C_out(full_adder_7_c_out));
  and and_17 (and_17_out, B[0], A[2]);
  and and_18 (and_18_out, B[1], A[2]);
  and and_19 (and_19_out, B[2], A[2]);
  and and_20 (and_20_out, B[3], A[2]);
  and and_21 (and_21_out, B[4], A[2]);
  and and_22 (and_22_out, B[5], A[2]);
  and and_23 (and_23_out, B[6], A[2]);
  and and_24 (and_24_out, B[7], A[2]);
  Half_adder half_adder_2 (.in_1(and_17_out), .in_2(full_adder_1_sum), .Sum(R[2]), .C_out(half_adder_2_c_out));
  Full_adder full_adder_8 (
    .A(and_18_out), .B(full_adder_2_sum), .C_in(half_adder_2_c_out), .Sum(full_adder_8_sum),
    .C_out(full_adder_8_c_out));
  Full_adder full_adder_9 (
    .A(and_19_out), .B(full_adder_3_sum), .C_in(full_adder_8_c_out), .Sum(full_adder_9_sum),
    .C_out(full_adder_9_c_out));
  Full_adder full_adder_10 (
    .A(and_20_out), .B(full_adder_4_sum), .C_in(full_adder_9_c_out), .Sum(full_adder_10_sum),
    .C_out(full_adder_10_c_out));
  Full_adder full_adder_11 (
    .A(and_21_out), .B(full_adder_5_sum), .C_in(full_adder_10_c_out), .Sum(full_adder_11_sum),
    .C_out(full_adder_11_c_out));
  Full_adder full_adder_12 (
    .A(and_22_out), .B(full_adder_6_sum), .C_in(full_adder_11_c_out), .Sum(full_adder_12_sum),
    .C_out(full_adder_12_c_out));
  Full_adder full_adder_13 (
    .A(and_23_out), .B(full_adder_7_sum), .C_in(full_adder_12_c_out), .Sum(full_adder_13_sum),
    .C_out(full_adder_13_c_out));
  Full_adder full_adder_14 (
    .A(and_24_out), .B(full_adder_7_c_out), .C_in(full_adder_13_c_out), .Sum(full_adder_14_sum),
    .C_out(full_adder_14_c_out));
  and and_25 (and_25_out, B[0], A[3]);
  and and_26 (and_26_out, B[1], A[3]);
  and and_27 (and_27_out, B[2], A[3]);
  and and_28 (and_28_out, B[3], A[3]);
  and and_29 (and_29_out, B[4], A[3]);
  and and_30 (and_30_out, B[5], A[3]);
  and and_31 (and_31_out, B[6], A[3]);
  and and_32 (and_32_out, B[7], A[3]);
  Half_adder half_adder_3 (.in_1(and_25_out), .in_2(full_adder_8_sum), .Sum(R[3]), .C_out(half_adder_3_c_out));
  Full_adder full_adder_15 (
    .A(and_26_out), .B(full_adder_9_sum), .C_in(half_adder_3_c_out), .Sum(full_adder_15_sum),
    .C_out(full_adder_15_c_out));
  Full_adder full_adder_16 (
    .A(and_27_out), .B(full_adder_10_sum), .C_in(full_adder_15_c_out), .Sum(full_adder_16_sum),
    .C_out(full_adder_16_c_out));
  Full_adder full_adder_17 (
    .A(and_28_out), .B(full_adder_11_sum), .C_in(full_adder_16_c_out), .Sum(full_adder_17_sum),
    .C_out(full_adder_17_c_out));
  Full_adder full_adder_18 (
    .A(and_29_out), .B(full_adder_12_sum), .C_in(full_adder_17_c_out), .Sum(full_adder_18_sum),
    .C_out(full_adder_18_c_out));
  Full_adder full_adder_19 (
    .A(and_30_out), .B(full_adder_13_sum), .C_in(full_adder_18_c_out), .Sum(full_adder_19_sum),
    .C_out(full_adder_19_c_out));
  Full_adder full_adder_20 (
    .A(and_31_out), .B(full_adder_14_sum), .C_in(full_adder_19_c_out), .Sum(full_adder_20_sum),
    .C_out(full_adder_20_c_out));
  Full_adder full_adder_21 (
    .A(and_32_out), .B(full_adder_14_c_out), .C_in(full_adder_20_c_out), .Sum(full_adder_21_sum),
    .C_out(full_adder_21_c_out));
  and and_33 (and_33_out, B[0], A[4]);
  and and_34 (and_34_out, B[1], A[4]);
  and and_35 (and_35_out, B[2], A[4]);
  and and_36 (and_36_out, B[3], A[4]);
  and and_37 (and_37_out, B[4], A[4]);
  and and_38 (and_38_out, B[5], A[4]);
  and and_39 (and_39_out, B[6], A[4]);
  and and_40 (and_40_out, B[7], A[4]);
  Half_adder half_adder_4 (.in_1(and_33_out), .in_2(full_adder_15_sum), .Sum(R[4]), .C_out(half_adder_4_c_out));
  Full_adder full_adder_22 (
    .A(and_34_out), .B(full_adder_16_sum), .C_in(half_adder_4_c_out), .Sum(full_adder_22_sum),
    .C_out(full_adder_22_c_out));
  Full_adder full_adder_23 (
    .A(and_35_out), .B(full_adder_17_sum), .C_in(full_adder_22_c_out), .Sum(full_adder_23_sum),
    .C_out(full_adder_23_c_out));
  Full_adder full_adder_24 (
    .A(and_36_out), .B(full_adder_18_sum), .C_in(full_adder_23_c_out), .Sum(full_adder_24_sum),
    .C_out(full_adder_24_c_out));
  Full_adder full_adder_25 (
    .A(and_37_out), .B(full_adder_19_sum), .C_in(full_adder_24_c_out), .Sum(full_adder_25_sum),
    .C_out(full_adder_25_c_out));
  Full_adder full_adder_26 (
    .A(and_38_out), .B(full_adder_20_sum), .C_in(full_adder_25_c_out), .Sum(full_adder_26_sum),
    .C_out(full_adder_26_c_out));
  Full_adder full_adder_27 (
    .A(and_39_out), .B(full_adder_21_sum), .C_in(full_adder_26_c_out), .Sum(full_adder_27_sum),
    .C_out(full_adder_27_c_out));
  Full_adder full_adder_28 (
    .A(and_40_out), .B(full_adder_21_c_out), .C_in(full_adder_27_c_out), .Sum(full_adder_28_sum),
    .C_out(full_adder_28_c_out));
  and and_41 (and_41_out, B[0], A[5]);
  and and_42 (and_42_out, B[1], A[5]);
  and and_43 (and_43_out, B[2], A[5]);
  and and_44 (and_44_out, B[3], A[5]);
  and and_45 (and_45_out, B[4], A[5]);
  and and_46 (and_46_out, B[5], A[5]);
  and and_47 (and_47_out, B[6], A[5]);
  and and_48 (and_48_out, B[7], A[5]);
  Half_adder half_adder_5 (.in_1(and_41_out), .in_2(full_adder_22_sum), .Sum(R[5]), .C_out(half_adder_5_c_out));
  Full_adder full_adder_29 (
    .A(and_42_out), .B(full_adder_23_sum), .C_in(half_adder_5_c_out), .Sum(full_adder_29_sum),
    .C_out(full_adder_29_c_out));
  Full_adder full_adder_30 (
    .A(and_43_out), .B(full_adder_24_sum), .C_in(full_adder_29_c_out), .Sum(full_adder_30_sum),
    .C_out(full_adder_30_c_out));
  Full_adder full_adder_31 (
    .A(and_44_out), .B(full_adder_25_sum), .C_in(full_adder_30_c_out), .Sum(full_adder_31_sum),
    .C_out(full_adder_31_c_out));
  Full_adder full_adder_32 (
    .A(and_45_out), .B(full_adder_26_sum), .C_in(full_adder_31_c_out), .Sum(full_adder_32_sum),
    .C_out(full_adder_32_c_out));
  Full_adder full_adder_33 (
    .A(and_46_out), .B(full_adder_27_sum), .C_in(full_adder_32_c_out), .Sum(full_adder_33_sum),
    .C_out(full_adder_33_c_out));
  Full_adder full_adder_34 (
    .A(and_47_out), .B(full_adder_28_sum), .C_in(full_adder_33_c_out), .Sum(full_adder_34_sum),
    .C_out(full_adder_34_c_out));
  Full_adder full_adder_35 (
    .A(and_48_out), .B(full_adder_28_c_out), .C_in(full_adder_34_c_out), .Sum(full_adder_35_sum),
    .C_out(full_adder_35_c_out));
  and and_49 (and_49_out, B[0], A[6]);
  and and_50 (and_50_out, B[1], A[6]);
  and and_51 (and_51_out, B[2], A[6]);
  and and_52 (and_52_out, B[3], A[6]);
  and and_53 (and_53_out, B[4], A[6]);
  and and_54 (and_54_out, B[5], A[6]);
  and and_55 (and_55_out, B[6], A[6]);
  and and_56 (and_56_out, B[7], A[6]);
  Half_adder half_adder_6 (.in_1(and_49_out), .in_2(full_adder_29_sum), .Sum(R[6]), .C_out(half_adder_6_c_out));
  Full_adder full_adder_36 (
    .A(and_50_out), .B(full_adder_30_sum), .C_in(half_adder_6_c_out), .Sum(full_adder_36_sum),
    .C_out(full_adder_36_c_out));
  Full_adder full_adder_37 (
    .A(and_51_out), .B(full_adder_31_sum), .C_in(full_adder_36_c_out), .Sum(full_adder_37_sum),
    .C_out(full_adder_37_c_out));
  Full_adder full_adder_38 (
    .A(and_52_out), .B(full_adder_32_sum), .C_in(full_adder_37_c_out), .Sum(full_adder_38_sum),
    .C_out(full_adder_38_c_out));
  Full_adder full_adder_39 (
    .A(and_53_out), .B(full_adder_33_sum), .C_in(full_adder_38_c_out), .Sum(full_adder_39_sum),
    .C_out(full_adder_39_c_out));
  Full_adder full_adder_40 (
    .A(and_54_out), .B(full_adder_34_sum), .C_in(full_adder_39_c_out), .Sum(full_adder_40_sum),
    .C_out(full_adder_40_c_out));
  Full_adder full_adder_41 (
    .A(and_55_out), .B(full_adder_35_sum), .C_in(full_adder_40_c_out), .Sum(full_adder_41_sum),
    .C_out(full_adder_41_c_out));
  Full_adder full_adder_42 (
    .A(and_56_out), .B(full_adder_35_c_out), .C_in(full_adder_41_c_out), .Sum(full_adder_42_sum),
    .C_out(full_adder_42_c_out));
  and and_57 (and_57_out, B[0], A[7]);
  and and_58 (and_58_out, B[1], A[7]);
  and and_59 (and_59_out, B[2], A[7]);
  and and_60 (and_60_out, B[3], A[7]);
  and and_61 (and_61_out, B[4], A[7]);
  and and_62 (and_62_out, B[5], A[7]);
  and and_63 (and_63_out, B[6], A[7]);
  and and_64 (and_64_out, B[7], A[7]);
  Half_adder half_adder_7 (.in_1(and_57_out), .in_2(full_adder_36_sum), .Sum(R[7]), .C_out(half_adder_7_c_out));
  Full_adder full_adder_43 (
    .A(and_58_out), .B(full_adder_37_sum), .C_in(half_adder_7_c_out), .Sum(full_adder_43_sum),
    .C_out(full_adder_43_c_out));
  Full_adder full_adder_44 (
    .A(and_59_out), .B(full_adder_38_sum), .C_in(full_adder_43_c_out), .Sum(full_adder_44_sum),
    .C_out(full_adder_44_c_out));
  Full_adder full_adder_45 (
    .A(and_60_out), .B(full_adder_39_sum), .C_in(full_adder_44_c_out), .Sum(full_adder_45_sum),
    .C_out(full_adder_45_c_out));
  Full_adder full_adder_46 (
    .A(and_61_out), .B(full_adder_40_sum), .C_in(full_adder_45_c_out), .Sum(full_adder_46_sum),
    .C_out(full_adder_46_c_out));
  Full_adder full_adder_47 (
    .A(and_62_out), .B(full_adder_41_sum), .C_in(full_adder_46_c_out), .Sum(full_adder_47_sum),
    .C_out(full_adder_47_c_out));
  Full_adder full_adder_48 (
    .A(and_63_out), .B(full_adder_42_sum), .C_in(full_adder_47_c_out), .Sum(full_adder_48_sum),
    .C_out(full_adder_48_c_out));
  Full_adder full_adder_49 (
    .A(and_64_out), .B(full_adder_42_c_out), .C_in(full_adder_48_c_out), .Sum(full_adder_49_sum));  // open: C_out
  or or_1 (C, full_adder_43_sum, full_adder_44_sum, full_adder_45_sum, full_adder_46_sum, full_adder_47_sum, full_adder_48_sum, full_adder_49_sum);
endmodule

// HA
module Half_adder (
  input  in_1,
  input  in_2,
  output Sum,
  output C_out
);

  wire not_1_out, or_1_out;

  or or_1 (or_1_out, in_1, in_2);
  and and_1 (C_out, in_1, in_2);
  not not_1 (not_1_out, C_out);
  and and_2 (Sum, or_1_out, not_1_out);
endmodule

// FA
module Full_adder (
  input  A,
  input  B,
  input  C_in,
  output Sum,
  output C_out
);

  wire and_1_out, and_2_out, and_3_out, not_1_out, not_2_out, or_1_out, or_2_out;

  and and_1 (and_1_out, A, B);
  and and_2 (and_2_out, C_in, and_3_out);
  or or_1 (or_1_out, B, A);
  not not_1 (not_1_out, and_1_out);
  or or_2 (or_2_out, and_3_out, C_in);
  not not_2 (not_2_out, and_2_out);
  and and_3 (and_3_out, or_1_out, not_1_out);
  and and_4 (Sum, or_2_out, not_2_out);
  or or_3 (C_out, and_1_out, and_2_out);
endmodule
