// Logisim project CPUmain.circ as structural Verilog: 1 circuit, main circuit main
module main (
  input  Manual_R,
  input  Manual_W,
  input  [15:0] Manual_Data_in,
  input  Enable_Manual,
  input  Populate_Memory_Enable,
  input  Counter_reset,
  input  Disable_Clock,
  output [15:0] A0,
  output [15:0] A16,
  output [15:0] A1,
  output [15:0] A17,
  output [15:0] A2,
  output [15:0] A18,
  output [15:0] A3,
  output [15:0] A19,
  output [15:0] A4,
  output [15:0] A20,
  output [15:0] A5,
  output [15:0] A21,
  output [15:0] A6,
  output [15:0] A22,
  output [15:0] A7,
  output [15:0] A23,
  output [15:0] A8,
  output [15:0] A24,
  output [15:0] A9,
  output [15:0] A25,
  output [15:0] A10,
  output [15:0] A26,
  output [15:0] A11,
  output [15:0] A27,
  output [15:0] A12,
  output [15:0] A28,
  output [15:0] A13,
  output [15:0] A29,
  output [15:0] A14,
  output [15:0] A30,
  output [15:0] A15,
  output [15:0] A31,
  output [15:0] Instruction_in_IR,
  output [7:0] R3,
  output [7:0] R2,
  output [7:0] R1,
  output [7:0] R0
);

  wire A, B, C, Cir, clock_1_out, Cmar, controlled_buffer_1_out, controlled_buffer_2_out, counter_1_carry,
       Cpc, Cx, Ebr, Eir, Emem, Epc, Erd, Ers, Ex, F0, F1, F2, not_1_out, or_1_out, or_2_out, or_3_out, R,
       Rda, Rdb, Rsa, Rsb, Trap, W, Wd, Ws, Z;
  wire [1:0] controlled_buffer_6_out, controlled_buffer_7_out;
  wire [3:0] main_1__1_s, main_1__10_s, main_1__100_s;
  wire [4:0] counter_1_q, mar_1_address_stored, multiplexer_1_out;
  wire [7:0] alu_1_result, controlled_buffer_3_out, register_1_q;
  wire [15:0] intermediate_register_1_value_stored, memory_32address_1_out_13, multiplexer_2_out,
       multiplexer_3_out, multiplexer_4_out, program_counter_1_address_out, registerfile_1_a,
       registerfile_1_b, rom_1_data;
  wire [15:8] controlled_buffer_3_out_2;

  Hex_Digit_Display hex_digit_display_1 (.value(main_1__10_s));  // open: dp
  Hex_Digit_Display hex_digit_display_2 (.value(main_1__100_s));  // open: dp
  Hex_Digit_Display hex_digit_display_3 (.value(main_1__1_s));  // open: dp
  Counter #(.width(5), .max('h1f), .trigger("falling")) counter_1 (
    .Q(counter_1_q), .carry(counter_1_carry), .clk(controlled_buffer_1_out), .clr(Counter_reset));  // open: load, D, count
  assign controlled_buffer_1_out = not_1_out ? controlled_buffer_2_out : 1'bz;  // Controlled_Buffer controlled_buffer_1
  not not_1 (not_1_out, or_3_out);
  assign controlled_buffer_2_out = Populate_Memory_Enable ? clock_1_out : 1'bz;  // Controlled_Buffer controlled_buffer_2
  Clock clock_1 (.out(clock_1_out));
  or or_1 (or_1_out, Manual_R, R);
  or or_2 (or_2_out, Manual_W, Populate_Memory_Enable, W);
  buf or_3 (or_3_out, counter_1_carry);  // OR_Gate
  Control_Unit control_unit_1 (
    .Z(Z), .C(C), .Wd(Wd), .Emem(Emem), .Ws(Ws), .Rsb(Rsb), .Rda(Rda), .Rdb(Rdb), .Epc(Epc), .Ebr(Ebr),
    .A(A), .F2(F2), .F1(F1), .Erd(Erd), .F0(F0), .Cir(Cir), .Cmar(Cmar), .Cpc(Cpc), .R(R), .W(W), .Eir(Eir),
    .Rsa(Rsa), .Ex(Ex), .Cx(Cx), .Ers(Ers), .B(B), .Instruction_In(Instruction_in_IR),
    .Disable_Clock(Disable_Clock), .Trap(Trap));
  ROM #(.addrWidth(5), .dataWidth(16)) rom_1 (.addr(counter_1_q), .data(rom_1_data));  // open: sel
  Multiplexer #(.width(5)) multiplexer_1 (
    .in0(mar_1_address_stored), .in1(counter_1_q), .out(multiplexer_1_out), .sel(Populate_Memory_Enable));  // open: en
  Register #(.width(16), .trigger("high")) IR (
    .D({controlled_buffer_3_out_2, controlled_buffer_3_out}), .Q(Instruction_in_IR), .clk(Cir));  // open: en, clr
  Program_Counter program_counter_1 (
    .Branch_to({controlled_buffer_3_out_2, controlled_buffer_3_out}), .Ebr(Ebr), .Cpc(Cpc),
    .Address_Out(program_counter_1_address_out));
  Memory_32Address memory_32address_1 (
    .Manual_select(Enable_Manual), .Address(multiplexer_1_out), .out_7(A16), .out_8(A0), .out_9(A17),
    .out_10(A1), .out_11(A18), .out_12(A2), .out_13(memory_32address_1_out_13), .out_14(A19), .out_15(A3),
    .out_16(A20), .out_17(A4), .out_18(A21), .out_19(A5), .out_20(A22), .out_21(A6), .out_22(A23),
    .out_23(A7), .out_24(A24), .out_25(A8), .out_26(A25), .out_27(A9), .out_28(A26), .out_29(A10),
    .out_30(A27), .out_31(A11), .out_32(A28), .out_33(A12), .out_34(A29), .out_35(A13), .out_36(A30),
    .out_37(A14), .out_38(A31), .out_39(A15), .Manual_input(Manual_Data_in), .Data_in(multiplexer_2_out),
    .Write_enable(or_2_out), .Read_enable(or_1_out));
  MAR mar_1 (.Address_in(controlled_buffer_3_out[4:0]), .Allow_write(Cmar), .Address_stored(mar_1_address_stored));
  assign {controlled_buffer_3_out_2, controlled_buffer_3_out} = Epc ? program_counter_1_address_out : 16'bz;  // Controlled_Buffer controlled_buffer_3
  HexDigitalDecode_main main_1 (
    .Value_in(register_1_q), ._100_s(main_1__100_s), ._10_s(main_1__10_s), ._1_s(main_1__1_s));
  assign {controlled_buffer_3_out_2, controlled_buffer_3_out} = Emem ? memory_32address_1_out_13 : 16'bz;  // Controlled_Buffer controlled_buffer_4
  Multiplexer #(.width(16)) multiplexer_2 (
    .in0({controlled_buffer_3_out_2, controlled_buffer_3_out}), .in1(rom_1_data), .out(multiplexer_2_out),
    .sel(Populate_Memory_Enable));  // open: en
  assign {controlled_buffer_3_out_2, controlled_buffer_3_out} = Eir ? {{8{1'b0}}, Instruction_in_IR[7:0]} : 16'bz;  // Controlled_Buffer controlled_buffer_5
  Register #(.trigger("high")) register_1 (.D(controlled_buffer_3_out), .Q(register_1_q), .clk(Trap));  // open: en, clr
  assign controlled_buffer_6_out = Erd ? Instruction_in_IR[1:0] : 2'bz;  // Controlled_Buffer controlled_buffer_6
  assign controlled_buffer_7_out = Ers ? Instruction_in_IR[9:8] : 2'bz;  // Controlled_Buffer controlled_buffer_7
  assign {controlled_buffer_3_out_2, controlled_buffer_3_out} = Ex ? intermediate_register_1_value_stored : 16'bz;  // Controlled_Buffer controlled_buffer_8
  Multiplexer #(.width(16)) multiplexer_3 (
    .in0(registerfile_1_b), .in1({controlled_buffer_3_out_2, controlled_buffer_3_out}),
    .out(multiplexer_3_out), .sel(B));  // open: en
  Intermediate_register intermediate_register_1 (
    .Data_in(alu_1_result), .Allow_write(Cx), .Value_stored(intermediate_register_1_value_stored));
  RegisterFile registerfile_1 (
    .Data_from_bus({controlled_buffer_3_out_2, controlled_buffer_3_out}), .Ws(Ws),
    .S(controlled_buffer_7_out), .Wd(Wd), .D(controlled_buffer_6_out), .A(registerfile_1_a), .RSA(Rsa),
    .RDA(Rda), .B(registerfile_1_b), .RDB(Rdb), .RSB(Rsb), .R0(R0), .R1(R1), .R2(R2), .R3(R3));
  ALU alu_1 (
    .A(multiplexer_4_out), .B(multiplexer_3_out), .F0(F0), .F1(F1), .F2(F2), .Result(alu_1_result), .C(C),
    .Z(Z));
  Multiplexer #(.width(16)) multiplexer_4 (
    .in0(registerfile_1_a), .in1({controlled_buffer_3_out_2, controlled_buffer_3_out}),
    .out(multiplexer_4_out), .sel(A));  // open: en

  // Notes on the sheet:
  //   contents of rom_1 (hex, n*v repeats v):
  //   405 505 2401 3001 2401 9003 f100 ffff
endmodule
