// Logisim project DecodeUnit.circ as structural Verilog: 3 circuits, main circuit Control Unit
// CU
module Control_Unit (
  input  [15:0] Instruction_In,
  input  Disable_Clock,
  input  Z,
  input  C,
  output Wd,
  output Emem,
  output Ws,
  output Rsb,
  output Rda,
  output Rdb,
  output Epc,
  output Ebr,
  output A,
  output F2,
  output F1,
  output Erd,
  output F0,
  output Trap,
  output Cir,
  output Cmar,
  output Cpc,
  output R,
  output W,
  output Eir,
  output Rsa,
  output Ex,
  output Cx,
  output Ers,
  output B
);

  wire Add00T0, Add00T1, Add01T0, Add01T1, Add10T0, Add10T1, Add10T2, Add11T0, Add11T1, Add11T2, ADD_00_out,
       ADD_01_out, ADD_10_out, ADD_11_out, And00T0, And00T1, And01T0, And01T1, And10T0, And10T1, And10T2,
       And11T0, And11T1, And11T2, AND_00_out, AND_01_out, and_1_out, and_2_out, and_6_out, and_9_out,
       AND_10_out, AND_11_out, and_13_out, and_21_out, and_25_out, and_33_out, and_37_out, and_45_out,
       and_49_out, and_57_out, and_61_out, and_69_out, and_73_out, and_83_out, and_87_out, and_89_out,
       and_91_out, and_93_out, and_95_out, and_97_out, and_99_out, and_101_out, and_103_out, BCC_out, BccT0,
       BCS_out, BcsT0, BEQ_out, BeqT0, BHI_out, BhiT0, BLS_out, BlsT0, BNE_out, BneT0, ConditionNotMet,
       FETCH_4_out, FetchT0, FetchT1, FetchT2, JmpT0, JUMP_out, Move00T0, Move00T1, Move01T0, Move10T0,
       Move10T1, Move11T0, Move11T1, Move11T2, MOVE_00_out, MOVE_01_out, MOVE_10_out, MOVE_11_out, Mul00T0,
       Mul00T1, Mul01T0, Mul01T1, Mul10T0, Mul10T1, Mul10T2, Mul11T0, Mul11T1, Mul11T2, MUL_00_out,
       MUL_01_out, MUL_10_out, MUL_11_out, not_1_out, not_2_out, not_3_out, not_4_out, not_5_out, not_6_out,
       not_7_out, not_8_out, not_9_out, NOT_10_out, not_11_out, NotT0, NotT1, Or00T0, Or00T1, Or01T0, Or01T1,
       Or10T0, Or10T1, Or10T2, Or11T0, Or11T1, Or11T2, OR_00_out, OR_01_out, or_2_out, or_3_out, or_4_out,
       or_6_out, or_7_out, or_9_out, OR_10_out, OR_11_out, or_12_out, or_13_out, or_17_out, or_18_out,
       or_24_out, or_25_out, or_29_out, or_30_out, or_31_out, or_34_out, or_35_out, or_38_out, or_39_out,
       or_45_out, or_46_out, or_47_out, s_r_ff_1_q, s_r_ff_1_qn, Sub00T0, Sub00T1, Sub01T0, Sub01T1, Sub10T0,
       Sub10T1, Sub10T2, Sub11T0, Sub11T1, Sub11T2, SUB_00_out, SUB_01_out, SUB_10_out, SUB_11_out, T0, T1,
       T2, T3, T4, T5, T6, T7, Trap00T0, Trap01T0, Trap01T1, TRAP_00_out, TRAP_01_out, Xor00T0, Xor00T1,
       Xor01T0, Xor01T1, Xor10T0, Xor10T1, Xor10T2, Xor11T0, Xor11T1, Xor11T2, XOR_00_out, XOR_01_out,
       XOR_10_out, XOR_11_out;

  or or_1 (R, FetchT1, Move10T1, Add10T1, Add11T1, Sub10T1, Sub11T1, Mul10T1, Mul11T1, And10T1, And11T1, Or10T1, Or11T1, Xor10T1, Xor11T1, Trap01T1);
  or or_2 (or_2_out, ConditionNotMet, Trap01T1, and_103_out, and_101_out, and_99_out, and_97_out, and_95_out);
  or or_3 (or_3_out, and_93_out, and_91_out, and_89_out, and_87_out, and_83_out, Xor01T1, Xor00T1, NotT1, and_73_out, and_69_out, Or01T1, Or00T1, and_61_out, and_57_out, And01T1, And00T1, and_49_out, and_45_out, Mul01T1, Mul00T1, and_37_out, and_33_out, Sub01T1, Sub00T1, and_25_out, and_21_out, Add01T1, Add00T1, and_13_out, and_9_out, and_6_out, Move00T1);
  or or_4 (or_4_out, or_2_out, or_3_out);
  S_R_Flip_Flop #(.trigger("high")) s_r_ff_1 (
    .S(FETCH_4_out), .clk(1'b1), .R(or_4_out), .Q(s_r_ff_1_q), .Qn(s_r_ff_1_qn));  // open: preset, reset, en
  or or_5 (W, Move11T2, Add11T2, Sub11T2, Mul11T2, And11T2, Or11T2, Xor11T2);
  or or_6 (or_6_out, and_1_out, Disable_Clock);
  or or_7 (or_7_out, or_4_out, FETCH_4_out);
  Sequencer sequencer_1 (
    .Clear_to_state_T0(or_7_out), .Disable_Clock(or_6_out), .T0(T0), .T1(T1), .T2(T2), .T3(T3), .T4(T4),
    .T5(T5), .T6(T6), .T7(T7));
  and and_1 (and_1_out, Instruction_In[15], Instruction_In[14], Instruction_In[13], Instruction_In[12], Instruction_In[11], Instruction_In[10], Instruction_In[9], Instruction_In[8], Instruction_In[7], Instruction_In[6], Instruction_In[5], Instruction_In[4], Instruction_In[3], Instruction_In[2], Instruction_In[1], Instruction_In[0]);
  not not_1 (not_1_out, Instruction_In[15]);
  and FETCH (FetchT0, s_r_ff_1_qn, T0);
  and FETCH_2 (FetchT1, s_r_ff_1_qn, T1);
  and FETCH_3 (FetchT2, s_r_ff_1_qn, T2);
  and FETCH_4 (FETCH_4_out, s_r_ff_1_qn, T3);
  not not_2 (not_2_out, Instruction_In[14]);
  not not_3 (not_3_out, Instruction_In[13]);
  not not_4 (not_4_out, Instruction_In[12]);
  or or_8 (Cmar, FetchT0, Move10T0, Move11T0, Add10T0, Add11T0, Sub10T0, Sub11T0, Mul10T0, Mul11T0, And10T0, And11T0, Or10T0, Or11T0, Xor10T0, Xor11T0, Trap01T0);
  not not_5 (not_5_out, Z);
  not not_6 (not_6_out, C);
  and and_2 (and_2_out, not_5_out, not_6_out);
  or or_9 (or_9_out, C, Z);
  or or_10 (Cpc, FetchT2, BeqT0, BneT0, BhiT0, BcsT0, BccT0, BlsT0, JmpT0);
  buf or_11 (Cir, FetchT1);  // OR_Gate
  not not_7 (not_7_out, Instruction_In[11]);
  not not_8 (not_8_out, Instruction_In[10]);
  not not_9 (not_9_out, Z);
  or or_12 (or_12_out, Move00T0, Move11T1, Add00T0, Add01T0, Add10T1, Add11T1, Sub00T0, Sub01T0, Sub10T1, Sub11T1, Mul00T0, Mul01T0, Mul10T1, Mul11T1, And00T0, And01T0);
  or or_13 (or_13_out, And10T1, And11T1, Or00T0, Or01T0, Or10T1, Or11T1, NotT0, Xor00T0, Xor01T0, Xor10T1, Xor11T1, Trap00T0);
  and MOVE_00 (MOVE_00_out, s_r_ff_1_q, not_8_out, not_7_out, not_4_out, not_3_out, not_2_out, not_1_out);
  and MOVE_01 (MOVE_01_out, s_r_ff_1_q, Instruction_In[10], not_7_out, not_4_out, not_3_out, not_2_out, not_1_out);
  and MOVE_10 (MOVE_10_out, s_r_ff_1_q, not_8_out, Instruction_In[11], not_4_out, not_3_out, not_2_out, not_1_out);
  and MOVE_11 (MOVE_11_out, s_r_ff_1_q, Instruction_In[10], Instruction_In[11], not_4_out, not_3_out, not_2_out, not_1_out);
  and ADD_00 (ADD_00_out, s_r_ff_1_q, not_8_out, not_7_out, Instruction_In[12], not_3_out, not_2_out, not_1_out);
  and ADD_01 (ADD_01_out, s_r_ff_1_q, Instruction_In[10], not_7_out, Instruction_In[12], not_3_out, not_2_out, not_1_out);
  and ADD_10 (ADD_10_out, s_r_ff_1_q, not_8_out, Instruction_In[11], Instruction_In[12], not_3_out, not_2_out, not_1_out);
  and ADD_11 (ADD_11_out, s_r_ff_1_q, Instruction_In[10], Instruction_In[11], Instruction_In[12], not_3_out, not_2_out, not_1_out);
  and SUB_00 (SUB_00_out, s_r_ff_1_q, not_8_out, not_7_out, not_4_out, Instruction_In[13], not_2_out, not_1_out);
  and SUB_01 (SUB_01_out, s_r_ff_1_q, Instruction_In[10], not_7_out, not_4_out, Instruction_In[13], not_2_out, not_1_out);
  and SUB_10 (SUB_10_out, s_r_ff_1_q, not_8_out, Instruction_In[11], not_4_out, Instruction_In[13], not_2_out, not_1_out);
  and SUB_11 (SUB_11_out, s_r_ff_1_q, Instruction_In[10], Instruction_In[11], not_4_out, Instruction_In[13], not_2_out, not_1_out);
  and MUL_00 (MUL_00_out, s_r_ff_1_q, not_8_out, not_7_out, Instruction_In[12], Instruction_In[13], not_2_out, not_1_out);
  and MUL_01 (MUL_01_out, s_r_ff_1_q, Instruction_In[10], not_7_out, Instruction_In[12], Instruction_In[13], not_2_out, not_1_out);
  and MUL_10 (MUL_10_out, s_r_ff_1_q, not_8_out, Instruction_In[11], Instruction_In[12], Instruction_In[13], not_2_out, not_1_out);
  and MUL_11 (MUL_11_out, s_r_ff_1_q, Instruction_In[10], Instruction_In[11], Instruction_In[12], Instruction_In[13], not_2_out, not_1_out);
  and AND_00 (AND_00_out, s_r_ff_1_q, not_8_out, not_7_out, not_4_out, not_3_out, Instruction_In[14], not_1_out);
  and AND_01 (AND_01_out, s_r_ff_1_q, Instruction_In[10], not_7_out, not_4_out, not_3_out, Instruction_In[14], not_1_out);
  and AND_10 (AND_10_out, s_r_ff_1_q, not_8_out, Instruction_In[11], not_4_out, not_3_out, Instruction_In[14], not_1_out);
  and AND_11 (AND_11_out, s_r_ff_1_q, Instruction_In[10], Instruction_In[11], not_4_out, not_3_out, Instruction_In[14], not_1_out);
  and OR_00 (OR_00_out, s_r_ff_1_q, not_8_out, not_7_out, Instruction_In[12], not_3_out, Instruction_In[14], not_1_out);
  and OR_01 (OR_01_out, s_r_ff_1_q, Instruction_In[10], not_7_out, Instruction_In[12], not_3_out, Instruction_In[14], not_1_out);
  and OR_10_dup2 (OR_10_out, s_r_ff_1_q, not_8_out, Instruction_In[11], Instruction_In[12], not_3_out, Instruction_In[14], not_1_out);
  and OR_11_dup2 (OR_11_out, s_r_ff_1_q, Instruction_In[10], Instruction_In[11], Instruction_In[12], not_3_out, Instruction_In[14], not_1_out);
  and NOT_10 (NOT_10_out, s_r_ff_1_q, not_4_out, Instruction_In[13], Instruction_In[14], not_1_out);
  and XOR_00 (XOR_00_out, s_r_ff_1_q, not_8_out, not_7_out, Instruction_In[12], Instruction_In[13], Instruction_In[14], not_1_out);
  and XOR_01 (XOR_01_out, s_r_ff_1_q, Instruction_In[10], not_7_out, Instruction_In[12], Instruction_In[13], Instruction_In[14], not_1_out);
  and XOR_10 (XOR_10_out, s_r_ff_1_q, not_8_out, Instruction_In[11], Instruction_In[12], Instruction_In[13], Instruction_In[14], not_1_out);
  and XOR_11 (XOR_11_out, s_r_ff_1_q, Instruction_In[10], Instruction_In[11], Instruction_In[12], Instruction_In[13], Instruction_In[14], not_1_out);
  and BEQ (BEQ_out, s_r_ff_1_q, Z, not_4_out, not_3_out, not_2_out, Instruction_In[15]);
  and BNE (BNE_out, s_r_ff_1_q, not_9_out, Instruction_In[12], not_3_out, not_2_out, Instruction_In[15]);
  and BHI (BHI_out, s_r_ff_1_q, and_2_out, not_4_out, Instruction_In[13], not_2_out, Instruction_In[15]);
  and BCS (BCS_out, s_r_ff_1_q, C, Instruction_In[12], Instruction_In[13], not_2_out, Instruction_In[15]);
  and BCC (BCC_out, s_r_ff_1_q, not_6_out, not_4_out, not_3_out, Instruction_In[14], Instruction_In[15]);
  and BLS (BLS_out, s_r_ff_1_q, or_9_out, Instruction_In[12], not_3_out, Instruction_In[14], Instruction_In[15]);
  and JUMP (JUMP_out, s_r_ff_1_q, not_4_out, Instruction_In[13], Instruction_In[14], Instruction_In[15]);
  and TRAP_00 (TRAP_00_out, s_r_ff_1_q, Instruction_In[12], Instruction_In[13], Instruction_In[14], Instruction_In[15], not_8_out, not_7_out);
  and TRAP_01 (TRAP_01_out, s_r_ff_1_q, Instruction_In[12], Instruction_In[13], Instruction_In[14], Instruction_In[15], Instruction_In[10], not_7_out);
  or or_14 (Cx, or_12_out, or_13_out);
  and and_3 (Move00T0, MOVE_00_out, T0);
  and and_4 (Move00T1, MOVE_00_out, T1);
  or or_15 (Ws, Add01T1, Add10T2, Sub01T1, Sub10T2, Mul01T1, Mul10T2, And01T1, And10T2, Or01T1, Or10T2, NotT1, Xor01T1, Xor10T2, Move01T0, Move10T1);
  and and_5 (Move01T0, MOVE_01_out, T0);
  and and_6 (and_6_out, MOVE_01_out, T1);
  or or_16 (Wd, Move00T1, Add00T1, Sub00T1, Mul00T1, And00T1, Or00T1, Xor00T1);
  and and_7 (Move10T0, MOVE_10_out, T0);
  and and_8 (Move10T1, MOVE_10_out, T1);
  and and_9 (and_9_out, MOVE_10_out, T4);
  and and_10_dup2 (Move11T0, MOVE_11_out, T0);
  and and_11_dup2 (Move11T1, MOVE_11_out, T1);
  and and_12 (Move11T2, MOVE_11_out, T2);
  and and_13 (and_13_out, MOVE_11_out, T4);
  or or_17 (or_17_out, Move00T0, Move11T1, Add00T0, Add01T0, Add10T1, Add11T1, Sub01T0, Sub10T1, Mul00T0, Mul01T0, Mul10T1, Mul11T1, And00T0, And01T0, And10T1, And11T1);
  or or_18 (or_18_out, Or00T0, Or01T0, Or10T1, Or11T1, NotT0, Xor00T0, Xor01T0, Xor10T1, Xor11T1, Trap00T0);
  or or_19 (Rsa, or_17_out, or_18_out);
  and and_14 (Add00T0, ADD_00_out, T0);
  and and_15 (Add00T1, ADD_00_out, T1);
  or or_20 (Rsb, Sub00T0, Sub11T1);
  and and_16 (Add01T0, ADD_01_out, T0);
  and and_17 (Add01T1, ADD_01_out, T1);
  buf or_21 (Rda, Sub00T0);  // OR_Gate
  and and_18 (Add10T0, ADD_10_out, T0);
  and and_19 (Add10T1, ADD_10_out, T1);
  and and_20 (Add10T2, ADD_10_out, T2);
  and and_21 (and_21_out, ADD_10_out, T4);
  or or_22 (Rdb, Add00T0, Mul00T0, And00T0, Or00T0, Xor00T0);
  and and_22 (Add11T0, ADD_11_out, T0);
  and and_23 (Add11T1, ADD_11_out, T1);
  and and_24 (Add11T2, ADD_11_out, T2);
  and and_25 (and_25_out, ADD_11_out, T4);
  or or_23 (Emem, FetchT1, Move10T1, Add10T1, Add11T1, Sub10T1, Sub11T1, Mul10T1, Mul11T1, And10T1, And11T1, Or10T1, Or11T1, Xor10T1, Xor11T1, Trap01T1);
  and and_26 (Sub00T0, SUB_00_out, T0);
  and and_27 (Sub00T1, SUB_00_out, T1);
  and and_28 (Sub01T0, SUB_01_out, T0);
  and and_29 (Sub01T1, SUB_01_out, T1);
  or or_24 (or_24_out, Move01T0, Move10T0, Move11T0, Add01T0, Add10T0, Add11T0, Sub01T0, Sub10T0, Sub11T0, Mul01T0, Mul10T0, Mul11T0, And01T0, And10T0, And11T0);
  or or_25 (or_25_out, Or01T0, Or10T0, Or11T0, Xor01T0, Xor10T0, Xor11T0, BeqT0, BneT0, BhiT0, BcsT0, BccT0, BlsT0, JmpT0, Trap01T0);
  or or_26 (Eir, or_24_out, or_25_out);
  and and_30 (Sub10T0, SUB_10_out, T0);
  and and_31 (Sub10T1, SUB_10_out, T1);
  and and_32 (Sub10T2, SUB_10_out, T2);
  and and_33 (and_33_out, SUB_10_out, T4);
  buf or_27 (Epc, FetchT0);  // OR_Gate
  and and_34 (Sub11T0, SUB_11_out, T0);
  and and_35 (Sub11T1, SUB_11_out, T1);
  and and_36 (Sub11T2, SUB_11_out, T2);
  and and_37 (and_37_out, SUB_11_out, T4);
  or or_28 (Ebr, BeqT0, BneT0, BhiT0, BcsT0, BccT0, BlsT0, JmpT0);
  and and_38 (Mul00T0, MUL_00_out, T0);
  and and_39 (Mul00T1, MUL_00_out, T1);
  and and_40 (Mul01T0, MUL_01_out, T0);
  and and_41 (Mul01T1, MUL_01_out, T1);
  or or_29 (or_29_out, Move00T0, Move11T1, Add00T0, Add01T0, Add01T1, Add10T1, Add10T2, Add11T1, Sub00T0, Sub01T0, Sub01T1, Sub10T1, Sub10T2, Sub11T1, Mul00T0, Mul01T0);
  or or_30 (or_30_out, Mul01T1, Mul10T1, Mul10T2, Mul11T1, And00T0, And01T0, And01T1, And10T1, And10T2, And11T1, Or00T0, Or01T0, Or01T1, Or10T1, Or10T2, Or11T1);
  or or_31 (or_31_out, NotT0, NotT1, Xor00T0, Xor01T0, Xor01T1, Xor10T1, Xor10T2, Xor11T1, Move01T0, Move10T1, Trap00T0);
  and and_42 (Mul10T0, MUL_10_out, T0);
  and and_43 (Mul10T1, MUL_10_out, T1);
  and and_44 (Mul10T2, MUL_10_out, T2);
  and and_45 (and_45_out, MUL_10_out, T4);
  or or_32 (Ers, or_29_out, or_30_out, or_31_out);
  and and_46 (Mul11T0, MUL_11_out, T0);
  and and_47 (Mul11T1, MUL_11_out, T1);
  and and_48 (Mul11T2, MUL_11_out, T2);
  and and_49 (and_49_out, MUL_11_out, T4);
  and and_50 (And00T0, AND_00_out, T0);
  and and_51 (And00T1, AND_00_out, T1);
  or or_33 (Erd, Add00T0, Add00T1, Sub00T0, Sub00T1, Mul00T0, Mul00T1, And00T0, And00T1, Or00T0, Or00T1, Xor00T0, Xor00T1, Move00T1);
  and and_52 (And01T0, AND_01_out, T0);
  and and_53 (And01T1, AND_01_out, T1);
  or or_34 (or_34_out, Move00T1, Move11T2, Add00T1, Add01T1, Add10T2, Add11T2, Sub00T1, Sub01T1, Sub10T2, Sub11T2, Mul00T1, Mul01T1, Mul10T2, Mul11T2, And00T1, And01T1);
  or or_35 (or_35_out, And10T2, And11T2, Or00T1, Or01T1, Or10T2, Or11T2, NotT1, Xor00T1, Xor01T1, Xor10T2, Xor11T2, Trap00T0);
  and and_54 (And10T0, AND_10_out, T0);
  and and_55 (And10T1, AND_10_out, T1);
  and and_56 (And10T2, AND_10_out, T2);
  and and_57 (and_57_out, AND_10_out, T4);
  or or_36 (Ex, or_34_out, or_35_out);
  and and_58 (And11T0, AND_11_out, T0);
  and and_59 (And11T1, AND_11_out, T1);
  and and_60 (And11T2, AND_11_out, T2);
  and and_61 (and_61_out, AND_11_out, T4);
  buf or_37 (A, Sub11T1);  // OR_Gate
  and and_62 (Or00T0, OR_00_out, T0);
  and and_63 (Or00T1, OR_00_out, T1);
  or or_38 (or_38_out, Add01T0, Add10T1, Add11T1, Sub01T0, Sub10T1, Mul01T0, Mul10T1, Mul11T1, And01T0, And10T1, And11T1, Or01T0, Or10T1, Or11T1, Xor01T0, Xor10T1);
  buf or_39 (or_39_out, Xor11T1);  // OR_Gate
  and and_64 (Or01T0, OR_01_out, T0);
  and and_65 (Or01T1, OR_01_out, T1);
  or or_40 (B, or_38_out, or_39_out);
  and and_66 (Or10T0, OR_10_out, T0);
  and and_67 (Or10T1, OR_10_out, T1);
  and and_68 (Or10T2, OR_10_out, T2);
  and and_69 (and_69_out, OR_10_out, T4);
  and and_70 (Or11T0, OR_11_out, T0);
  and and_71 (Or11T1, OR_11_out, T1);
  and and_72 (Or11T2, OR_11_out, T2);
  and and_73 (and_73_out, OR_11_out, T4);
  or or_41 (F2, And00T0, And01T0, And10T1, And11T1, Or00T0, Or01T0, Or10T1, Or11T1, NotT0, Xor00T0, Xor01T0, Xor10T1, Xor11T1);
  and and_74 (NotT0, NOT_10_out, T0);
  and and_75 (NotT1, NOT_10_out, T1);
  or or_42 (F1, Sub00T0, Sub01T0, Sub10T1, Sub11T1, Mul00T0, Mul01T0, Mul10T1, Mul11T1, NotT0, Xor00T0, Xor01T0, Xor10T1, Xor11T1);
  and and_76 (Xor00T0, XOR_00_out, T0);
  and and_77 (Xor00T1, XOR_00_out, T1);
  and and_78 (Xor01T0, XOR_01_out, T0);
  and and_79 (Xor01T1, XOR_01_out, T1);
  or or_43 (F0, Add00T0, Add01T0, Add10T1, Add11T1, Mul00T0, Mul01T0, Mul10T1, Mul11T1, Or00T0, Or01T0, Or10T1, Or11T1, Xor00T0, Xor01T0, Xor10T1, Xor11T1);
  and and_80 (Xor10T0, XOR_10_out, T0);
  and and_81 (Xor10T1, XOR_10_out, T1);
  and and_82 (Xor10T2, XOR_10_out, T2);
  and and_83 (and_83_out, XOR_10_out, T4);
  or or_44 (Trap, Trap00T0, Trap01T1);
  and and_84 (Xor11T0, XOR_11_out, T0);
  and and_85 (Xor11T1, XOR_11_out, T1);
  and and_86 (Xor11T2, XOR_11_out, T2);
  and and_87 (and_87_out, XOR_11_out, T4);
  and and_88 (BeqT0, BEQ_out, T0);
  and and_89 (and_89_out, BEQ_out, T1);
  and and_90 (BneT0, BNE_out, T0);
  and and_91 (and_91_out, BNE_out, T1);
  and and_92 (BhiT0, BHI_out, T0);
  and and_93 (and_93_out, BHI_out, T1);
  and and_94 (BcsT0, BCS_out, T0);
  and and_95 (and_95_out, BCS_out, T1);
  and and_96 (BccT0, BCC_out, T0);
  and and_97 (and_97_out, BCC_out, T1);
  and and_98 (BlsT0, BLS_out, T0);
  and and_99 (and_99_out, BLS_out, T1);
  and and_100 (JmpT0, JUMP_out, T0);
  and and_101 (and_101_out, JUMP_out, T1);
  not not_11 (not_11_out, s_r_ff_1_q);
  and and_102 (Trap00T0, TRAP_00_out, T0);
  and and_103 (and_103_out, TRAP_00_out, T1);
  and and_104 (Trap01T1, TRAP_01_out, T1);
  and and_105 (Trap01T0, TRAP_01_out, T0);
  or or_45 (or_45_out, not_11_out, TRAP_01_out, TRAP_00_out, JUMP_out, MOVE_00_out, MOVE_01_out, MOVE_10_out);
  or or_46 (or_46_out, or_45_out, or_47_out);
  or or_47 (or_47_out, MOVE_11_out, ADD_00_out, ADD_01_out, ADD_10_out, ADD_11_out, SUB_00_out, SUB_01_out, SUB_10_out, SUB_11_out, MUL_00_out, MUL_01_out, MUL_10_out, MUL_11_out, AND_00_out, AND_01_out, AND_10_out, AND_11_out, OR_00_out, OR_01_out, OR_10_out, OR_11_out, NOT_10_out, XOR_00_out, XOR_01_out, XOR_10_out, XOR_11_out, BEQ_out, BNE_out, BHI_out, BCS_out, BCC_out, BLS_out);
  not not_12 (ConditionNotMet, or_46_out);
endmodule

module Sequencer (
  input  Clear_to_state_T0,
  input  Disable_Clock,
  output T0,
  output T1,
  output T2,
  output T3,
  output T4,
  output T5,
  output T6,
  output T7
);

  wire clock_1_out, controlled_buffer_1_out, j_k_ff_1_q, j_k_ff_1_qn, j_k_ff_2_q, j_k_ff_2_qn, j_k_ff_3_q,
       j_k_ff_3_qn, not_1_out;

  not not_1 (not_1_out, Disable_Clock);
  Clock clock_1 (.out(clock_1_out));
  assign controlled_buffer_1_out = not_1_out ? clock_1_out : 1'bz;  // Controlled_Buffer controlled_buffer_1
  J_K_Flip_Flop #(.trigger("falling")) j_k_ff_1 (
    .J(1'b1), .clk(controlled_buffer_1_out), .K(1'b1), .Q(j_k_ff_1_q), .Qn(j_k_ff_1_qn),
    .reset(Clear_to_state_T0));  // open: preset, en
  J_K_Flip_Flop #(.trigger("falling")) j_k_ff_2 (
    .J(1'b1), .clk(j_k_ff_1_q), .K(1'b1), .Q(j_k_ff_2_q), .Qn(j_k_ff_2_qn), .reset(Clear_to_state_T0));  // open: preset, en
  J_K_Flip_Flop #(.trigger("falling")) j_k_ff_3 (
    .J(1'b1), .clk(j_k_ff_2_q), .K(1'b1), .Q(j_k_ff_3_q), .Qn(j_k_ff_3_qn), .reset(Clear_to_state_T0));  // open: preset, en
  and and_1 (T0, j_k_ff_3_qn, j_k_ff_2_qn, j_k_ff_1_qn);
  and and_2 (T1, j_k_ff_3_qn, j_k_ff_2_qn, j_k_ff_1_q);
  and and_3 (T2, j_k_ff_3_qn, j_k_ff_2_q, j_k_ff_1_qn);
  and and_4 (T3, j_k_ff_3_qn, j_k_ff_2_q, j_k_ff_1_q);
  and and_5 (T4, j_k_ff_3_q, j_k_ff_2_qn, j_k_ff_1_qn);
  and and_6 (T5, j_k_ff_3_q, j_k_ff_2_qn, j_k_ff_1_q);
  and and_7 (T6, j_k_ff_3_q, j_k_ff_2_q, j_k_ff_1_qn);
  and and_8 (T7, j_k_ff_3_q, j_k_ff_2_q, j_k_ff_1_q);
endmodule

module JK_flipflop (
  input  J,
  input  CLK,
  input  K,
  input  Clear,
  output Q,
  output nQ
);

  wire and_1_out, and_2_out, and_3_out, and_4_out, and_5_out, and_6_out, and_7_out, and_8_out, buffer_1_out,
       not_1_out, not_2_out, not_3_out, not_4_out, not_5_out, not_6_out, not_7_out, not_8_out, not_9_out;

  not not_1 (not_1_out, CLK);
  and and_1 (and_1_out, nQ, J, not_1_out);
  not not_2 (not_2_out, and_1_out);
  not not_3 (not_3_out, and_2_out);
  and and_2 (and_2_out, not_1_out, K, Q);
  not not_4 (not_4_out, Clear);
  buf buffer_1 (buffer_1_out, not_2_out);
  and and_3 (and_3_out, buffer_1_out, not_6_out);
  and and_4 (and_4_out, not_5_out, not_4_out, not_3_out);
  not not_5 (not_5_out, and_3_out);
  not not_6 (not_6_out, and_4_out);
  not not_7 (not_7_out, not_1_out);
  and and_5 (and_5_out, not_7_out, not_5_out);
  and and_6 (and_6_out, not_7_out, not_6_out);
  not not_8 (not_8_out, and_5_out);
  not not_9 (not_9_out, and_6_out);
  and and_7 (and_7_out, not_8_out, nQ);
  not not_10 (Q, and_7_out);
  not not_11 (nQ, and_8_out);
  and and_8 (and_8_out, Q, not_4_out, not_9_out);
endmodule
