// Logisim project HexDigitalDecode.circ as structural Verilog: 2 circuits, main circuit main
module main (
  input  [7:0] Value_in,
  output [3:0] _10_s,
  output [3:0] _1_s,
  output [3:0] _100_s
);

  wire _1_out_5, _1_out_6, _1_out_7, _1_out_8, _2_out_5, _2_out_6, _2_out_7, _2_out_8, _3_out_5, _3_out_6,
       _3_out_7, _3_out_8, _4_out_5, _4_out_6, _4_out_7, _4_out_8, _6_out_6, _6_out_7, _6_out_8;

  C _6 (
    .in_1(1'b0), .in_2(_1_out_5), .in_3(_2_out_5), .in_4(_3_out_5), .out_5(_100_s[1]), .out_6(_6_out_6),
    .out_7(_6_out_7), .out_8(_6_out_8));
  C _1 (
    .in_1(1'b0), .in_2(Value_in[7]), .in_3(Value_in[6]), .in_4(Value_in[5]), .out_5(_1_out_5),
    .out_6(_1_out_6), .out_7(_1_out_7), .out_8(_1_out_8));
  C _2 (
    .in_1(_1_out_6), .in_2(_1_out_7), .in_3(_1_out_8), .in_4(Value_in[4]), .out_5(_2_out_5),
    .out_6(_2_out_6), .out_7(_2_out_7), .out_8(_2_out_8));
  C _3 (
    .in_1(_2_out_6), .in_2(_2_out_7), .in_3(_2_out_8), .in_4(Value_in[3]), .out_5(_3_out_5),
    .out_6(_3_out_6), .out_7(_3_out_7), .out_8(_3_out_8));
  C _7 (
    .in_1(_6_out_6), .in_2(_6_out_7), .in_3(_6_out_8), .in_4(_4_out_5), .out_5(_100_s[0]), .out_6(_10_s[3]),
    .out_7(_10_s[2]), .out_8(_10_s[1]));
  C _4 (
    .in_1(_3_out_6), .in_2(_3_out_7), .in_3(_3_out_8), .in_4(Value_in[2]), .out_5(_4_out_5),
    .out_6(_4_out_6), .out_7(_4_out_7), .out_8(_4_out_8));
  C _5 (
    .in_1(_4_out_6), .in_2(_4_out_7), .in_3(_4_out_8), .in_4(Value_in[1]), .out_5(_10_s[0]), .out_6(_1_s[3]),
    .out_7(_1_s[2]), .out_8(_1_s[1]));

  assign _1_s[0] = Value_in[0];
  assign _100_s[3:2] = 2'b00;
endmodule

module C (
  input  in_1,
  input  in_2,
  input  in_3,
  input  in_4,
  output out_5,
  output out_6,
  output out_7,
  output out_8
);

  wire comparator_1_lt;
  wire [3:0] adder_1_out;

  Comparator #(.width(4), .mode("unsigned")) comparator_1 (
    .a({in_1, in_2, in_3, in_4}), .b(4'b0101), .lt(comparator_1_lt));  // open: gt, eq
  Adder #(.width(4)) adder_1 (.a({in_1, in_2, in_3, in_4}), .b(4'b0011), .out(adder_1_out));  // open: cin, cout
  Multiplexer #(.width(4)) multiplexer_1 (
    .in0(adder_1_out), .in1({in_1, in_2, in_3, in_4}), .out({out_5, out_6, out_7, out_8}),
    .sel(comparator_1_lt));  // open: en
endmodule
