// Logisim project MemoryUnit32Address.circ as structural Verilog: 4 circuits, main circuit Memory 32Address
// 32 Address Memory
module Memory_32Address (
  input  [15:0] Data_in,
  input  [15:0] Manual_input,
  input  Read_enable,
  input  Write_enable,
  input  Manual_select,
  input  [4:0] Address,
  output [15:0] out_7,
  output [15:0] out_8,
  output [15:0] out_9,
  output [15:0] out_10,
  output [15:0] out_11,
  output [15:0] out_12,
  output [15:0] out_13,
  output [15:0] out_14,
  output [15:0] out_15,
  output [15:0] out_16,
  output [15:0] out_17,
  output [15:0] out_18,
  output [15:0] out_19,
  output [15:0] out_20,
  output [15:0] out_21,
  output [15:0] out_22,
  output [15:0] out_23,
  output [15:0] out_24,
  output [15:0] out_25,
  output [15:0] out_26,
  output [15:0] out_27,
  output [15:0] out_28,
  output [15:0] out_29,
  output [15:0] out_30,
  output [15:0] out_31,
  output [15:0] out_32,
  output [15:0] out_33,
  output [15:0] out_34,
  output [15:0] out_35,
  output [15:0] out_36,
  output [15:0] out_37,
  output [15:0] out_38,
  output [15:0] out_39
);

  wire n5_32_bit_decoder_1_out_6, n5_32_bit_decoder_1_out_7, n5_32_bit_decoder_1_out_8,
       n5_32_bit_decoder_1_out_9, n5_32_bit_decoder_1_out_10, n5_32_bit_decoder_1_out_11,
       n5_32_bit_decoder_1_out_12, n5_32_bit_decoder_1_out_13, n5_32_bit_decoder_1_out_14,
       n5_32_bit_decoder_1_out_15, n5_32_bit_decoder_1_out_16, n5_32_bit_decoder_1_out_17,
       n5_32_bit_decoder_1_out_18, n5_32_bit_decoder_1_out_19, n5_32_bit_decoder_1_out_20,
       n5_32_bit_decoder_1_out_21, n5_32_bit_decoder_1_out_22, n5_32_bit_decoder_1_out_23,
       n5_32_bit_decoder_1_out_24, n5_32_bit_decoder_1_out_25, n5_32_bit_decoder_1_out_26,
       n5_32_bit_decoder_1_out_27, n5_32_bit_decoder_1_out_28, n5_32_bit_decoder_1_out_29,
       n5_32_bit_decoder_1_out_30, n5_32_bit_decoder_1_out_31, n5_32_bit_decoder_1_out_32,
       n5_32_bit_decoder_1_out_33, n5_32_bit_decoder_1_out_34, n5_32_bit_decoder_1_out_35,
       n5_32_bit_decoder_1_out_36, n5_32_bit_decoder_1_out_37;
  wire [15:0] multiplexer_1_out;

  _5_32_bit_decoder u_5_32_bit_decoder_1 (
    .out_6(n5_32_bit_decoder_1_out_6), .out_7(n5_32_bit_decoder_1_out_7), .out_8(n5_32_bit_decoder_1_out_8),
    .out_9(n5_32_bit_decoder_1_out_9), .out_10(n5_32_bit_decoder_1_out_10),
    .out_11(n5_32_bit_decoder_1_out_11), .out_12(n5_32_bit_decoder_1_out_12),
    .out_13(n5_32_bit_decoder_1_out_13), .out_14(n5_32_bit_decoder_1_out_14),
    .out_15(n5_32_bit_decoder_1_out_15), .out_16(n5_32_bit_decoder_1_out_16),
    .out_17(n5_32_bit_decoder_1_out_17), .out_18(n5_32_bit_decoder_1_out_18),
    .out_19(n5_32_bit_decoder_1_out_19), .out_20(n5_32_bit_decoder_1_out_20),
    .out_21(n5_32_bit_decoder_1_out_21), .out_22(n5_32_bit_decoder_1_out_22),
    .out_23(n5_32_bit_decoder_1_out_23), .out_24(n5_32_bit_decoder_1_out_24),
    .out_25(n5_32_bit_decoder_1_out_25), .out_26(n5_32_bit_decoder_1_out_26),
    .out_27(n5_32_bit_decoder_1_out_27), .out_28(n5_32_bit_decoder_1_out_28),
    .out_29(n5_32_bit_decoder_1_out_29), .out_30(n5_32_bit_decoder_1_out_30),
    .out_31(n5_32_bit_decoder_1_out_31), .out_32(n5_32_bit_decoder_1_out_32),
    .out_33(n5_32_bit_decoder_1_out_33), .out_34(n5_32_bit_decoder_1_out_34),
    .out_35(n5_32_bit_decoder_1_out_35), .out_36(n5_32_bit_decoder_1_out_36),
    .out_37(n5_32_bit_decoder_1_out_37), ._4(Address[4]), ._3(Address[3]), ._2(Address[2]), ._1(Address[1]),
    ._0(Address[0]));
  Multiplexer #(.width(16)) multiplexer_1 (
    .in0(Data_in), .in1(Manual_input), .out(multiplexer_1_out), .sel(Manual_select));  // open: en
  Memory_line_16_bit memory_line_16_bit_1 (
    .Write(Write_enable), .Enable(n5_32_bit_decoder_1_out_6), .Data_in(multiplexer_1_out), .out_4(out_8));
  Memory_line_16_bit memory_line_16_bit_2 (
    .Write(Write_enable), .Enable(n5_32_bit_decoder_1_out_7), .Data_in(multiplexer_1_out), .out_4(out_10));
  Memory_line_16_bit memory_line_16_bit_3 (
    .Write(Write_enable), .Enable(n5_32_bit_decoder_1_out_8), .Data_in(multiplexer_1_out), .out_4(out_12));
  Memory_line_16_bit memory_line_16_bit_4 (
    .Write(Write_enable), .Enable(n5_32_bit_decoder_1_out_9), .Data_in(multiplexer_1_out), .out_4(out_15));
  Memory_line_16_bit memory_line_16_bit_5 (
    .Write(Write_enable), .Enable(n5_32_bit_decoder_1_out_10), .Data_in(multiplexer_1_out), .out_4(out_17));
  Memory_line_16_bit memory_line_16_bit_6 (
    .Write(Write_enable), .Enable(n5_32_bit_decoder_1_out_11), .Data_in(multiplexer_1_out), .out_4(out_19));
  Memory_line_16_bit memory_line_16_bit_7 (
    .Write(Write_enable), .Enable(n5_32_bit_decoder_1_out_12), .Data_in(multiplexer_1_out), .out_4(out_21));
  Memory_line_16_bit memory_line_16_bit_8 (
    .Write(Write_enable), .Enable(n5_32_bit_decoder_1_out_13), .Data_in(multiplexer_1_out), .out_4(out_23));
  Memory_line_16_bit memory_line_16_bit_9 (
    .Write(Write_enable), .Enable(n5_32_bit_decoder_1_out_14), .Data_in(multiplexer_1_out), .out_4(out_25));
  Memory_line_16_bit memory_line_16_bit_10 (
    .Write(Write_enable), .Enable(n5_32_bit_decoder_1_out_15), .Data_in(multiplexer_1_out), .out_4(out_27));
  Memory_line_16_bit memory_line_16_bit_11 (
    .Write(Write_enable), .Enable(n5_32_bit_decoder_1_out_16), .Data_in(multiplexer_1_out), .out_4(out_29));
  Memory_line_16_bit memory_line_16_bit_12 (
    .Write(Write_enable), .Enable(n5_32_bit_decoder_1_out_17), .Data_in(multiplexer_1_out), .out_4(out_31));
  Memory_line_16_bit memory_line_16_bit_13 (
    .Write(Write_enable), .Enable(n5_32_bit_decoder_1_out_18), .Data_in(multiplexer_1_out), .out_4(out_33));
  Memory_line_16_bit memory_line_16_bit_14 (
    .Write(Write_enable), .Enable(n5_32_bit_decoder_1_out_19), .Data_in(multiplexer_1_out), .out_4(out_35));
  Memory_line_16_bit memory_line_16_bit_15 (
    .Write(Write_enable), .Enable(n5_32_bit_decoder_1_out_20), .Data_in(multiplexer_1_out), .out_4(out_37));
  Memory_line_16_bit memory_line_16_bit_16 (
    .Write(Write_enable), .Enable(n5_32_bit_decoder_1_out_21), .Data_in(multiplexer_1_out), .out_4(out_39));
  Memory_line_16_bit memory_line_16_bit_17 (
    .Write(Write_enable), .Enable(n5_32_bit_decoder_1_out_22), .Data_in(multiplexer_1_out), .out_4(out_7));
  Memory_line_16_bit memory_line_16_bit_18 (
    .Write(Write_enable), .Enable(n5_32_bit_decoder_1_out_23), .Data_in(multiplexer_1_out), .out_4(out_9));
  Memory_line_16_bit memory_line_16_bit_19 (
    .Write(Write_enable), .Enable(n5_32_bit_decoder_1_out_24), .Data_in(multiplexer_1_out), .out_4(out_11));
  Memory_line_16_bit memory_line_16_bit_20 (
    .Write(Write_enable), .Enable(n5_32_bit_decoder_1_out_25), .Data_in(multiplexer_1_out), .out_4(out_14));
  Memory_line_16_bit memory_line_16_bit_21 (
    .Write(Write_enable), .Enable(n5_32_bit_decoder_1_out_26), .Data_in(multiplexer_1_out), .out_4(out_16));
  Memory_line_16_bit memory_line_16_bit_22 (
    .Write(Write_enable), .Enable(n5_32_bit_decoder_1_out_27), .Data_in(multiplexer_1_out), .out_4(out_18));
  Memory_line_16_bit memory_line_16_bit_23 (
    .Write(Write_enable), .Enable(n5_32_bit_decoder_1_out_28), .Data_in(multiplexer_1_out), .out_4(out_20));
  Memory_line_16_bit memory_line_16_bit_24 (
    .Write(Write_enable), .Enable(n5_32_bit_decoder_1_out_29), .Data_in(multiplexer_1_out), .out_4(out_22));
  Memory_line_16_bit memory_line_16_bit_25 (
    .Write(Write_enable), .Enable(n5_32_bit_decoder_1_out_30), .Data_in(multiplexer_1_out), .out_4(out_24));
  Memory_line_16_bit memory_line_16_bit_26 (
    .Write(Write_enable), .Enable(n5_32_bit_decoder_1_out_31), .Data_in(multiplexer_1_out), .out_4(out_26));
  Memory_line_16_bit memory_line_16_bit_27 (
    .Write(Write_enable), .Enable(n5_32_bit_decoder_1_out_32), .Data_in(multiplexer_1_out), .out_4(out_28));
  Memory_line_16_bit memory_line_16_bit_28 (
    .Write(Write_enable), .Enable(n5_32_bit_decoder_1_out_33), .Data_in(multiplexer_1_out), .out_4(out_30));
  Memory_line_16_bit memory_line_16_bit_29 (
    .Write(Write_enable), .Enable(n5_32_bit_decoder_1_out_34), .Data_in(multiplexer_1_out), .out_4(out_32));
  Memory_line_16_bit memory_line_16_bit_30 (
    .Write(Write_enable), .Enable(n5_32_bit_decoder_1_out_35), .Data_in(multiplexer_1_out), .out_4(out_34));
  Memory_line_16_bit memory_line_16_bit_31 (
    .Write(Write_enable), .Enable(n5_32_bit_decoder_1_out_36), .Data_in(multiplexer_1_out), .out_4(out_36));
  Memory_line_16_bit memory_line_16_bit_32 (
    .Write(Write_enable), .Enable(n5_32_bit_decoder_1_out_37), .Data_in(multiplexer_1_out), .out_4(out_38));
  Multiplexer #(.select(5), .width(16)) multiplexer_2 (
    .in0(out_8), .in1(out_10), .in2(out_12), .in3(out_15), .in4(out_17), .in5(out_19), .in6(out_21),
    .in7(out_23), .in8(out_25), .in9(out_27), .in10(out_29), .in11(out_31), .in12(out_33), .in13(out_35),
    .in14(out_37), .in15(out_39), .in16(out_7), .in17(out_9), .in18(out_11), .in19(out_14), .in20(out_16),
    .in21(out_18), .in22(out_20), .in23(out_22), .in24(out_24), .in25(out_26), .in26(out_28), .in27(out_30),
    .in28(out_32), .in29(out_34), .in30(out_36), .in31(out_38), .out(out_13), .sel(Address), .en(Read_enable));

  // Other names for the same wires on the sheet: A1[15:0] = out_8; A2[15:0] = out_10; A3[15:0] = out_12;
  //   A4[15:0] = out_15; A5[15:0] = out_17; A6[15:0] = out_19; A7[15:0] = out_21; A8[15:0] = out_23;
  //   A9[15:0] = out_25; A10[15:0] = out_27; A11[15:0] = out_29; A12[15:0] = out_31; A13[15:0] = out_33;
  //   A14[15:0] = out_35; A15[15:0] = out_37; A16[15:0] = out_39; A17[15:0] = out_7; A18[15:0] = out_9;
  //   A19[15:0] = out_11; A20[15:0] = out_14; A21[15:0] = out_16; A22[15:0] = out_18; A23[15:0] = out_20;
  //   A24[15:0] = out_22; A25[15:0] = out_24; A26[15:0] = out_26; A27[15:0] = out_28; A28[15:0] = out_30;
  //   A29[15:0] = out_32; A30[15:0] = out_34; A31[15:0] = out_36; A32[15:0] = out_38
endmodule

module _5_32_bit_decoder (
  input  _0,
  input  _1,
  input  _2,
  input  _3,
  input  _4,
  output out_6,
  output out_7,
  output out_8,
  output out_9,
  output out_10,
  output out_11,
  output out_12,
  output out_13,
  output out_14,
  output out_15,
  output out_16,
  output out_17,
  output out_18,
  output out_19,
  output out_20,
  output out_21,
  output out_22,
  output out_23,
  output out_24,
  output out_25,
  output out_26,
  output out_27,
  output out_28,
  output out_29,
  output out_30,
  output out_31,
  output out_32,
  output out_33,
  output out_34,
  output out_35,
  output out_36,
  output out_37
);

  wire not_1_out, not_2_out, not_3_out, not_4_out, not_5_out;

  not not_1 (not_1_out, _4);
  not not_2 (not_2_out, _3);
  not not_3 (not_3_out, _2);
  not not_4 (not_4_out, _1);
  not not_5 (not_5_out, _0);
  and and_1 (out_6, not_5_out, not_4_out, not_3_out, not_2_out, not_1_out);
  and and_2 (out_7, _0, not_4_out, not_3_out, not_2_out, not_1_out);
  and and_3 (out_8, not_5_out, _1, not_3_out, not_2_out, not_1_out);
  and and_4 (out_9, _0, _1, not_3_out, not_2_out, not_1_out);
  and and_5 (out_10, not_5_out, not_4_out, _2, not_2_out, not_1_out);
  and and_6 (out_11, _0, not_4_out, _2, not_2_out, not_1_out);
  and and_7 (out_12, not_5_out, _1, _2, not_2_out, not_1_out);
  and and_8 (out_13, _0, _1, _2, not_2_out, not_1_out);
  and and_9 (out_14, not_5_out, not_4_out, not_3_out, _3, not_1_out);
  and and_10 (out_15, _0, not_4_out, not_3_out, _3, not_1_out);
  and and_11 (out_16, not_5_out, _1, not_3_out, _3, not_1_out);
  and and_12 (out_17, _0, _1, not_3_out, _3, not_1_out);
  and and_13 (out_18, not_5_out, not_4_out, _2, _3, not_1_out);
  and and_14 (out_19, _0, not_4_out, _2, _3, not_1_out);
  and and_15 (out_20, not_5_out, _1, _2, _3, not_1_out);
  and and_16 (out_22, not_5_out, not_4_out, not_3_out, not_2_out, _4);
  and and_17 (out_23, _0, not_4_out, not_3_out, not_2_out, _4);
  and and_18 (out_24, not_5_out, _1, not_3_out, not_2_out, _4);
  and and_19 (out_25, _0, _1, not_3_out, not_2_out, _4);
  and and_20 (out_26, not_5_out, not_4_out, _2, not_2_out, _4);
  and and_21 (out_27, _0, not_4_out, _2, not_2_out, _4);
  and and_22 (out_28, not_5_out, _1, _2, not_2_out, _4);
  and and_23 (out_29, _0, _1, _2, not_2_out, _4);
  and and_24 (out_30, not_5_out, not_4_out, not_3_out, _3, _4);
  and and_25 (out_31, _0, not_4_out, not_3_out, _3, _4);
  and and_26 (out_32, not_5_out, _1, not_3_out, _3, _4);
  and and_27 (out_33, _0, _1, not_3_out, _3, _4);
  and and_28 (out_34, not_5_out, not_4_out, _2, _3, _4);
  and and_29 (out_35, _0, not_4_out, _2, _3, _4);
  and and_30 (out_36, not_5_out, _1, _2, _3, _4);
  and and_31 (out_21, _0, _1, _2, _3, not_1_out);
  and and_32 (out_37, _0, _1, _2, _3, _4);
endmodule

// D
module D_flip_flop (
  input  Data_in,
  input  Enable,
  output out_3
);

  wire and_1_out, and_2_out, and_3_out, and_4_out, not_1_out, not_2_out, not_3_out, not_5_out;

  not not_1 (not_1_out, Data_in);
  and and_1 (and_1_out, Data_in, Enable);
  not not_2 (not_2_out, and_1_out);
  and and_2 (and_2_out, Enable, not_1_out);
  not not_3 (not_3_out, and_2_out);
  not not_4 (out_3, and_3_out);
  and and_3 (and_3_out, not_2_out, not_5_out);
  and and_4 (and_4_out, out_3, not_3_out);
  not not_5 (not_5_out, and_4_out);
endmodule

// 16-bit Memory Line
module Memory_line_16_bit (
  input  [15:0] Data_in,
  input  Write,
  input  Enable,
  output [15:0] out_4
);

  wire and_1_out;

  and and_1 (and_1_out, Write, Enable);
  D_Flip_Flop #(.trigger("high")) d_ff_1 (
    .clk(and_1_out), .D(Data_in[0]), .Q(out_4[0]));  // open: Qn, preset, en, reset
  D_Flip_Flop #(.trigger("high")) d_ff_2 (
    .clk(and_1_out), .D(Data_in[1]), .Q(out_4[1]));  // open: Qn, preset, en, reset
  D_Flip_Flop #(.trigger("high")) d_ff_3 (
    .clk(and_1_out), .D(Data_in[2]), .Q(out_4[2]));  // open: Qn, preset, en, reset
  D_Flip_Flop #(.trigger("high")) d_ff_4 (
    .clk(and_1_out), .D(Data_in[3]), .Q(out_4[3]));  // open: Qn, preset, en, reset
  D_Flip_Flop #(.trigger("high")) d_ff_5 (
    .clk(and_1_out), .D(Data_in[4]), .Q(out_4[4]));  // open: Qn, preset, en, reset
  D_Flip_Flop #(.trigger("high")) d_ff_6 (
    .clk(and_1_out), .D(Data_in[5]), .Q(out_4[5]));  // open: Qn, preset, en, reset
  D_Flip_Flop #(.trigger("high")) d_ff_7 (
    .clk(and_1_out), .D(Data_in[6]), .Q(out_4[6]));  // open: Qn, preset, en, reset
  D_Flip_Flop #(.trigger("high")) d_ff_8 (
    .clk(and_1_out), .D(Data_in[7]), .Q(out_4[7]));  // open: Qn, preset, en, reset
  D_Flip_Flop #(.trigger("high")) d_ff_9 (
    .clk(and_1_out), .D(Data_in[8]), .Q(out_4[8]));  // open: Qn, preset, en, reset
  D_Flip_Flop #(.trigger("high")) d_ff_10 (
    .clk(and_1_out), .D(Data_in[9]), .Q(out_4[9]));  // open: Qn, preset, en, reset
  D_Flip_Flop #(.trigger("high")) d_ff_11 (
    .clk(and_1_out), .D(Data_in[10]), .Q(out_4[10]));  // open: Qn, preset, en, reset
  D_Flip_Flop #(.trigger("high")) d_ff_12 (
    .clk(and_1_out), .D(Data_in[11]), .Q(out_4[11]));  // open: Qn, preset, en, reset
  D_Flip_Flop #(.trigger("high")) d_ff_13 (
    .clk(and_1_out), .D(Data_in[12]), .Q(out_4[12]));  // open: Qn, preset, en, reset
  D_Flip_Flop #(.trigger("high")) d_ff_14 (
    .clk(and_1_out), .D(Data_in[13]), .Q(out_4[13]));  // open: Qn, preset, en, reset
  D_Flip_Flop #(.trigger("high")) d_ff_15 (
    .clk(and_1_out), .D(Data_in[14]), .Q(out_4[14]));  // open: Qn, preset, en, reset
  D_Flip_Flop #(.trigger("high")) d_ff_16 (
    .clk(and_1_out), .D(Data_in[15]), .Q(out_4[15]), .en(and_1_out));  // open: Qn, preset, reset
endmodule
