// Logisim project Registers.circ as structural Verilog: 7 circuits, main circuit RegisterFile
// Registers
module RegisterFile (
  input  [15:0] Data_from_bus,
  input  Ws,
  input  [1:0] S,
  input  RSA,
  input  RDA,
  input  Wd,
  input  [1:0] D,
  input  RDB,
  input  RSB,
  output [7:0] R0,
  output [7:0] R1,
  output [7:0] R2,
  output [7:0] R3,
  output [15:0] A,
  output [15:0] B
);

  wire and_1_out, and_2_out, and_3_out, and_4_out, demultiplexer_1_out0, demultiplexer_1_out1,
       demultiplexer_1_out2, demultiplexer_1_out3, demultiplexer_2_out0, demultiplexer_2_out1,
       demultiplexer_2_out2, demultiplexer_2_out3, not_1_out, not_2_out, not_3_out, not_4_out, not_5_out,
       not_6_out, not_7_out, not_8_out, or_1_out, or_2_out, or_3_out, or_4_out, or_5_out, or_6_out, or_7_out,
       or_8_out;
  wire [7:0] buffer_1_out, buffer_2_out, buffer_3_out, multiplexer_1_out, multiplexer_2_out,
       multiplexer_3_out, multiplexer_4_out;

  Demultiplexer #(.select(2)) demultiplexer_1 (
    .out0(demultiplexer_1_out0), .out1(demultiplexer_1_out1), .out2(demultiplexer_1_out2),
    .out3(demultiplexer_1_out3), .in(Wd), .sel(D));  // open: en
  Demultiplexer #(.select(2)) demultiplexer_2 (
    .out0(demultiplexer_2_out0), .out1(demultiplexer_2_out1), .out2(demultiplexer_2_out2),
    .out3(demultiplexer_2_out3), .in(Ws), .sel(S));  // open: en
  assign buffer_1_out = Data_from_bus[7:0];  // Buffer buffer_1, 8 bits wide
  assign buffer_2_out = buffer_3_out;  // Buffer buffer_2, 8 bits wide
  assign buffer_3_out = buffer_1_out;  // Buffer buffer_3, 8 bits wide
  or or_1 (or_1_out, demultiplexer_2_out0, demultiplexer_1_out0);
  or or_2 (or_2_out, demultiplexer_2_out1, demultiplexer_1_out1);
  or or_3 (or_3_out, demultiplexer_2_out2, demultiplexer_1_out2);
  or or_4 (or_4_out, demultiplexer_2_out3, demultiplexer_1_out3);
  DataRegister u_R0 (.Data_in(buffer_2_out), .Allow_write(or_1_out), .Value_stored(R0));
  DataRegister u_R1 (.Data_in(buffer_2_out), .Allow_write(or_2_out), .Value_stored(R1));
  DataRegister u_R2 (.Data_in(buffer_2_out), .Allow_write(or_3_out), .Value_stored(R2));
  DataRegister u_R3 (.Data_in(buffer_2_out), .Allow_write(or_4_out), .Value_stored(R3));
  Multiplexer #(.select(2), .width(8)) multiplexer_1 (
    .in0(R0), .in1(R1), .in2(R2), .in3(R3), .out(multiplexer_1_out), .sel(S), .en(RSA));
  Multiplexer #(.select(2), .width(8)) multiplexer_2 (
    .in0(R0), .in1(R1), .in2(R2), .in3(R3), .out(multiplexer_2_out), .sel(D), .en(RDA));
  Multiplexer #(.select(2), .width(8)) multiplexer_3 (
    .in0(R0), .in1(R1), .in2(R2), .in3(R3), .out(multiplexer_3_out), .sel(D), .en(RDB));
  Multiplexer #(.select(2), .width(8)) multiplexer_4 (
    .in0(R0), .in1(R1), .in2(R2), .in3(R3), .out(multiplexer_4_out), .sel(S), .en(RSB));
  Multiplexer #(.width(8)) multiplexer_5 (
    .in0(multiplexer_1_out), .in1(multiplexer_2_out), .out(A[7:0]), .sel(or_5_out), .en(not_8_out));
  not not_1 (not_1_out, RSA);
  Multiplexer #(.width(8)) multiplexer_6 (
    .in0(multiplexer_3_out), .in1(multiplexer_4_out), .out(B[7:0]), .sel(or_6_out), .en(not_7_out));
  not not_2 (not_2_out, RDB);
  not not_3 (not_3_out, RSB);
  not not_4 (not_4_out, RDB);
  and and_1 (and_1_out, RSA, RDA);
  not not_5 (not_5_out, RSA);
  not not_6 (not_6_out, RDA);
  or or_5 (or_5_out, not_1_out, RDA);
  and and_2 (and_2_out, RDB, RSB);
  and and_3 (and_3_out, not_2_out, not_3_out);
  or or_6 (or_6_out, not_4_out, RSB);
  and and_4 (and_4_out, not_5_out, not_6_out);
  not not_7 (not_7_out, or_7_out);
  or or_7 (or_7_out, and_2_out, and_3_out);
  not not_8 (not_8_out, or_8_out);
  or or_8 (or_8_out, and_1_out, and_4_out);

  assign A[15:8] = {8{1'b0}};
  assign B[15:8] = {8{1'b0}};
endmodule

// PC
module Program_Counter (
  input  [15:0] Branch_to,
  input  Ebr,
  input  Cpc,
  output [15:0] Address_Out
);

  wire [4:0] Incrementer_result, multiplexer_1_out;

  Multiplexer #(.width(5)) multiplexer_1 (
    .in0(Incrementer_result), .in1(Branch_to[4:0]), .out(multiplexer_1_out), .sel(Ebr));  // open: en
  Register #(.width(5), .trigger("falling")) register_1 (
    .D(multiplexer_1_out), .Q(Address_Out[4:0]), .clk(Cpc));  // open: en, clr
  Incrementor Incrementer (.A(Address_Out[4:0]), .Result(Incrementer_result));

  assign Address_Out[15:5] = {11{1'b0}};
endmodule

// +1
module Incrementor (
  input  [4:0] A,
  output [4:0] Result
);

  wire full_adder_1_c_out, full_adder_2_c_out, full_adder_3_c_out, full_adder_4_c_out, full_adder_5_c_out;

  Full_adder full_adder_1 (.A(A[0]), .B(1'b1), .C_in(1'b0), .Sum(Result[0]), .C_out(full_adder_1_c_out));
  Full_adder full_adder_2 (.A(A[1]), .B(1'b0), .C_in(full_adder_1_c_out), .Sum(Result[1]), .C_out(full_adder_2_c_out));
  Full_adder full_adder_3 (.A(A[2]), .B(1'b0), .C_in(full_adder_2_c_out), .Sum(Result[2]), .C_out(full_adder_3_c_out));
  Full_adder full_adder_4 (.A(A[3]), .B(1'b0), .C_in(full_adder_3_c_out), .Sum(Result[3]), .C_out(full_adder_4_c_out));
  Full_adder full_adder_5 (.A(A[4]), .B(1'b0), .C_in(full_adder_4_c_out), .Sum(Result[4]), .C_out(full_adder_5_c_out));
endmodule

module MAR (
  input  [4:0] Address_in,
  input  Allow_write,
  output [4:0] Address_stored
);

  wire and_1_out, and_2_out, and_3_out, and_4_out, and_5_out, and_6_out, and_7_out, and_8_out, and_9_out,
       and_10_out, and_11_out, and_12_out, and_13_out, and_14_out, and_15_out, and_16_out, and_17_out,
       and_18_out, and_19_out, and_20_out, not_1_out, not_2_out, not_3_out, not_4_out, not_5_out, not_6_out,
       not_7_out, not_8_out, not_9_out, not_10_out, not_11_out, not_12_out, not_13_out, not_14_out,
       not_15_out, not_17_out, not_19_out, not_21_out, not_23_out, not_25_out;

  not not_1 (not_1_out, Address_in[0]);
  not not_2 (not_2_out, Address_in[1]);
  not not_3 (not_3_out, Address_in[2]);
  not not_4 (not_4_out, Address_in[3]);
  not not_5 (not_5_out, Address_in[4]);
  and and_1 (and_1_out, Address_in[0], Allow_write);
  and and_2 (and_2_out, Allow_write, not_1_out);
  and and_3 (and_3_out, Address_in[1], Allow_write);
  and and_4 (and_4_out, Allow_write, not_2_out);
  and and_5 (and_5_out, Address_in[2], Allow_write);
  and and_6 (and_6_out, Allow_write, not_3_out);
  and and_7 (and_7_out, Address_in[3], Allow_write);
  and and_8 (and_8_out, Allow_write, not_4_out);
  and and_9 (and_9_out, Address_in[4], Allow_write);
  and and_10 (and_10_out, Allow_write, not_5_out);
  not not_6 (not_6_out, and_1_out);
  not not_7 (not_7_out, and_2_out);
  not not_8 (not_8_out, and_3_out);
  not not_9 (not_9_out, and_4_out);
  not not_10 (not_10_out, and_5_out);
  not not_11 (not_11_out, and_6_out);
  not not_12 (not_12_out, and_7_out);
  not not_13 (not_13_out, and_8_out);
  not not_14 (not_14_out, and_9_out);
  not not_15 (not_15_out, and_10_out);
  and and_11 (and_11_out, not_6_out, not_17_out);
  and and_12 (and_12_out, Address_stored[0], not_7_out);
  and and_13 (and_13_out, not_8_out, not_19_out);
  and and_14 (and_14_out, Address_stored[1], not_9_out);
  and and_15 (and_15_out, not_10_out, not_21_out);
  and and_16 (and_16_out, Address_stored[2], not_11_out);
  and and_17 (and_17_out, not_12_out, not_23_out);
  and and_18 (and_18_out, Address_stored[3], not_13_out);
  and and_19 (and_19_out, not_14_out, not_25_out);
  and and_20 (and_20_out, Address_stored[4], not_15_out);
  not not_16 (Address_stored[0], and_11_out);
  not not_17 (not_17_out, and_12_out);
  not not_18 (Address_stored[1], and_13_out);
  not not_19 (not_19_out, and_14_out);
  not not_20 (Address_stored[2], and_15_out);
  not not_21 (not_21_out, and_16_out);
  not not_22 (Address_stored[3], and_17_out);
  not not_23 (not_23_out, and_18_out);
  not not_24 (Address_stored[4], and_19_out);
  not not_25 (not_25_out, and_20_out);
endmodule

// X
module Intermediate_register (
  input  [7:0] Data_in,
  input  Allow_write,
  output [15:0] Value_stored
);

  wire and_1_out, and_2_out, and_3_out, and_4_out, and_5_out, and_6_out, and_7_out, and_8_out, and_9_out,
       and_10_out, and_11_out, and_12_out, and_13_out, and_14_out, and_15_out, and_16_out, and_17_out,
       and_18_out, and_19_out, and_20_out, and_21_out, and_22_out, and_23_out, and_24_out, and_25_out,
       and_26_out, and_27_out, and_28_out, and_29_out, and_30_out, and_31_out, and_32_out, not_1_out,
       not_2_out, not_3_out, not_4_out, not_5_out, not_6_out, not_7_out, not_8_out, not_9_out, not_10_out,
       not_11_out, not_12_out, not_13_out, not_14_out, not_15_out, not_16_out, not_17_out, not_18_out,
       not_19_out, not_20_out, not_21_out, not_22_out, not_23_out, not_24_out, not_26_out, not_28_out,
       not_30_out, not_32_out, not_34_out, not_36_out, not_38_out, not_40_out;

  not not_1 (not_1_out, Data_in[0]);
  not not_2 (not_2_out, Data_in[1]);
  not not_3 (not_3_out, Data_in[2]);
  not not_4 (not_4_out, Data_in[3]);
  not not_5 (not_5_out, Data_in[4]);
  not not_6 (not_6_out, Data_in[5]);
  not not_7 (not_7_out, Data_in[6]);
  not not_8 (not_8_out, Data_in[7]);
  and and_1 (and_1_out, Data_in[0], Allow_write);
  and and_2 (and_2_out, Allow_write, not_1_out);
  and and_3 (and_3_out, Data_in[1], Allow_write);
  and and_4 (and_4_out, Allow_write, not_2_out);
  and and_5 (and_5_out, Data_in[2], Allow_write);
  and and_6 (and_6_out, Allow_write, not_3_out);
  and and_7 (and_7_out, Data_in[3], Allow_write);
  and and_8 (and_8_out, Allow_write, not_4_out);
  and and_9 (and_9_out, Data_in[4], Allow_write);
  and and_10 (and_10_out, Allow_write, not_5_out);
  and and_11 (and_11_out, Data_in[5], Allow_write);
  and and_12 (and_12_out, Allow_write, not_6_out);
  and and_13 (and_13_out, Data_in[6], Allow_write);
  and and_14 (and_14_out, Allow_write, not_7_out);
  and and_15 (and_15_out, Data_in[7], Allow_write);
  and and_16 (and_16_out, Allow_write, not_8_out);
  not not_9 (not_9_out, and_1_out);
  not not_10 (not_10_out, and_2_out);
  not not_11 (not_11_out, and_3_out);
  not not_12 (not_12_out, and_4_out);
  not not_13 (not_13_out, and_5_out);
  not not_14 (not_14_out, and_6_out);
  not not_15 (not_15_out, and_7_out);
  not not_16 (not_16_out, and_8_out);
  not not_17 (not_17_out, and_9_out);
  not not_18 (not_18_out, and_10_out);
  not not_19 (not_19_out, and_11_out);
  not not_20 (not_20_out, and_12_out);
  not not_21 (not_21_out, and_13_out);
  not not_22 (not_22_out, and_14_out);
  not not_23 (not_23_out, and_15_out);
  not not_24 (not_24_out, and_16_out);
  and and_17 (and_17_out, not_9_out, not_26_out);
  and and_18 (and_18_out, Value_stored[0], not_10_out);
  and and_19 (and_19_out, not_11_out, not_28_out);
  and and_20 (and_20_out, Value_stored[1], not_12_out);
  and and_21 (and_21_out, not_13_out, not_30_out);
  and and_22 (and_22_out, Value_stored[2], not_14_out);
  and and_23 (and_23_out, not_15_out, not_32_out);
  and and_24 (and_24_out, Value_stored[3], not_16_out);
  and and_25 (and_25_out, not_17_out, not_34_out);
  and and_26 (and_26_out, Value_stored[4], not_18_out);
  and and_27 (and_27_out, not_19_out, not_36_out);
  and and_28 (and_28_out, Value_stored[5], not_20_out);
  and and_29 (and_29_out, not_21_out, not_38_out);
  and and_30 (and_30_out, Value_stored[6], not_22_out);
  and and_31 (and_31_out, not_23_out, not_40_out);
  and and_32 (and_32_out, Value_stored[7], not_24_out);
  not not_25 (Value_stored[0], and_17_out);
  not not_26 (not_26_out, and_18_out);
  not not_27 (Value_stored[1], and_19_out);
  not not_28 (not_28_out, and_20_out);
  not not_29 (Value_stored[2], and_21_out);
  not not_30 (not_30_out, and_22_out);
  not not_31 (Value_stored[3], and_23_out);
  not not_32 (not_32_out, and_24_out);
  not not_33 (Value_stored[4], and_25_out);
  not not_34 (not_34_out, and_26_out);
  not not_35 (Value_stored[5], and_27_out);
  not not_36 (not_36_out, and_28_out);
  not not_37 (Value_stored[6], and_29_out);
  not not_38 (not_38_out, and_30_out);
  not not_39 (Value_stored[7], and_31_out);
  not not_40 (not_40_out, and_32_out);

  assign Value_stored[15:8] = {8{1'b0}};
endmodule

module DataRegister (
  input  [7:0] Data_in,
  input  Allow_write,
  output [7:0] Value_stored
);

  wire and_1_out, and_2_out, and_3_out, and_4_out, and_5_out, and_6_out, and_7_out, and_8_out, and_9_out,
       and_10_out, and_11_out, and_12_out, and_13_out, and_14_out, and_15_out, and_16_out, and_17_out,
       and_18_out, and_19_out, and_20_out, and_21_out, and_22_out, and_23_out, and_24_out, and_25_out,
       and_26_out, and_27_out, and_28_out, and_29_out, and_30_out, and_31_out, and_32_out, not_1_out,
       not_2_out, not_3_out, not_4_out, not_5_out, not_6_out, not_7_out, not_8_out, not_9_out, not_10_out,
       not_11_out, not_12_out, not_13_out, not_14_out, not_15_out, not_16_out, not_17_out, not_18_out,
       not_19_out, not_20_out, not_21_out, not_22_out, not_23_out, not_24_out, not_26_out, not_28_out,
       not_30_out, not_32_out, not_34_out, not_36_out, not_38_out, not_40_out;

  not not_1 (not_1_out, Data_in[0]);
  not not_2 (not_2_out, Data_in[1]);
  not not_3 (not_3_out, Data_in[2]);
  not not_4 (not_4_out, Data_in[3]);
  not not_5 (not_5_out, Data_in[4]);
  not not_6 (not_6_out, Data_in[5]);
  not not_7 (not_7_out, Data_in[6]);
  not not_8 (not_8_out, Data_in[7]);
  and and_1 (and_1_out, Data_in[0], Allow_write);
  and and_2 (and_2_out, Allow_write, not_1_out);
  and and_3 (and_3_out, Data_in[1], Allow_write);
  and and_4 (and_4_out, Allow_write, not_2_out);
  and and_5 (and_5_out, Data_in[2], Allow_write);
  and and_6 (and_6_out, Allow_write, not_3_out);
  and and_7 (and_7_out, Data_in[3], Allow_write);
  and and_8 (and_8_out, Allow_write, not_4_out);
  and and_9 (and_9_out, Data_in[4], Allow_write);
  and and_10 (and_10_out, Allow_write, not_5_out);
  and and_11 (and_11_out, Data_in[5], Allow_write);
  and and_12 (and_12_out, Allow_write, not_6_out);
  and and_13 (and_13_out, Data_in[6], Allow_write);
  and and_14 (and_14_out, Allow_write, not_7_out);
  and and_15 (and_15_out, Data_in[7], Allow_write);
  and and_16 (and_16_out, Allow_write, not_8_out);
  not not_9 (not_9_out, and_1_out);
  not not_10 (not_10_out, and_2_out);
  not not_11 (not_11_out, and_3_out);
  not not_12 (not_12_out, and_4_out);
  not not_13 (not_13_out, and_5_out);
  not not_14 (not_14_out, and_6_out);
  not not_15 (not_15_out, and_7_out);
  not not_16 (not_16_out, and_8_out);
  not not_17 (not_17_out, and_9_out);
  not not_18 (not_18_out, and_10_out);
  not not_19 (not_19_out, and_11_out);
  not not_20 (not_20_out, and_12_out);
  not not_21 (not_21_out, and_13_out);
  not not_22 (not_22_out, and_14_out);
  not not_23 (not_23_out, and_15_out);
  not not_24 (not_24_out, and_16_out);
  and and_17 (and_17_out, not_9_out, not_26_out);
  and and_18 (and_18_out, Value_stored[0], not_10_out);
  and and_19 (and_19_out, not_11_out, not_28_out);
  and and_20 (and_20_out, Value_stored[1], not_12_out);
  and and_21 (and_21_out, not_13_out, not_30_out);
  and and_22 (and_22_out, Value_stored[2], not_14_out);
  and and_23 (and_23_out, not_15_out, not_32_out);
  and and_24 (and_24_out, Value_stored[3], not_16_out);
  and and_25 (and_25_out, not_17_out, not_34_out);
  and and_26 (and_26_out, Value_stored[4], not_18_out);
  and and_27 (and_27_out, not_19_out, not_36_out);
  and and_28 (and_28_out, Value_stored[5], not_20_out);
  and and_29 (and_29_out, not_21_out, not_38_out);
  and and_30 (and_30_out, Value_stored[6], not_22_out);
  and and_31 (and_31_out, not_23_out, not_40_out);
  and and_32 (and_32_out, Value_stored[7], not_24_out);
  not not_25 (Value_stored[0], and_17_out);
  not not_26 (not_26_out, and_18_out);
  not not_27 (Value_stored[1], and_19_out);
  not not_28 (not_28_out, and_20_out);
  not not_29 (Value_stored[2], and_21_out);
  not not_30 (not_30_out, and_22_out);
  not not_31 (Value_stored[3], and_23_out);
  not not_32 (not_32_out, and_24_out);
  not not_33 (Value_stored[4], and_25_out);
  not not_34 (not_34_out, and_26_out);
  not not_35 (Value_stored[5], and_27_out);
  not not_36 (not_36_out, and_28_out);
  not not_37 (Value_stored[6], and_29_out);
  not not_38 (not_38_out, and_30_out);
  not not_39 (Value_stored[7], and_31_out);
  not not_40 (not_40_out, and_32_out);

  // Notes on the sheet:
  //   Data_in: pull=down
  //   Value_stored: pull=up
  //   Allow_write: pull=down
endmodule

module InstructionRegister (
  input  [15:0] Instruction_in,
  input  Cir,
  output [15:0] Instruction_to_CU
);

  wire and_1_out, and_2_out, and_3_out, and_4_out, and_5_out, and_6_out, and_7_out, and_8_out, and_9_out,
       and_10_out, and_11_out, and_12_out, and_13_out, and_14_out, and_15_out, and_16_out, and_17_out,
       and_18_out, and_19_out, and_20_out, and_21_out, and_22_out, and_23_out, and_24_out, and_25_out,
       and_26_out, and_27_out, and_28_out, and_29_out, and_30_out, and_31_out, and_32_out, and_33_out,
       and_34_out, and_35_out, and_36_out, and_37_out, and_38_out, and_39_out, and_40_out, and_41_out,
       and_42_out, and_43_out, and_44_out, and_45_out, and_46_out, and_47_out, and_48_out, and_49_out,
       and_50_out, and_51_out, and_52_out, and_53_out, and_54_out, and_55_out, and_56_out, and_57_out,
       and_58_out, and_59_out, and_60_out, and_61_out, and_62_out, and_63_out, and_64_out, not_1_out,
       not_2_out, not_3_out, not_4_out, not_5_out, not_6_out, not_7_out, not_8_out, not_9_out, not_10_out,
       not_11_out, not_12_out, not_13_out, not_14_out, not_15_out, not_16_out, not_17_out, not_18_out,
       not_19_out, not_20_out, not_21_out, not_22_out, not_23_out, not_24_out, not_25_out, not_26_out,
       not_27_out, not_28_out, not_29_out, not_30_out, not_31_out, not_32_out, not_33_out, not_34_out,
       not_35_out, not_36_out, not_37_out, not_38_out, not_39_out, not_40_out, not_41_out, not_42_out,
       not_43_out, not_44_out, not_45_out, not_46_out, not_47_out, not_48_out, not_50_out, not_52_out,
       not_54_out, not_56_out, not_58_out, not_60_out, not_62_out, not_64_out, not_66_out, not_68_out,
       not_70_out, not_72_out, not_74_out, not_76_out, not_78_out, not_80_out;

  not not_1 (not_1_out, Instruction_in[0]);
  not not_2 (not_2_out, Instruction_in[1]);
  not not_3 (not_3_out, Instruction_in[2]);
  not not_4 (not_4_out, Instruction_in[3]);
  not not_5 (not_5_out, Instruction_in[4]);
  not not_6 (not_6_out, Instruction_in[5]);
  not not_7 (not_7_out, Instruction_in[6]);
  not not_8 (not_8_out, Instruction_in[7]);
  not not_9 (not_9_out, Instruction_in[8]);
  not not_10 (not_10_out, Instruction_in[9]);
  not not_11 (not_11_out, Instruction_in[10]);
  not not_12 (not_12_out, Instruction_in[11]);
  not not_13 (not_13_out, Instruction_in[12]);
  not not_14 (not_14_out, Instruction_in[13]);
  not not_15 (not_15_out, Instruction_in[14]);
  not not_16 (not_16_out, Instruction_in[15]);
  and and_1 (and_1_out, Instruction_in[0], Cir);
  and and_2 (and_2_out, Cir, not_1_out);
  and and_3 (and_3_out, Instruction_in[1], Cir);
  and and_4 (and_4_out, Cir, not_2_out);
  and and_5 (and_5_out, Instruction_in[2], Cir);
  and and_6 (and_6_out, Cir, not_3_out);
  and and_7 (and_7_out, Instruction_in[3], Cir);
  and and_8 (and_8_out, Cir, not_4_out);
  and and_9 (and_9_out, Instruction_in[4], Cir);
  and and_10 (and_10_out, Cir, not_5_out);
  and and_11 (and_11_out, Instruction_in[5], Cir);
  and and_12 (and_12_out, Cir, not_6_out);
  and and_13 (and_13_out, Instruction_in[6], Cir);
  and and_14 (and_14_out, Cir, not_7_out);
  and and_15 (and_15_out, Instruction_in[7], Cir);
  and and_16 (and_16_out, Cir, not_8_out);
  and and_17 (and_17_out, Instruction_in[8], Cir);
  and and_18 (and_18_out, Cir, not_9_out);
  and and_19 (and_19_out, Instruction_in[9], Cir);
  and and_20 (and_20_out, Cir, not_10_out);
  and and_21 (and_21_out, Instruction_in[10], Cir);
  and and_22 (and_22_out, Cir, not_11_out);
  and and_23 (and_23_out, Instruction_in[11], Cir);
  and and_24 (and_24_out, Cir, not_12_out);
  and and_25 (and_25_out, Instruction_in[12], Cir);
  and and_26 (and_26_out, Cir, not_13_out);
  and and_27 (and_27_out, Instruction_in[13], Cir);
  and and_28 (and_28_out, Cir, not_14_out);
  and and_29 (and_29_out, Instruction_in[14], Cir);
  and and_30 (and_30_out, Cir, not_15_out);
  and and_31 (and_31_out, Instruction_in[15], Cir);
  and and_32 (and_32_out, Cir, not_16_out);
  not not_17 (not_17_out, and_1_out);
  not not_18 (not_18_out, and_2_out);
  not not_19 (not_19_out, and_3_out);
  not not_20 (not_20_out, and_4_out);
  not not_21 (not_21_out, and_5_out);
  not not_22 (not_22_out, and_6_out);
  not not_23 (not_23_out, and_7_out);
  not not_24 (not_24_out, and_8_out);
  not not_25 (not_25_out, and_9_out);
  not not_26 (not_26_out, and_10_out);
  not not_27 (not_27_out, and_11_out);
  not not_28 (not_28_out, and_12_out);
  not not_29 (not_29_out, and_13_out);
  not not_30 (not_30_out, and_14_out);
  not not_31 (not_31_out, and_15_out);
  not not_32 (not_32_out, and_16_out);
  not not_33 (not_33_out, and_17_out);
  not not_34 (not_34_out, and_18_out);
  not not_35 (not_35_out, and_19_out);
  not not_36 (not_36_out, and_20_out);
  not not_37 (not_37_out, and_21_out);
  not not_38 (not_38_out, and_22_out);
  not not_39 (not_39_out, and_23_out);
  not not_40 (not_40_out, and_24_out);
  not not_41 (not_41_out, and_25_out);
  not not_42 (not_42_out, and_26_out);
  not not_43 (not_43_out, and_27_out);
  not not_44 (not_44_out, and_28_out);
  not not_45 (not_45_out, and_29_out);
  not not_46 (not_46_out, and_30_out);
  not not_47 (not_47_out, and_31_out);
  not not_48 (not_48_out, and_32_out);
  and and_33 (and_33_out, not_17_out, not_50_out);
  and and_34 (and_34_out, Instruction_to_CU[0], not_18_out);
  and and_35 (and_35_out, not_19_out, not_52_out);
  and and_36 (and_36_out, Instruction_to_CU[1], not_20_out);
  and and_37 (and_37_out, not_21_out, not_54_out);
  and and_38 (and_38_out, Instruction_to_CU[2], not_22_out);
  and and_39 (and_39_out, not_23_out, not_56_out);
  and and_40 (and_40_out, Instruction_to_CU[3], not_24_out);
  and and_41 (and_41_out, not_25_out, not_58_out);
  and and_42 (and_42_out, Instruction_to_CU[4], not_26_out);
  and and_43 (and_43_out, not_27_out, not_60_out);
  and and_44 (and_44_out, Instruction_to_CU[5], not_28_out);
  and and_45 (and_45_out, not_29_out, not_62_out);
  and and_46 (and_46_out, Instruction_to_CU[6], not_30_out);
  and and_47 (and_47_out, not_31_out, not_64_out);
  and and_48 (and_48_out, Instruction_to_CU[7], not_32_out);
  and and_49 (and_49_out, not_33_out, not_66_out);
  and and_50 (and_50_out, Instruction_to_CU[8], not_34_out);
  and and_51 (and_51_out, not_35_out, not_68_out);
  and and_52 (and_52_out, Instruction_to_CU[9], not_36_out);
  and and_53 (and_53_out, not_37_out, not_70_out);
  and and_54 (and_54_out, Instruction_to_CU[10], not_38_out);
  and and_55 (and_55_out, not_39_out, not_72_out);
  and and_56 (and_56_out, Instruction_to_CU[11], not_40_out);
  and and_57 (and_57_out, not_41_out, not_74_out);
  and and_58 (and_58_out, Instruction_to_CU[12], not_42_out);
  and and_59 (and_59_out, not_43_out, not_76_out);
  and and_60 (and_60_out, Instruction_to_CU[13], not_44_out);
  and and_61 (and_61_out, not_45_out, not_78_out);
  and and_62 (and_62_out, Instruction_to_CU[14], not_46_out);
  and and_63 (and_63_out, not_47_out, not_80_out);
  and and_64 (and_64_out, Instruction_to_CU[15], not_48_out);
  not not_49 (Instruction_to_CU[0], and_33_out);
  not not_50 (not_50_out, and_34_out);
  not not_51 (Instruction_to_CU[1], and_35_out);
  not not_52 (not_52_out, and_36_out);
  not not_53 (Instruction_to_CU[2], and_37_out);
  not not_54 (not_54_out, and_38_out);
  not not_55 (Instruction_to_CU[3], and_39_out);
  not not_56 (not_56_out, and_40_out);
  not not_57 (Instruction_to_CU[4], and_41_out);
  not not_58 (not_58_out, and_42_out);
  not not_59 (Instruction_to_CU[5], and_43_out);
  not not_60 (not_60_out, and_44_out);
  not not_61 (Instruction_to_CU[6], and_45_out);
  not not_62 (not_62_out, and_46_out);
  not not_63 (Instruction_to_CU[7], and_47_out);
  not not_64 (not_64_out, and_48_out);
  not not_65 (Instruction_to_CU[8], and_49_out);
  not not_66 (not_66_out, and_50_out);
  not not_67 (Instruction_to_CU[9], and_51_out);
  not not_68 (not_68_out, and_52_out);
  not not_69 (Instruction_to_CU[10], and_53_out);
  not not_70 (not_70_out, and_54_out);
  not not_71 (Instruction_to_CU[11], and_55_out);
  not not_72 (not_72_out, and_56_out);
  not not_73 (Instruction_to_CU[12], and_57_out);
  not not_74 (not_74_out, and_58_out);
  not not_75 (Instruction_to_CU[13], and_59_out);
  not not_76 (not_76_out, and_60_out);
  not not_77 (Instruction_to_CU[14], and_61_out);
  not not_78 (not_78_out, and_62_out);
  not not_79 (Instruction_to_CU[15], and_63_out);
  not not_80 (not_80_out, and_64_out);
endmodule
