// Logisim project for syeda.circ as structural Verilog: 1 circuit, main circuit main
module main (
  input  in_1,
  input  in_2,
  input  in_3,
  input  in_4
);

  wire and_1_out, and_2_out, and_3_out, and_4_out, and_5_out, and_6_out, and_7_out, and_8_out, and_9_out,
       and_10_out, and_11_out, and_12_out, and_13_out, and_14_out, and_15_out, and_16_out, decoder_1_out0,
       decoder_1_out1, decoder_1_out2, decoder_1_out3, decoder_2_out0, decoder_2_out1, decoder_2_out2,
       decoder_2_out3;

  // Probe on {in_4, in_3}
  // Probe on {in_1, in_2}
  Decoder #(.select(2)) decoder_1 (
    .out0(decoder_1_out0), .out1(decoder_1_out1), .out2(decoder_1_out2), .out3(decoder_1_out3),
    .sel({in_4, in_3}));  // open: en
  Decoder #(.select(2)) decoder_2 (
    .out0(decoder_2_out0), .out1(decoder_2_out1), .out2(decoder_2_out2), .out3(decoder_2_out3),
    .sel({in_1, in_2}));  // open: en
  and and_1 (and_1_out, decoder_2_out3, decoder_1_out0);
  LED led_1 (.in(and_1_out));
  LED led_2 (.in(and_2_out));
  and and_2 (and_2_out, decoder_2_out3, decoder_1_out1);
  and and_3 (and_3_out, decoder_2_out3, decoder_1_out2);
  LED led_3 (.in(and_3_out));
  LED led_4 (.in(and_4_out));
  and and_4 (and_4_out, decoder_2_out3, decoder_1_out3);
  LED led_5 (.in(and_5_out));
  and and_5 (and_5_out, decoder_2_out1, decoder_1_out0);
  LED led_6 (.in(and_6_out));
  and and_6 (and_6_out, decoder_2_out2, decoder_1_out0);
  LED led_7 (.in(and_8_out));
  and and_7 (and_7_out, decoder_2_out2, decoder_1_out1);
  and and_8 (and_8_out, decoder_2_out1, decoder_1_out1);
  LED led_8 (.in(and_7_out));
  LED led_9 (.in(and_9_out));
  and and_9 (and_9_out, decoder_2_out1, decoder_1_out2);
  and and_10 (and_10_out, decoder_2_out2, decoder_1_out2);
  LED led_10 (.in(and_10_out));
  and and_11 (and_11_out, decoder_2_out1, decoder_1_out3);
  LED led_11 (.in(and_12_out));
  LED led_12 (.in(and_11_out));
  and and_12 (and_12_out, decoder_2_out2, decoder_1_out3);
  and and_13 (and_13_out, decoder_2_out0, decoder_1_out0);
  LED led_13 (.in(and_13_out));
  and and_14 (and_14_out, decoder_2_out0, decoder_1_out1);
  LED led_14 (.in(and_14_out));
  and and_15 (and_15_out, decoder_2_out0, decoder_1_out2);
  LED led_15 (.in(and_15_out));
  and and_16 (and_16_out, decoder_2_out0, decoder_1_out3);
  LED led_16 (.in(and_16_out));
endmodule
