// Logisim project test but cooler.circ as structural Verilog
module test (
  input  b1,
  input  b2,
  input  cin,
  input  a1,
  input  b1_2,
  input  a2,
  input  b2_2,
  input  b1_3,
  input  a3,
  input  b3,
  input  b2_3,
  input  a4,
  input  b4,
  input  cin_2,
  input  a5,
  input  b5,
  input  a6,
  input  b6,
  input  a7,
  input  b7,
  input  a8,
  input  b8,
  input  [7:0] in_23,
  input  in_24,
  input  right___left,
  input  logical___arith,
  input  rotate___no,
  input  [7:0] in_28,
  output sum,
  output carry,
  output c1,
  output c2,
  output s,
  output c3,
  output cout,
  output c4,
  output c5,
  output c6,
  output c7,
  output c8,
  output ccout,
  output lostExists,
  output lost,
  output [7:0] out_44
);

  wire AND_3_out, AND_out, full_adder_d1_w1_1_cout, full_adder_d1_w1_2_cout, full_adder_d1_w1_3_cout,
       full_adder_d1_w1_4_cout, full_adder_d1_w1_5_cout, full_adder_d1_w1_6_cout, full_adder_d1_w1_7_cout,
       full_adder_d8_w1_1_cout, XOR_out;
  wire [7:0] full_adder_d8_w1_1_bytec, logicxshift_d8_w8_1_b;

  // Probe on in_23
  // Probe on logicxshift_d8_w8_1_b
  // Probe on logicxshift_d8_w8_1_b
  xor XOR (XOR_out, b1_3, b2_3);
  and AND (AND_out, b2_3, b1_3);
  // Probe on full_adder_d8_w1_1_bytec
  full_adder_d8_w1 full_adder_d8_w1_1 (
    .byteA(8'h1a), .byteB(8'h20), .cin(1'b0), .byteC(full_adder_d8_w1_1_bytec), .cout(full_adder_d8_w1_1_cout));
  // Probe on full_adder_d8_w1_1_cout
  xor XOR_2 (sum, b2, b1);
  and AND_2 (carry, b1, b2);
  and AND_3 (AND_3_out, XOR_out, cin_2);
  logicXshift_d8_w8 logicxshift_d8_w8_1 (.right(in_24), .a(in_23), .b(logicxshift_d8_w8_1_b));  // open: lost
  xor XOR_3 (s, XOR_out, cin_2);
  or OR (cout, AND_3_out, AND_out);
  full_adder_d1_w1 full_adder_d1_w1_1 (.b1(a1), .b2(b1_2), .cin(cin), .s(c1), .cout(full_adder_d1_w1_1_cout));
  full_adder_d1_w1 full_adder_d1_w1_2 (
    .b1(a2), .b2(b2_2), .cin(full_adder_d1_w1_1_cout), .s(c2), .cout(full_adder_d1_w1_2_cout));
  full_adder_d1_w1 full_adder_d1_w1_3 (
    .b1(a3), .b2(b3), .cin(full_adder_d1_w1_2_cout), .s(c3), .cout(full_adder_d1_w1_3_cout));
  full_adder_d1_w1 full_adder_d1_w1_4 (
    .b1(a4), .b2(b4), .cin(full_adder_d1_w1_3_cout), .s(c4), .cout(full_adder_d1_w1_4_cout));
  full_adder_d1_w1 full_adder_d1_w1_5 (
    .b1(a5), .b2(b5), .cin(full_adder_d1_w1_4_cout), .s(c5), .cout(full_adder_d1_w1_5_cout));
  full_adder_d1_w1 full_adder_d1_w1_6 (
    .b1(a6), .b2(b6), .cin(full_adder_d1_w1_5_cout), .s(c6), .cout(full_adder_d1_w1_6_cout));
  full_adder_d1_w1 full_adder_d1_w1_7 (
    .b1(a7), .b2(b7), .cin(full_adder_d1_w1_6_cout), .s(c7), .cout(full_adder_d1_w1_7_cout));
  full_adder_d1_w1 full_adder_d1_w1_8 (.b1(a8), .b2(b8), .cin(full_adder_d1_w1_7_cout), .s(c8), .cout(ccout));
  XXshift_d8_w8 xxshift_d8_w8_1 (
    .right___left(right___left), .logical___arith(logical___arith), .rotate___no(rotate___no), .byteA(in_28),
    .lost(lost), .byteB(out_44), .lostExists(lostExists));

  // Notes on the sheet:
  //   half adder
  //   full adder
  //   a bunch of full adders stapled together equals...
  //   a byte adder :O
endmodule

module cmos_NAND (
  input  x,
  input  y,
  output x_NAND_y
);

  wire transistor_3_out;

  Transistor transistor_1 (.in(1'b1), .out(x_NAND_y), .gate(x));
  Transistor #(.\type ("n")) transistor_2 (.in(transistor_3_out), .out(x_NAND_y), .gate(x));
  Transistor #(.\type ("n")) transistor_3 (.in(1'b0), .out(transistor_3_out), .gate(y));
  Transistor transistor_4 (.in(1'b1), .out(x_NAND_y), .gate(y));
endmodule

module cmos_NOR (
  input  x,
  input  y,
  output x_NOR_y
);

  wire transistor_2_out;

  Transistor #(.\type ("n")) transistor_1 (.in(1'b0), .out(x_NOR_y), .gate(x));
  Transistor transistor_2 (.in(1'b1), .out(transistor_2_out), .gate(x));
  Transistor transistor_3 (.in(transistor_2_out), .out(x_NOR_y), .gate(y));
  Transistor #(.\type ("n")) transistor_4 (.in(1'b0), .out(x_NOR_y), .gate(y));
endmodule

module cmos_digital_repeater (
  input  x,
  output NOT_NOT_x
);

  wire transistor_1_out;

  Transistor transistor_1 (.in(1'b1), .out(transistor_1_out), .gate(x));
  Transistor #(.\type ("n")) transistor_2 (.in(1'b0), .out(transistor_1_out), .gate(x));
  Transistor transistor_3 (.in(1'b1), .out(NOT_NOT_x), .gate(transistor_1_out));
  Transistor #(.\type ("n")) transistor_4 (.in(1'b0), .out(NOT_NOT_x), .gate(transistor_1_out));
endmodule

module half_adder_d1_w1 (
  input  b1,
  input  b2,
  output sum,
  output carry
);

  xor XOR (sum, b2, b1);
  and AND (carry, b1, b2);
endmodule

// +
module full_adder_d1_w1 (
  input  b1,
  input  b2,
  input  cin,
  output s,
  output cout
);

  wire AND_2_out, AND_out, XOR_out;

  xor XOR (XOR_out, b1, b2);
  and AND (AND_out, XOR_out, cin);
  and AND_2 (AND_2_out, b2, b1);
  xor XOR_2 (s, XOR_out, cin);
  or OR (cout, AND_out, AND_2_out);
endmodule

module full_adder_d8_w8 (
  input  cin,
  input  a0,
  input  b0,
  input  a1,
  input  b1,
  input  a2,
  input  b2,
  input  a3,
  input  b3,
  input  a4,
  input  b4,
  input  a5,
  input  b5,
  input  a6,
  input  b6,
  input  a7,
  input  b7,
  output c1,
  output c2,
  output c3,
  output c4,
  output c5,
  output c6,
  output c7,
  output c8,
  output ccout
);

  wire full_adder_d1_w1_1_cout, full_adder_d1_w1_2_cout, full_adder_d1_w1_3_cout, full_adder_d1_w1_4_cout,
       full_adder_d1_w1_5_cout, full_adder_d1_w1_6_cout, full_adder_d1_w1_7_cout;

  full_adder_d1_w1 full_adder_d1_w1_1 (.b1(a0), .b2(b0), .cin(cin), .s(c1), .cout(full_adder_d1_w1_1_cout));
  full_adder_d1_w1 full_adder_d1_w1_2 (
    .b1(a1), .b2(b1), .cin(full_adder_d1_w1_1_cout), .s(c2), .cout(full_adder_d1_w1_2_cout));
  full_adder_d1_w1 full_adder_d1_w1_3 (
    .b1(a2), .b2(b2), .cin(full_adder_d1_w1_2_cout), .s(c3), .cout(full_adder_d1_w1_3_cout));
  full_adder_d1_w1 full_adder_d1_w1_4 (
    .b1(a3), .b2(b3), .cin(full_adder_d1_w1_3_cout), .s(c4), .cout(full_adder_d1_w1_4_cout));
  full_adder_d1_w1 full_adder_d1_w1_5 (
    .b1(a4), .b2(b4), .cin(full_adder_d1_w1_4_cout), .s(c5), .cout(full_adder_d1_w1_5_cout));
  full_adder_d1_w1 full_adder_d1_w1_6 (
    .b1(a5), .b2(b5), .cin(full_adder_d1_w1_5_cout), .s(c6), .cout(full_adder_d1_w1_6_cout));
  full_adder_d1_w1 full_adder_d1_w1_7 (
    .b1(a6), .b2(b6), .cin(full_adder_d1_w1_6_cout), .s(c7), .cout(full_adder_d1_w1_7_cout));
  full_adder_d1_w1 full_adder_d1_w1_8 (.b1(a7), .b2(b7), .cin(full_adder_d1_w1_7_cout), .s(c8), .cout(ccout));
endmodule

// a+b=c
module full_adder_d8_w1 (
  input  [7:0] byteA,
  input  [7:0] byteB,
  input  cin,
  output [7:0] byteC,
  output cout
);

  full_adder_d8_w8 full_adder_d8_w8_1 (
    .cin(cin), .a0(byteA[0]), .b0(byteB[0]), .a1(byteA[1]), .b1(byteB[1]), .a2(byteA[2]), .b2(byteB[2]),
    .a3(byteA[3]), .b3(byteB[3]), .a4(byteA[4]), .b4(byteB[4]), .a5(byteA[5]), .b5(byteB[5]), .a6(byteA[6]),
    .b6(byteB[6]), .a7(byteA[7]), .b7(byteB[7]), .c1(byteC[0]), .c2(byteC[1]), .c3(byteC[2]), .c4(byteC[3]),
    .c5(byteC[4]), .c6(byteC[5]), .c7(byteC[6]), .c8(byteC[7]), .ccout(cout));

  // Notes on the sheet:
  //   byteC: pull=down
  //   byteB: pull=down
  //   byteA: pull=down
endmodule

// 16+16
module full_adder_d16_w1 (
  input  [15:0] _2byteA,
  input  [15:0] _2byteB,
  input  cin,
  output [15:0] a_b,
  output cout
);

  wire full_adder_d8_w1_1_cout;

  // Probe on _2byteA
  // Probe on _2byteB
  full_adder_d8_w1 full_adder_d8_w1_1 (
    .byteA(_2byteA[7:0]), .byteB(_2byteB[7:0]), .cin(cin), .byteC(a_b[7:0]), .cout(full_adder_d8_w1_1_cout));
  full_adder_d8_w1 full_adder_d8_w1_2 (
    .byteA(_2byteB[15:8]), .byteB(_2byteA[15:8]), .cin(full_adder_d8_w1_1_cout), .byteC(a_b[15:8]),
    .cout(cout));
  // Probe on a_b

  // Notes on the sheet:
  //   _2byteB: pull=down
  //   a_b: pull=down
  //   _2byteA: pull=down
endmodule

// >> / <<
module logicXshift_d8_w1 (
  input  right,
  input  a1,
  input  a2,
  input  a3,
  input  a4,
  input  a5,
  input  a6,
  input  a7,
  input  a8,
  output b1,
  output b2,
  output b3,
  output b4,
  output b5,
  output b6,
  output b7,
  output b8,
  output lost
);

  wire AND_2_out, AND_3_out, AND_4_out, AND_5_out, AND_6_out, AND_7_out, AND_8_out, AND_9_out, AND_10_out,
       AND_11_out, AND_12_out, AND_13_out, AND_14_out, AND_15_out, AND_16_out, AND_out, not_1_out;

  not not_1 (not_1_out, right);
  and AND (AND_out, not_1_out, a1);
  and AND_2 (AND_2_out, not_1_out, a2);
  and AND_3 (AND_3_out, not_1_out, a3);
  and AND_4 (AND_4_out, not_1_out, a4);
  and AND_5 (AND_5_out, not_1_out, a5);
  and AND_6 (AND_6_out, not_1_out, a6);
  and AND_7 (AND_7_out, not_1_out, a7);
  and AND_8 (AND_8_out, not_1_out, a8);
  and AND_9 (AND_9_out, right, a1);
  and AND_10 (AND_10_out, right, a2);
  and AND_11 (AND_11_out, right, a3);
  and AND_12 (AND_12_out, right, a4);
  and AND_13 (AND_13_out, right, a5);
  and AND_14 (AND_14_out, right, a6);
  and AND_15 (AND_15_out, right, a7);
  and AND_16 (AND_16_out, right, a8);
  or OR (lost, AND_out, AND_16_out);
  or OR_2 (b1, 1'b0, AND_2_out);
  or OR_3 (b2, AND_9_out, AND_3_out);
  or OR_4 (b3, AND_10_out, AND_4_out);
  or OR_5 (b4, AND_11_out, AND_5_out);
  or OR_6 (b5, AND_12_out, AND_6_out);
  or OR_7 (b6, AND_13_out, AND_7_out);
  or OR_8 (b7, AND_14_out, AND_8_out);
  or OR_9 (b8, AND_15_out, 1'b0);
endmodule

// > / <
module logicXshift_d8_w8 (
  input  right,
  input  [7:0] a,
  output [7:0] b,
  output lost
);

  logicXshift_d8_w1 logicxshift_d8_w1_1 (
    .right(right), .a1(a[0]), .a2(a[1]), .a3(a[2]), .a4(a[3]), .a5(a[4]), .a6(a[5]), .a7(a[6]), .a8(a[7]),
    .b1(b[0]), .b2(b[1]), .b3(b[2]), .b4(b[3]), .b5(b[4]), .b6(b[5]), .b7(b[6]), .b8(b[7]), .lost(lost));
endmodule

module XXshift_d8_w1 (
  input  right___left,
  input  logical___arith,
  input  rotate___no,
  input  a1,
  input  a2,
  input  a3,
  input  a4,
  input  a5,
  input  a6,
  input  a7,
  input  a8,
  output lost,
  output lostExists,
  output b1,
  output b2,
  output b3,
  output b4,
  output b5,
  output b6,
  output b7,
  output b8
);

  wire AND_2_out, AND_3_out, AND_4_out, AND_5_out, AND_6_out, AND_7_out, AND_8_out, AND_9_out, AND_10_out,
       AND_11_out, AND_12_out, AND_13_out, AND_14_out, AND_15_out, AND_17_out, AND_18_out, AND_19_out,
       lcarry, log___arith, not_2_out, OR_10_out, OR_out, rcarry;

  not not_1 (log___arith, logical___arith);
  and AND (lcarry, right___left, a1);
  and AND_2 (AND_2_out, right___left, a2);
  and AND_3 (AND_3_out, right___left, a3);
  and AND_4 (AND_4_out, right___left, a4);
  and AND_5 (AND_5_out, right___left, a5);
  and AND_6 (AND_6_out, right___left, a6);
  and AND_7 (AND_7_out, right___left, a7);
  and AND_8 (AND_8_out, right___left, a8);
  not not_2 (not_2_out, right___left);
  and AND_9 (AND_9_out, not_2_out, a1);
  and AND_10 (AND_10_out, not_2_out, a2);
  and AND_11 (AND_11_out, not_2_out, a3);
  and AND_12 (AND_12_out, not_2_out, a4);
  and AND_13 (AND_13_out, not_2_out, a5);
  and AND_14 (AND_14_out, not_2_out, a6);
  and AND_15 (AND_15_out, not_2_out, a7);
  and AND_16 (rcarry, not_2_out, a8);
  and AND_17 (AND_17_out, a8, right___left, log___arith, ~rotate___no);  // AND_Gate
  or OR (OR_out, 1'b0, AND_17_out);
  and AND_18 (AND_18_out, rotate___no, lcarry);
  and AND_19 (AND_19_out, rotate___no, rcarry);
  or OR_2 (b1, 1'b0, AND_19_out, AND_2_out);
  or OR_3 (b2, AND_9_out, AND_3_out);
  or OR_4 (b3, AND_10_out, AND_4_out);
  or OR_5 (b4, AND_11_out, AND_5_out);
  or OR_6 (b5, AND_12_out, AND_6_out);
  or OR_7 (b6, AND_13_out, AND_7_out);
  or OR_8 (b7, AND_14_out, AND_8_out);
  or OR_9 (b8, AND_15_out, AND_18_out, OR_out);
  or OR_10 (OR_10_out, lcarry, rcarry);
  not not_3 (lostExists, rotate___no);
  and AND_20 (lost, OR_10_out, lostExists);

  // Other names for the same wires on the sheet: rot___no = rotate___no
endmodule

// _> / <
module XXshift_d8_w8 (
  input  right___left,
  input  logical___arith,
  input  rotate___no,
  input  [7:0] byteA,
  output lostExists,
  output lost,
  output [7:0] byteB
);

  XXshift_d8_w1 xxshift_d8_w1_1 (
    .right___left(right___left), .logical___arith(logical___arith), .rotate___no(rotate___no), .a1(byteA[0]),
    .a2(byteA[1]), .a3(byteA[2]), .a4(byteA[3]), .a5(byteA[4]), .a6(byteA[5]), .a7(byteA[6]), .a8(byteA[7]),
    .lost(lost), .b1(byteB[0]), .b2(byteB[1]), .b3(byteB[2]), .b4(byteB[3]), .b5(byteB[4]), .b6(byteB[5]),
    .b7(byteB[6]), .b8(byteB[7]), .lostExists(lostExists));
endmodule

// Sl
module Slatchgated_reset_d1_w1 (
  input  reset,
  input  write_Enable,
  input  data_in,
  output Q
);

  wire AND_2_out, AND_out, not_1_out, not_3_out, OR_2_out, OR_out;

  not not_1 (not_1_out, data_in);
  and AND (AND_out, not_1_out, write_Enable);
  and AND_2 (AND_2_out, write_Enable, data_in);
  or OR (OR_out, reset, AND_out, not_3_out);
  not not_2 (Q, OR_out);
  not not_3 (not_3_out, OR_2_out);
  or OR_2 (OR_2_out, Q, AND_2_out);
  // Probe on Q

  // Notes on the sheet:
  //   Q: pull=down
  //   reset: pull=down
endmodule

module SRlatchgated_d1_w1 (
  input  Reset,
  input  write_Enable,
  input  Set,
  output Q,
  output nQ
);

  wire AND_2_out, AND_out, OR_2_out, OR_out;

  and AND (AND_out, Reset, write_Enable);
  and AND_2 (AND_2_out, write_Enable, Set);
  or OR (OR_out, AND_out, nQ);
  or OR_2 (OR_2_out, Q, AND_2_out);
  not not_1 (Q, OR_out);
  not not_2 (nQ, OR_2_out);
endmodule

module SRlatch_d1_w1 (
  input  Reset,
  input  Set,
  output Q,
  output nQ
);

  wire OR_2_out, OR_out;

  or OR (OR_out, Reset, nQ);
  or OR_2 (OR_2_out, Q, Set);
  not not_1 (Q, OR_out);
  not not_2 (nQ, OR_2_out);
endmodule

module JKlatch_clock (
  input  J___set,
  input  clock,
  input  K___reset,
  output Q,
  output nQ
);

  wire nand_1_out, nand_2_out;

  nand nand_1 (nand_1_out, nQ, J___set, clock);
  nand nand_2 (nand_2_out, clock, K___reset, Q);
  nand nand_3 (Q, nand_1_out, nQ);
  nand nand_4 (nQ, Q, nand_2_out);
endmodule

module _1byte_gatedSR_memory_d8_w1 (
  input  [7:0] data_in,
  input  write_enable,
  output [7:0] data_out
);

  // Probe on data_in
  // Probe on data_out
  // Probe on data_out
  Slatchgated_reset_d1_w1 slatchgated_reset_d1_w1_1 (
    .write_Enable(write_enable), .data_in(data_in[0]), .reset(1'b0), .Q(data_out[0]));
  Slatchgated_reset_d1_w1 slatchgated_reset_d1_w1_2 (
    .write_Enable(write_enable), .data_in(data_in[1]), .reset(1'b0), .Q(data_out[1]));
  Slatchgated_reset_d1_w1 slatchgated_reset_d1_w1_3 (
    .write_Enable(write_enable), .data_in(data_in[2]), .reset(1'b0), .Q(data_out[2]));
  Slatchgated_reset_d1_w1 slatchgated_reset_d1_w1_4 (
    .write_Enable(write_enable), .data_in(data_in[3]), .reset(1'b0), .Q(data_out[3]));
  Slatchgated_reset_d1_w1 slatchgated_reset_d1_w1_5 (
    .write_Enable(write_enable), .data_in(data_in[4]), .reset(1'b0), .Q(data_out[4]));
  Slatchgated_reset_d1_w1 slatchgated_reset_d1_w1_6 (
    .write_Enable(write_enable), .data_in(data_in[5]), .reset(1'b0), .Q(data_out[5]));
  Slatchgated_reset_d1_w1 slatchgated_reset_d1_w1_7 (
    .write_Enable(write_enable), .data_in(data_in[6]), .reset(1'b0), .Q(data_out[6]));
  Slatchgated_reset_d1_w1 slatchgated_reset_d1_w1_8 (
    .write_Enable(write_enable), .data_in(data_in[7]), .reset(1'b0), .Q(data_out[7]));
  // Probe on data_out

  // Notes on the sheet:
  //   data_in: pull=down
endmodule

module _1byte_gatedSR_memory_d8_w1_OLD (
  input  [7:0] data_in,
  input  RESET,
  input  write_enable,
  output [7:0] data_out
);

  wire or_1_out;
  wire [7:0] transistor_1_out;

  Transistor #(.\type ("n"), .gate("br"), .width(8)) transistor_1 (
    .in(data_in), .out(transistor_1_out), .gate(write_enable));
  Pull_Resistor pull_resistor_1 (.node(transistor_1_out));
  or or_1 (or_1_out, RESET, write_enable);
  // Probe on data_out
  Slatchgated_reset_d1_w1 slatchgated_reset_d1_w1_1 (
    .write_Enable(or_1_out), .data_in(transistor_1_out[0]), .Q(data_out[0]));  // open: reset
  Slatchgated_reset_d1_w1 slatchgated_reset_d1_w1_2 (
    .write_Enable(or_1_out), .data_in(transistor_1_out[1]), .Q(data_out[1]));  // open: reset
  Slatchgated_reset_d1_w1 slatchgated_reset_d1_w1_3 (
    .write_Enable(or_1_out), .data_in(transistor_1_out[2]), .Q(data_out[2]));  // open: reset
  Slatchgated_reset_d1_w1 slatchgated_reset_d1_w1_4 (
    .write_Enable(or_1_out), .data_in(transistor_1_out[3]), .Q(data_out[3]));  // open: reset
  Slatchgated_reset_d1_w1 slatchgated_reset_d1_w1_5 (
    .write_Enable(or_1_out), .data_in(transistor_1_out[4]), .Q(data_out[4]));  // open: reset
  Slatchgated_reset_d1_w1 slatchgated_reset_d1_w1_6 (
    .write_Enable(or_1_out), .data_in(transistor_1_out[5]), .Q(data_out[5]));  // open: reset
  Slatchgated_reset_d1_w1 slatchgated_reset_d1_w1_7 (
    .write_Enable(or_1_out), .data_in(transistor_1_out[6]), .Q(data_out[6]));  // open: reset
  Slatchgated_reset_d1_w1 slatchgated_reset_d1_w1_8 (
    .write_Enable(or_1_out), .data_in(transistor_1_out[7]), .Q(data_out[7]));  // open: reset
endmodule

module _1byte_gatedSR_memory_d8_w1_NEW_LESS_LAG (
  input  [7:0] data_in,
  input  RESET,
  input  write_enable,
  output [7:0] data_out
);

  wire or_1_out;
  wire [7:0] transistor_1_out;

  _1byte_gatedSR_memory_d8_w1_OLD u_1byte_gatedsr_memory_d8_w1_old_1 ();  // open: data_in, RESET, write_enable, data_out
  Transistor #(.\type ("n"), .gate("br"), .width(8)) transistor_1 (
    .in(data_in), .out(transistor_1_out), .gate(write_enable));
  Transistor #(.gate("br"), .width(8)) transistor_2 (.in({8{1'b0}}), .out(transistor_1_out), .gate(write_enable));
  or or_1 (or_1_out, RESET, write_enable);
  // Probe on data_out
  Slatchgated_reset_d1_w1 slatchgated_reset_d1_w1_1 (
    .write_Enable(or_1_out), .data_in(transistor_1_out[0]), .Q(data_out[0]));  // open: reset
  Slatchgated_reset_d1_w1 slatchgated_reset_d1_w1_2 (
    .write_Enable(or_1_out), .data_in(transistor_1_out[1]), .Q(data_out[1]));  // open: reset
  Slatchgated_reset_d1_w1 slatchgated_reset_d1_w1_3 (
    .write_Enable(or_1_out), .data_in(transistor_1_out[2]), .Q(data_out[2]));  // open: reset
  Slatchgated_reset_d1_w1 slatchgated_reset_d1_w1_4 (
    .write_Enable(or_1_out), .data_in(transistor_1_out[3]), .Q(data_out[3]));  // open: reset
  Slatchgated_reset_d1_w1 slatchgated_reset_d1_w1_5 (
    .write_Enable(or_1_out), .data_in(transistor_1_out[4]), .Q(data_out[4]));  // open: reset
  Slatchgated_reset_d1_w1 slatchgated_reset_d1_w1_6 (
    .write_Enable(or_1_out), .data_in(transistor_1_out[5]), .Q(data_out[5]));  // open: reset
  Slatchgated_reset_d1_w1 slatchgated_reset_d1_w1_7 (
    .write_Enable(or_1_out), .data_in(transistor_1_out[6]), .Q(data_out[6]));  // open: reset
  Slatchgated_reset_d1_w1 slatchgated_reset_d1_w1_8 (
    .write_Enable(or_1_out), .data_in(transistor_1_out[7]), .Q(data_out[7]));  // open: reset
endmodule

module _2byte_gatedSR_memory_d16_w1 (
  input  reset,
  input  [15:0] data_in,
  input  write_enable,
  output [15:0] data_out
);

  Slatchgated_reset_d1_w1 slatchgated_reset_d1_w1_1 (
    .write_Enable(write_enable), .data_in(data_in[0]), .reset(reset), .Q(data_out[0]));
  Slatchgated_reset_d1_w1 slatchgated_reset_d1_w1_2 (
    .write_Enable(write_enable), .data_in(data_in[1]), .reset(reset), .Q(data_out[1]));
  Slatchgated_reset_d1_w1 slatchgated_reset_d1_w1_3 (
    .write_Enable(write_enable), .data_in(data_in[2]), .reset(reset), .Q(data_out[2]));
  Slatchgated_reset_d1_w1 slatchgated_reset_d1_w1_4 (
    .write_Enable(write_enable), .data_in(data_in[3]), .reset(reset), .Q(data_out[3]));
  Slatchgated_reset_d1_w1 slatchgated_reset_d1_w1_5 (
    .write_Enable(write_enable), .data_in(data_in[4]), .reset(reset), .Q(data_out[4]));
  Slatchgated_reset_d1_w1 slatchgated_reset_d1_w1_6 (
    .write_Enable(write_enable), .data_in(data_in[5]), .reset(reset), .Q(data_out[5]));
  Slatchgated_reset_d1_w1 slatchgated_reset_d1_w1_7 (
    .write_Enable(write_enable), .data_in(data_in[6]), .reset(reset), .Q(data_out[6]));
  Slatchgated_reset_d1_w1 slatchgated_reset_d1_w1_8 (
    .write_Enable(write_enable), .data_in(data_in[7]), .reset(reset), .Q(data_out[7]));
  Slatchgated_reset_d1_w1 slatchgated_reset_d1_w1_9 (
    .write_Enable(write_enable), .data_in(data_in[8]), .reset(reset), .Q(data_out[8]));
  Slatchgated_reset_d1_w1 slatchgated_reset_d1_w1_10 (
    .write_Enable(write_enable), .data_in(data_in[9]), .reset(reset), .Q(data_out[9]));
  Slatchgated_reset_d1_w1 slatchgated_reset_d1_w1_11 (
    .write_Enable(write_enable), .data_in(data_in[10]), .reset(reset), .Q(data_out[10]));
  Slatchgated_reset_d1_w1 slatchgated_reset_d1_w1_12 (
    .write_Enable(write_enable), .data_in(data_in[11]), .reset(reset), .Q(data_out[11]));
  Slatchgated_reset_d1_w1 slatchgated_reset_d1_w1_13 (
    .write_Enable(write_enable), .data_in(data_in[12]), .reset(reset), .Q(data_out[12]));
  Slatchgated_reset_d1_w1 slatchgated_reset_d1_w1_14 (
    .write_Enable(write_enable), .data_in(data_in[13]), .reset(reset), .Q(data_out[13]));
  Slatchgated_reset_d1_w1 slatchgated_reset_d1_w1_15 (
    .write_Enable(write_enable), .data_in(data_in[14]), .reset(reset), .Q(data_out[14]));
  Slatchgated_reset_d1_w1 slatchgated_reset_d1_w1_16 (
    .write_Enable(write_enable), .data_in(data_in[15]), .reset(reset), .Q(data_out[15]));

  // Notes on the sheet:
  //   data_out: pull=down
  //   data_in: pull=down
endmodule

module _4x1byte_memory_unit_2bitAddr (
  input  [1:0] select,
  input  [7:0] data_in,
  input  write_enable,
  input  RESET,
  output [7:0] data_out
);

  wire AND_2_out, AND_3_out, AND_4_out, AND_out, n2_4_decoder_1__0, n2_4_decoder_1__1, n2_4_decoder_1__2,
       n2_4_decoder_1__3;
  wire [7:0] n1byte_gatedsr_memory_d8_w1_new_less_lag_1_data_out,
       n1byte_gatedsr_memory_d8_w1_new_less_lag_2_data_out,
       n1byte_gatedsr_memory_d8_w1_new_less_lag_3_data_out,
       n1byte_gatedsr_memory_d8_w1_new_less_lag_4_data_out, transistor_1_out;

  Pull_Resistor pull_resistor_1 (.node(select));
  _2_4_decoder u_2_4_decoder_1 (
    .s0(select[0]), .s1(select[1]), ._0(n2_4_decoder_1__0), ._1(n2_4_decoder_1__1), ._2(n2_4_decoder_1__2),
    ._3(n2_4_decoder_1__3));
  Transistor #(.\type ("n"), .gate("br"), .width(8)) transistor_1 (
    .in(data_in), .out(transistor_1_out), .gate(write_enable));
  Pull_Resistor pull_resistor_2 (.node(write_enable));
  and AND (AND_out, write_enable, n2_4_decoder_1__0);
  and AND_2 (AND_2_out, write_enable, n2_4_decoder_1__1);
  and AND_3 (AND_3_out, write_enable, n2_4_decoder_1__2);
  and AND_4 (AND_4_out, write_enable, n2_4_decoder_1__3);
  _1byte_gatedSR_memory_d8_w1_NEW_LESS_LAG u_1byte_gatedsr_memory_d8_w1_new_less_lag_1 (
    .data_in(transistor_1_out), .RESET(RESET), .write_enable(AND_out),
    .data_out(n1byte_gatedsr_memory_d8_w1_new_less_lag_1_data_out));
  _1byte_gatedSR_memory_d8_w1_NEW_LESS_LAG u_1byte_gatedsr_memory_d8_w1_new_less_lag_2 (
    .data_in(transistor_1_out), .RESET(RESET), .write_enable(AND_2_out),
    .data_out(n1byte_gatedsr_memory_d8_w1_new_less_lag_2_data_out));
  _1byte_gatedSR_memory_d8_w1_NEW_LESS_LAG u_1byte_gatedsr_memory_d8_w1_new_less_lag_3 (
    .data_in(transistor_1_out), .RESET(RESET), .write_enable(AND_3_out),
    .data_out(n1byte_gatedsr_memory_d8_w1_new_less_lag_3_data_out));
  _1byte_gatedSR_memory_d8_w1_NEW_LESS_LAG u_1byte_gatedsr_memory_d8_w1_new_less_lag_4 (
    .data_in(transistor_1_out), .RESET(RESET), .write_enable(AND_4_out),
    .data_out(n1byte_gatedsr_memory_d8_w1_new_less_lag_4_data_out));
  // Probe on n1byte_gatedsr_memory_d8_w1_new_less_lag_1_data_out
  // Probe on n1byte_gatedsr_memory_d8_w1_new_less_lag_2_data_out
  // Probe on n1byte_gatedsr_memory_d8_w1_new_less_lag_3_data_out
  // Probe on n1byte_gatedsr_memory_d8_w1_new_less_lag_4_data_out
  Transistor #(.\type ("n"), .width(8)) transistor_2 (
    .in(n1byte_gatedsr_memory_d8_w1_new_less_lag_1_data_out), .out(data_out), .gate(n2_4_decoder_1__0));
  Transistor #(.\type ("n"), .width(8)) transistor_3 (
    .in(n1byte_gatedsr_memory_d8_w1_new_less_lag_2_data_out), .out(data_out), .gate(n2_4_decoder_1__1));
  Transistor #(.\type ("n"), .width(8)) transistor_4 (
    .in(n1byte_gatedsr_memory_d8_w1_new_less_lag_3_data_out), .out(data_out), .gate(n2_4_decoder_1__2));
  Transistor #(.\type ("n"), .width(8)) transistor_5 (
    .in(n1byte_gatedsr_memory_d8_w1_new_less_lag_4_data_out), .out(data_out), .gate(n2_4_decoder_1__3));
endmodule

module _8x1byte_memory_unit_3bitAddr (
  input  [2:0] select,
  input  [7:0] data_in,
  input  write_enable,
  input  RESET,
  output [7:0] data_out
);

  wire AND_2_out, AND_3_out, AND_4_out, AND_5_out, AND_6_out, AND_7_out, AND_8_out, AND_out,
       n3_8_decoder_1__0, n3_8_decoder_1__1, n3_8_decoder_1__2, n3_8_decoder_1__3, n3_8_decoder_1__4,
       n3_8_decoder_1__5, n3_8_decoder_1__6, n3_8_decoder_1__7;
  wire [7:0] n1byte_gatedsr_memory_d8_w1_1_p4, n1byte_gatedsr_memory_d8_w1_2_p4,
       n1byte_gatedsr_memory_d8_w1_3_p4, n1byte_gatedsr_memory_d8_w1_4_p4, n1byte_gatedsr_memory_d8_w1_5_p4,
       n1byte_gatedsr_memory_d8_w1_6_p4, n1byte_gatedsr_memory_d8_w1_7_p4, n1byte_gatedsr_memory_d8_w1_8_p4;

  _3_8_decoder u_3_8_decoder_1 (
    .s0(select[0]), .s1(select[1]), .s2(select[2]), ._0(n3_8_decoder_1__0), ._1(n3_8_decoder_1__1),
    ._2(n3_8_decoder_1__2), ._3(n3_8_decoder_1__3), ._4(n3_8_decoder_1__4), ._5(n3_8_decoder_1__5),
    ._6(n3_8_decoder_1__6), ._7(n3_8_decoder_1__7));
  and AND (AND_out, write_enable, n3_8_decoder_1__0);
  and AND_2 (AND_2_out, write_enable, n3_8_decoder_1__1);
  and AND_3 (AND_3_out, write_enable, n3_8_decoder_1__2);
  and AND_4 (AND_4_out, write_enable, n3_8_decoder_1__3);
  and AND_5 (AND_5_out, write_enable, n3_8_decoder_1__4);
  and AND_6 (AND_6_out, write_enable, n3_8_decoder_1__5);
  and AND_7 (AND_7_out, write_enable, n3_8_decoder_1__6);
  and AND_8 (AND_8_out, write_enable, n3_8_decoder_1__7);
  // _1byte_gatedSR_memory_d8_w1 1byte_gatedsr_memory_d8_w1_1: pin names not known; wires that end beside it: data_in, RESET, AND_out, n1byte_gatedsr_memory_d8_w1_1_p4
  // _1byte_gatedSR_memory_d8_w1 1byte_gatedsr_memory_d8_w1_2: pin names not known; wires that end beside it: data_in, RESET, AND_2_out, n1byte_gatedsr_memory_d8_w1_2_p4
  // _1byte_gatedSR_memory_d8_w1 1byte_gatedsr_memory_d8_w1_3: pin names not known; wires that end beside it: data_in, RESET, AND_3_out, n1byte_gatedsr_memory_d8_w1_3_p4
  // _1byte_gatedSR_memory_d8_w1 1byte_gatedsr_memory_d8_w1_4: pin names not known; wires that end beside it: data_in, RESET, AND_4_out, n1byte_gatedsr_memory_d8_w1_4_p4
  // _1byte_gatedSR_memory_d8_w1 1byte_gatedsr_memory_d8_w1_5: pin names not known; wires that end beside it: data_in, RESET, AND_5_out, n1byte_gatedsr_memory_d8_w1_5_p4
  // _1byte_gatedSR_memory_d8_w1 1byte_gatedsr_memory_d8_w1_6: pin names not known; wires that end beside it: data_in, RESET, AND_6_out, n1byte_gatedsr_memory_d8_w1_6_p4
  // _1byte_gatedSR_memory_d8_w1 1byte_gatedsr_memory_d8_w1_7: pin names not known; wires that end beside it: data_in, RESET, AND_7_out, n1byte_gatedsr_memory_d8_w1_7_p4
  // _1byte_gatedSR_memory_d8_w1 1byte_gatedsr_memory_d8_w1_8: pin names not known; wires that end beside it: data_in, RESET, AND_8_out, n1byte_gatedsr_memory_d8_w1_8_p4
  // Probe on n1byte_gatedsr_memory_d8_w1_1_p4
  // Probe on n1byte_gatedsr_memory_d8_w1_2_p4
  // Probe on n1byte_gatedsr_memory_d8_w1_3_p4
  // Probe on n1byte_gatedsr_memory_d8_w1_4_p4
  // Probe on n1byte_gatedsr_memory_d8_w1_5_p4
  // Probe on n1byte_gatedsr_memory_d8_w1_6_p4
  // Probe on n1byte_gatedsr_memory_d8_w1_7_p4
  // Probe on n1byte_gatedsr_memory_d8_w1_8_p4
  Transistor #(.\type ("n"), .width(8)) transistor_1 (
    .in(n1byte_gatedsr_memory_d8_w1_1_p4), .out(data_out), .gate(n3_8_decoder_1__0));
  Transistor #(.\type ("n"), .width(8)) transistor_2 (
    .in(n1byte_gatedsr_memory_d8_w1_2_p4), .out(data_out), .gate(n3_8_decoder_1__1));
  Transistor #(.\type ("n"), .width(8)) transistor_3 (
    .in(n1byte_gatedsr_memory_d8_w1_3_p4), .out(data_out), .gate(n3_8_decoder_1__2));
  Transistor #(.\type ("n"), .width(8)) transistor_4 (
    .in(n1byte_gatedsr_memory_d8_w1_4_p4), .out(data_out), .gate(n3_8_decoder_1__3));
  Transistor #(.\type ("n"), .width(8)) transistor_5 (
    .in(n1byte_gatedsr_memory_d8_w1_5_p4), .out(data_out), .gate(n3_8_decoder_1__4));
  Transistor #(.\type ("n"), .width(8)) transistor_6 (
    .in(n1byte_gatedsr_memory_d8_w1_6_p4), .out(data_out), .gate(n3_8_decoder_1__5));
  Transistor #(.\type ("n"), .width(8)) transistor_7 (
    .in(n1byte_gatedsr_memory_d8_w1_7_p4), .out(data_out), .gate(n3_8_decoder_1__6));
  Transistor #(.\type ("n"), .width(8)) transistor_8 (
    .in(n1byte_gatedsr_memory_d8_w1_8_p4), .out(data_out), .gate(n3_8_decoder_1__7));
endmodule

module _16x1byte_memory_unit_4bitAddr (
  input  [3:0] select,
  input  [7:0] data_in,
  input  write_enable,
  input  RESET,
  output [7:0] data_out
);

  wire n2_4_decoder_1__0, n2_4_decoder_1__1, n2_4_decoder_1__2, n2_4_decoder_1__3, transistor_1_out,
       transistor_2_out, transistor_3_out, transistor_4_out;
  wire [7:0] n4x1byte_memory_unit_2bitaddr_1_data_out, n4x1byte_memory_unit_2bitaddr_2_data_out,
       n4x1byte_memory_unit_2bitaddr_3_data_out, n4x1byte_memory_unit_2bitaddr_4_data_out;

  _2_4_decoder u_2_4_decoder_1 (
    .s0(select[2]), .s1(select[3]), ._0(n2_4_decoder_1__0), ._1(n2_4_decoder_1__1), ._2(n2_4_decoder_1__2),
    ._3(n2_4_decoder_1__3));
  Transistor #(.\type ("n")) transistor_1 (.in(write_enable), .out(transistor_1_out), .gate(n2_4_decoder_1__0));
  Transistor #(.\type ("n")) transistor_2 (.in(write_enable), .out(transistor_2_out), .gate(n2_4_decoder_1__1));
  Transistor #(.\type ("n")) transistor_3 (.in(write_enable), .out(transistor_3_out), .gate(n2_4_decoder_1__2));
  Transistor #(.\type ("n")) transistor_4 (.in(write_enable), .out(transistor_4_out), .gate(n2_4_decoder_1__3));
  _4x1byte_memory_unit_2bitAddr u_4x1byte_memory_unit_2bitaddr_1 (
    .select(select[1:0]), .data_in(data_in), .write_enable(transistor_1_out), .RESET(RESET),
    .data_out(n4x1byte_memory_unit_2bitaddr_1_data_out));
  _4x1byte_memory_unit_2bitAddr u_4x1byte_memory_unit_2bitaddr_2 (
    .select(select[1:0]), .data_in(data_in), .write_enable(transistor_2_out), .RESET(RESET),
    .data_out(n4x1byte_memory_unit_2bitaddr_2_data_out));
  _4x1byte_memory_unit_2bitAddr u_4x1byte_memory_unit_2bitaddr_3 (
    .select(select[1:0]), .data_in(data_in), .write_enable(transistor_3_out), .RESET(RESET),
    .data_out(n4x1byte_memory_unit_2bitaddr_3_data_out));
  _4x1byte_memory_unit_2bitAddr u_4x1byte_memory_unit_2bitaddr_4 (
    .select(select[1:0]), .data_in(data_in), .write_enable(transistor_4_out), .RESET(RESET),
    .data_out(n4x1byte_memory_unit_2bitaddr_4_data_out));
  Transistor #(.\type ("n"), .width(8)) transistor_5 (
    .in(n4x1byte_memory_unit_2bitaddr_1_data_out), .out(data_out), .gate(n2_4_decoder_1__0));
  Transistor #(.\type ("n"), .width(8)) transistor_6 (
    .in(n4x1byte_memory_unit_2bitaddr_2_data_out), .out(data_out), .gate(n2_4_decoder_1__1));
  Transistor #(.\type ("n"), .width(8)) transistor_7 (
    .in(n4x1byte_memory_unit_2bitaddr_3_data_out), .out(data_out), .gate(n2_4_decoder_1__2));
  Transistor #(.\type ("n"), .width(8)) transistor_8 (
    .in(n4x1byte_memory_unit_2bitaddr_4_data_out), .out(data_out), .gate(n2_4_decoder_1__3));
endmodule

module _256x1byte_memory_unit_8bitAddr (
  input  [7:0] select,
  input  [7:0] data_in,
  input  write_enable,
  input  RESET,
  output [7:0] data_out
);

  wire n4_16_decoder_1_out_5, n4_16_decoder_1_out_6, n4_16_decoder_1_out_7, n4_16_decoder_1_out_8,
       n4_16_decoder_1_out_9, n4_16_decoder_1_out_10, n4_16_decoder_1_out_11, n4_16_decoder_1_out_12,
       n4_16_decoder_1_out_13, n4_16_decoder_1_out_14, n4_16_decoder_1_out_15, n4_16_decoder_1_out_16,
       n4_16_decoder_1_out_17, n4_16_decoder_1_out_18, n4_16_decoder_1_out_19, n4_16_decoder_1_out_20,
       transistor_1_out, transistor_2_out, transistor_3_out, transistor_4_out, transistor_5_out,
       transistor_6_out, transistor_7_out, transistor_8_out, transistor_17_out, transistor_18_out,
       transistor_19_out, transistor_20_out, transistor_21_out, transistor_22_out, transistor_23_out,
       transistor_24_out;
  wire [7:0] n16x1byte_memory_unit_4bitaddr_1_data_out, n16x1byte_memory_unit_4bitaddr_2_data_out,
       n16x1byte_memory_unit_4bitaddr_3_data_out, n16x1byte_memory_unit_4bitaddr_4_data_out,
       n16x1byte_memory_unit_4bitaddr_5_data_out, n16x1byte_memory_unit_4bitaddr_6_data_out,
       n16x1byte_memory_unit_4bitaddr_7_data_out, n16x1byte_memory_unit_4bitaddr_8_data_out,
       n16x1byte_memory_unit_4bitaddr_9_data_out, n16x1byte_memory_unit_4bitaddr_10_data_out,
       n16x1byte_memory_unit_4bitaddr_11_data_out, n16x1byte_memory_unit_4bitaddr_12_data_out,
       n16x1byte_memory_unit_4bitaddr_13_data_out, n16x1byte_memory_unit_4bitaddr_14_data_out,
       n16x1byte_memory_unit_4bitaddr_15_data_out, n16x1byte_memory_unit_4bitaddr_16_data_out;

  _4_16_decoder u_4_16_decoder_1 (
    .s0(select[0]), .s1(select[1]), .s2(select[2]), .s3(select[3]), .out_5(n4_16_decoder_1_out_5),
    .out_6(n4_16_decoder_1_out_6), .out_7(n4_16_decoder_1_out_7), .out_8(n4_16_decoder_1_out_8),
    .out_9(n4_16_decoder_1_out_9), .out_10(n4_16_decoder_1_out_10), .out_11(n4_16_decoder_1_out_11),
    .out_12(n4_16_decoder_1_out_12), .out_13(n4_16_decoder_1_out_13), .out_14(n4_16_decoder_1_out_14),
    .out_15(n4_16_decoder_1_out_15), .out_16(n4_16_decoder_1_out_16), .out_17(n4_16_decoder_1_out_17),
    .out_18(n4_16_decoder_1_out_18), .out_19(n4_16_decoder_1_out_19), .out_20(n4_16_decoder_1_out_20));
  Transistor #(.\type ("n"), .gate("br")) transistor_1 (
    .in(write_enable), .out(transistor_1_out), .gate(n4_16_decoder_1_out_5));
  Transistor #(.\type ("n"), .gate("br")) transistor_2 (
    .in(write_enable), .out(transistor_2_out), .gate(n4_16_decoder_1_out_6));
  Transistor #(.\type ("n"), .gate("br")) transistor_3 (
    .in(write_enable), .out(transistor_3_out), .gate(n4_16_decoder_1_out_7));
  Transistor #(.\type ("n"), .gate("br")) transistor_4 (
    .in(write_enable), .out(transistor_4_out), .gate(n4_16_decoder_1_out_8));
  Transistor #(.\type ("n"), .gate("br")) transistor_5 (
    .in(write_enable), .out(transistor_5_out), .gate(n4_16_decoder_1_out_9));
  Transistor #(.\type ("n"), .gate("br")) transistor_6 (
    .in(write_enable), .out(transistor_6_out), .gate(n4_16_decoder_1_out_10));
  Transistor #(.\type ("n"), .gate("br")) transistor_7 (
    .in(write_enable), .out(transistor_7_out), .gate(n4_16_decoder_1_out_11));
  Transistor #(.\type ("n"), .gate("br")) transistor_8 (
    .in(write_enable), .out(transistor_8_out), .gate(n4_16_decoder_1_out_12));
  _16x1byte_memory_unit_4bitAddr u_16x1byte_memory_unit_4bitaddr_1 (
    .select(select[7:4]), .data_in(data_in), .write_enable(transistor_1_out), .RESET(RESET),
    .data_out(n16x1byte_memory_unit_4bitaddr_1_data_out));
  _16x1byte_memory_unit_4bitAddr u_16x1byte_memory_unit_4bitaddr_2 (
    .select(select[7:4]), .data_in(data_in), .write_enable(transistor_2_out), .RESET(RESET),
    .data_out(n16x1byte_memory_unit_4bitaddr_2_data_out));
  _16x1byte_memory_unit_4bitAddr u_16x1byte_memory_unit_4bitaddr_3 (
    .select(select[7:4]), .data_in(data_in), .write_enable(transistor_3_out), .RESET(RESET),
    .data_out(n16x1byte_memory_unit_4bitaddr_3_data_out));
  _16x1byte_memory_unit_4bitAddr u_16x1byte_memory_unit_4bitaddr_4 (
    .select(select[7:4]), .data_in(data_in), .write_enable(transistor_4_out), .RESET(RESET),
    .data_out(n16x1byte_memory_unit_4bitaddr_4_data_out));
  _16x1byte_memory_unit_4bitAddr u_16x1byte_memory_unit_4bitaddr_5 (
    .select(select[7:4]), .data_in(data_in), .write_enable(transistor_5_out), .RESET(RESET),
    .data_out(n16x1byte_memory_unit_4bitaddr_5_data_out));
  _16x1byte_memory_unit_4bitAddr u_16x1byte_memory_unit_4bitaddr_6 (
    .select(select[7:4]), .data_in(data_in), .write_enable(transistor_6_out), .RESET(RESET),
    .data_out(n16x1byte_memory_unit_4bitaddr_6_data_out));
  _16x1byte_memory_unit_4bitAddr u_16x1byte_memory_unit_4bitaddr_7 (
    .select(select[7:4]), .data_in(data_in), .write_enable(transistor_7_out), .RESET(RESET),
    .data_out(n16x1byte_memory_unit_4bitaddr_7_data_out));
  _16x1byte_memory_unit_4bitAddr u_16x1byte_memory_unit_4bitaddr_8 (
    .select(select[7:4]), .data_in(data_in), .write_enable(transistor_8_out), .RESET(RESET),
    .data_out(n16x1byte_memory_unit_4bitaddr_8_data_out));
  Transistor #(.\type ("n"), .gate("br"), .width(8)) transistor_9 (
    .in(n16x1byte_memory_unit_4bitaddr_1_data_out), .out(data_out), .gate(n4_16_decoder_1_out_5));
  Transistor #(.\type ("n"), .gate("br"), .width(8)) transistor_10 (
    .in(n16x1byte_memory_unit_4bitaddr_2_data_out), .out(data_out), .gate(n4_16_decoder_1_out_6));
  Transistor #(.\type ("n"), .gate("br"), .width(8)) transistor_11 (
    .in(n16x1byte_memory_unit_4bitaddr_3_data_out), .out(data_out), .gate(n4_16_decoder_1_out_7));
  Transistor #(.\type ("n"), .gate("br"), .width(8)) transistor_12 (
    .in(n16x1byte_memory_unit_4bitaddr_4_data_out), .out(data_out), .gate(n4_16_decoder_1_out_8));
  Transistor #(.\type ("n"), .gate("br"), .width(8)) transistor_13 (
    .in(n16x1byte_memory_unit_4bitaddr_5_data_out), .out(data_out), .gate(n4_16_decoder_1_out_9));
  Transistor #(.\type ("n"), .gate("br"), .width(8)) transistor_14 (
    .in(n16x1byte_memory_unit_4bitaddr_6_data_out), .out(data_out), .gate(n4_16_decoder_1_out_10));
  Transistor #(.\type ("n"), .gate("br"), .width(8)) transistor_15 (
    .in(n16x1byte_memory_unit_4bitaddr_7_data_out), .out(data_out), .gate(n4_16_decoder_1_out_11));
  Transistor #(.\type ("n"), .gate("br"), .width(8)) transistor_16 (
    .in(n16x1byte_memory_unit_4bitaddr_8_data_out), .out(data_out), .gate(n4_16_decoder_1_out_12));
  Transistor #(.\type ("n"), .gate("br")) transistor_17 (
    .in(write_enable), .out(transistor_17_out), .gate(n4_16_decoder_1_out_13));
  Transistor #(.\type ("n"), .gate("br")) transistor_18 (
    .in(write_enable), .out(transistor_18_out), .gate(n4_16_decoder_1_out_14));
  Transistor #(.\type ("n"), .gate("br")) transistor_19 (
    .in(write_enable), .out(transistor_19_out), .gate(n4_16_decoder_1_out_15));
  Transistor #(.\type ("n"), .gate("br")) transistor_20 (
    .in(write_enable), .out(transistor_20_out), .gate(n4_16_decoder_1_out_16));
  Transistor #(.\type ("n"), .gate("br")) transistor_21 (
    .in(write_enable), .out(transistor_21_out), .gate(n4_16_decoder_1_out_17));
  Transistor #(.\type ("n"), .gate("br")) transistor_22 (
    .in(write_enable), .out(transistor_22_out), .gate(n4_16_decoder_1_out_18));
  Transistor #(.\type ("n"), .gate("br")) transistor_23 (
    .in(write_enable), .out(transistor_23_out), .gate(n4_16_decoder_1_out_19));
  Transistor #(.\type ("n"), .gate("br")) transistor_24 (
    .in(write_enable), .out(transistor_24_out), .gate(n4_16_decoder_1_out_20));
  _16x1byte_memory_unit_4bitAddr u_16x1byte_memory_unit_4bitaddr_9 (
    .select(select[7:4]), .data_in(data_in), .write_enable(transistor_17_out), .RESET(RESET),
    .data_out(n16x1byte_memory_unit_4bitaddr_9_data_out));
  _16x1byte_memory_unit_4bitAddr u_16x1byte_memory_unit_4bitaddr_10 (
    .select(select[7:4]), .data_in(data_in), .write_enable(transistor_18_out), .RESET(RESET),
    .data_out(n16x1byte_memory_unit_4bitaddr_10_data_out));
  _16x1byte_memory_unit_4bitAddr u_16x1byte_memory_unit_4bitaddr_11 (
    .select(select[7:4]), .data_in(data_in), .write_enable(transistor_19_out), .RESET(RESET),
    .data_out(n16x1byte_memory_unit_4bitaddr_11_data_out));
  _16x1byte_memory_unit_4bitAddr u_16x1byte_memory_unit_4bitaddr_12 (
    .data_in(data_in), .write_enable(transistor_20_out), .RESET(RESET),
    .data_out(n16x1byte_memory_unit_4bitaddr_12_data_out));  // open: select
  _16x1byte_memory_unit_4bitAddr u_16x1byte_memory_unit_4bitaddr_13 (
    .select(select[7:4]), .data_in(data_in), .write_enable(transistor_21_out), .RESET(RESET),
    .data_out(n16x1byte_memory_unit_4bitaddr_13_data_out));
  _16x1byte_memory_unit_4bitAddr u_16x1byte_memory_unit_4bitaddr_14 (
    .select(select[7:4]), .data_in(data_in), .write_enable(transistor_22_out), .RESET(RESET),
    .data_out(n16x1byte_memory_unit_4bitaddr_14_data_out));
  _16x1byte_memory_unit_4bitAddr u_16x1byte_memory_unit_4bitaddr_15 (
    .select(select[7:4]), .data_in(data_in), .write_enable(transistor_23_out), .RESET(RESET),
    .data_out(n16x1byte_memory_unit_4bitaddr_15_data_out));
  _16x1byte_memory_unit_4bitAddr u_16x1byte_memory_unit_4bitaddr_16 (
    .select(select[7:4]), .data_in(data_in), .write_enable(transistor_24_out), .RESET(RESET),
    .data_out(n16x1byte_memory_unit_4bitaddr_16_data_out));
  Transistor #(.\type ("n"), .gate("br"), .width(8)) transistor_25 (
    .in(n16x1byte_memory_unit_4bitaddr_9_data_out), .out(data_out), .gate(n4_16_decoder_1_out_13));
  Transistor #(.\type ("n"), .gate("br"), .width(8)) transistor_26 (
    .in(n16x1byte_memory_unit_4bitaddr_10_data_out), .out(data_out), .gate(n4_16_decoder_1_out_14));
  Transistor #(.\type ("n"), .gate("br"), .width(8)) transistor_27 (
    .in(n16x1byte_memory_unit_4bitaddr_11_data_out), .out(data_out), .gate(n4_16_decoder_1_out_15));
  Transistor #(.\type ("n"), .gate("br"), .width(8)) transistor_28 (
    .in(n16x1byte_memory_unit_4bitaddr_12_data_out), .out(data_out), .gate(n4_16_decoder_1_out_16));
  Transistor #(.\type ("n"), .gate("br"), .width(8)) transistor_29 (
    .in(n16x1byte_memory_unit_4bitaddr_13_data_out), .out(data_out), .gate(n4_16_decoder_1_out_17));
  Transistor #(.\type ("n"), .gate("br"), .width(8)) transistor_30 (
    .in(n16x1byte_memory_unit_4bitaddr_14_data_out), .out(data_out), .gate(n4_16_decoder_1_out_18));
  Transistor #(.\type ("n"), .gate("br"), .width(8)) transistor_31 (
    .in(n16x1byte_memory_unit_4bitaddr_15_data_out), .out(data_out), .gate(n4_16_decoder_1_out_19));
  Transistor #(.\type ("n"), .gate("br"), .width(8)) transistor_32 (
    .in(n16x1byte_memory_unit_4bitaddr_16_data_out), .out(data_out), .gate(n4_16_decoder_1_out_20));
endmodule

module _16x2byte_memory_unit_4bitAddr (
  input  reset,
  input  [15:0] data_in,
  input  [3:0] address,
  input  write_enable,
  output [15:0] data_out
);

  wire decoder_1_out0, decoder_1_out1, decoder_1_out2, decoder_1_out3, decoder_1_out4, decoder_1_out5,
       decoder_1_out6, decoder_1_out7, decoder_1_out8, decoder_1_out9, decoder_1_out10, decoder_1_out11,
       decoder_1_out12, decoder_1_out13, decoder_1_out14, decoder_1_out15;
  wire [15:0] n2byte_gatedsr_memory_d16_w1_1_data_out, n2byte_gatedsr_memory_d16_w1_2_data_out,
       n2byte_gatedsr_memory_d16_w1_3_data_out, n2byte_gatedsr_memory_d16_w1_4_data_out,
       n2byte_gatedsr_memory_d16_w1_5_data_out, n2byte_gatedsr_memory_d16_w1_6_data_out,
       n2byte_gatedsr_memory_d16_w1_7_data_out, n2byte_gatedsr_memory_d16_w1_8_data_out,
       n2byte_gatedsr_memory_d16_w1_9_data_out, n2byte_gatedsr_memory_d16_w1_10_data_out,
       n2byte_gatedsr_memory_d16_w1_11_data_out, n2byte_gatedsr_memory_d16_w1_12_data_out,
       n2byte_gatedsr_memory_d16_w1_13_data_out, n2byte_gatedsr_memory_d16_w1_14_data_out,
       n2byte_gatedsr_memory_d16_w1_15_data_out, n2byte_gatedsr_memory_d16_w1_16_data_out;

  Decoder #(.select(4), .disabled(0)) decoder_1 (
    .out0(decoder_1_out0), .out1(decoder_1_out1), .out2(decoder_1_out2), .out3(decoder_1_out3),
    .out4(decoder_1_out4), .out5(decoder_1_out5), .out6(decoder_1_out6), .out7(decoder_1_out7),
    .out8(decoder_1_out8), .out9(decoder_1_out9), .out10(decoder_1_out10), .out11(decoder_1_out11),
    .out12(decoder_1_out12), .out13(decoder_1_out13), .out14(decoder_1_out14), .out15(decoder_1_out15),
    .sel(address), .en(write_enable));
  _2byte_gatedSR_memory_d16_w1 u_2byte_gatedsr_memory_d16_w1_1 (
    .data_in(data_in), .write_enable(decoder_1_out0), .reset(reset),
    .data_out(n2byte_gatedsr_memory_d16_w1_1_data_out));
  _2byte_gatedSR_memory_d16_w1 u_2byte_gatedsr_memory_d16_w1_2 (
    .data_in(data_in), .write_enable(decoder_1_out1), .reset(reset),
    .data_out(n2byte_gatedsr_memory_d16_w1_2_data_out));
  _2byte_gatedSR_memory_d16_w1 u_2byte_gatedsr_memory_d16_w1_3 (
    .data_in(data_in), .write_enable(decoder_1_out2), .reset(reset),
    .data_out(n2byte_gatedsr_memory_d16_w1_3_data_out));
  _2byte_gatedSR_memory_d16_w1 u_2byte_gatedsr_memory_d16_w1_4 (
    .data_in(data_in), .write_enable(decoder_1_out3), .reset(reset),
    .data_out(n2byte_gatedsr_memory_d16_w1_4_data_out));
  _2byte_gatedSR_memory_d16_w1 u_2byte_gatedsr_memory_d16_w1_5 (
    .data_in(data_in), .write_enable(decoder_1_out4), .reset(reset),
    .data_out(n2byte_gatedsr_memory_d16_w1_5_data_out));
  _2byte_gatedSR_memory_d16_w1 u_2byte_gatedsr_memory_d16_w1_6 (
    .data_in(data_in), .write_enable(decoder_1_out5), .reset(reset),
    .data_out(n2byte_gatedsr_memory_d16_w1_6_data_out));
  _2byte_gatedSR_memory_d16_w1 u_2byte_gatedsr_memory_d16_w1_7 (
    .data_in(data_in), .write_enable(decoder_1_out6), .reset(reset),
    .data_out(n2byte_gatedsr_memory_d16_w1_7_data_out));
  _2byte_gatedSR_memory_d16_w1 u_2byte_gatedsr_memory_d16_w1_8 (
    .data_in(data_in), .write_enable(decoder_1_out7), .reset(reset),
    .data_out(n2byte_gatedsr_memory_d16_w1_8_data_out));
  _2byte_gatedSR_memory_d16_w1 u_2byte_gatedsr_memory_d16_w1_9 (
    .data_in(data_in), .write_enable(decoder_1_out8), .reset(reset),
    .data_out(n2byte_gatedsr_memory_d16_w1_9_data_out));
  _2byte_gatedSR_memory_d16_w1 u_2byte_gatedsr_memory_d16_w1_10 (
    .data_in(data_in), .write_enable(decoder_1_out9), .reset(reset),
    .data_out(n2byte_gatedsr_memory_d16_w1_10_data_out));
  _2byte_gatedSR_memory_d16_w1 u_2byte_gatedsr_memory_d16_w1_11 (
    .data_in(data_in), .write_enable(decoder_1_out10), .reset(reset),
    .data_out(n2byte_gatedsr_memory_d16_w1_11_data_out));
  _2byte_gatedSR_memory_d16_w1 u_2byte_gatedsr_memory_d16_w1_12 (
    .data_in(data_in), .write_enable(decoder_1_out11), .reset(reset),
    .data_out(n2byte_gatedsr_memory_d16_w1_12_data_out));
  _2byte_gatedSR_memory_d16_w1 u_2byte_gatedsr_memory_d16_w1_13 (
    .data_in(data_in), .write_enable(decoder_1_out12), .reset(reset),
    .data_out(n2byte_gatedsr_memory_d16_w1_13_data_out));
  _2byte_gatedSR_memory_d16_w1 u_2byte_gatedsr_memory_d16_w1_14 (
    .data_in(data_in), .write_enable(decoder_1_out13), .reset(reset),
    .data_out(n2byte_gatedsr_memory_d16_w1_14_data_out));
  _2byte_gatedSR_memory_d16_w1 u_2byte_gatedsr_memory_d16_w1_15 (
    .data_in(data_in), .write_enable(decoder_1_out14), .reset(reset),
    .data_out(n2byte_gatedsr_memory_d16_w1_15_data_out));
  _2byte_gatedSR_memory_d16_w1 u_2byte_gatedsr_memory_d16_w1_16 (
    .data_in(data_in), .write_enable(decoder_1_out15), .reset(reset),
    .data_out(n2byte_gatedsr_memory_d16_w1_16_data_out));
  Multiplexer #(.select(4), .width(16), .disabled(0), .enable("false")) multiplexer_1 (
    .in0(n2byte_gatedsr_memory_d16_w1_1_data_out), .in1(n2byte_gatedsr_memory_d16_w1_2_data_out),
    .in2(n2byte_gatedsr_memory_d16_w1_3_data_out), .in3(n2byte_gatedsr_memory_d16_w1_4_data_out),
    .in4(n2byte_gatedsr_memory_d16_w1_5_data_out), .in5(n2byte_gatedsr_memory_d16_w1_6_data_out),
    .in6(n2byte_gatedsr_memory_d16_w1_7_data_out), .in7(n2byte_gatedsr_memory_d16_w1_8_data_out),
    .in8(n2byte_gatedsr_memory_d16_w1_9_data_out), .in9(n2byte_gatedsr_memory_d16_w1_10_data_out),
    .in10(n2byte_gatedsr_memory_d16_w1_11_data_out), .in11(n2byte_gatedsr_memory_d16_w1_12_data_out),
    .in12(n2byte_gatedsr_memory_d16_w1_13_data_out), .in13(n2byte_gatedsr_memory_d16_w1_14_data_out),
    .in14(n2byte_gatedsr_memory_d16_w1_15_data_out), .in15(n2byte_gatedsr_memory_d16_w1_16_data_out),
    .out(data_out), .sel(address));
  Pull_Resistor pull_resistor_1 (.node(data_out));
endmodule

module _64x2byte_memory_unit_6bit_address (
  input  [15:0] data_in,
  input  reset,
  input  [5:0] address,
  input  write_enable,
  output [15:0] data_out
);

  wire decoder_1_out0, decoder_1_out1, decoder_1_out2, decoder_1_out3;
  wire [15:0] n16x2byte_memory_unit_4bitaddr_1_data_out, n16x2byte_memory_unit_4bitaddr_2_data_out,
       n16x2byte_memory_unit_4bitaddr_3_data_out, n16x2byte_memory_unit_4bitaddr_4_data_out;

  Decoder #(.select(2), .disabled(0)) decoder_1 (
    .out0(decoder_1_out0), .out1(decoder_1_out1), .out2(decoder_1_out2), .out3(decoder_1_out3),
    .sel(address[5:4]), .en(write_enable));
  _16x2byte_memory_unit_4bitAddr u_16x2byte_memory_unit_4bitaddr_1 (
    .data_in(data_in), .address(address[3:0]), .write_enable(decoder_1_out0), .reset(reset),
    .data_out(n16x2byte_memory_unit_4bitaddr_1_data_out));
  _16x2byte_memory_unit_4bitAddr u_16x2byte_memory_unit_4bitaddr_2 (
    .data_in(data_in), .address(address[3:0]), .write_enable(decoder_1_out1), .reset(reset),
    .data_out(n16x2byte_memory_unit_4bitaddr_2_data_out));
  _16x2byte_memory_unit_4bitAddr u_16x2byte_memory_unit_4bitaddr_3 (
    .data_in(data_in), .address(address[3:0]), .write_enable(decoder_1_out2), .reset(reset),
    .data_out(n16x2byte_memory_unit_4bitaddr_3_data_out));
  _16x2byte_memory_unit_4bitAddr u_16x2byte_memory_unit_4bitaddr_4 (
    .data_in(data_in), .address(address[3:0]), .write_enable(decoder_1_out3), .reset(reset),
    .data_out(n16x2byte_memory_unit_4bitaddr_4_data_out));
  Multiplexer #(.select(2), .width(16), .enable("false")) multiplexer_1 (
    .in0(n16x2byte_memory_unit_4bitaddr_1_data_out), .in1(n16x2byte_memory_unit_4bitaddr_2_data_out),
    .in2(n16x2byte_memory_unit_4bitaddr_3_data_out), .in3(n16x2byte_memory_unit_4bitaddr_4_data_out),
    .out(data_out), .sel(address[5:4]));
endmodule

module evan_hell (
  input  writeEnable,
  input  in_2,
  input  in_3
);

  wire nand_1_out, nand_2_out, nand_3_out, nand_4_out, nand_5_out, nand_6_out, nand_7_out, nand_8_out,
       nand_9_out, nand_10_out, nand_11_out, nand_12_out, not_1_out, not_2_out, not_3_out;

  not not_1 (not_1_out, in_2);
  not not_2 (not_2_out, not_3_out);
  not not_3 (not_3_out, not_1_out);
  // AND_Gate AND has open pins: in0=not_2_out, in1=in_2, out=open
  nand nand_1 (nand_1_out, in_3, writeEnable);
  nand nand_2 (nand_2_out, ~writeEnable, in_3);  // NAND_Gate
  nand nand_3 (nand_3_out, nand_1_out, nand_4_out);
  nand nand_4 (nand_4_out, nand_3_out, nand_2_out);
  LED led_1 (.in(nand_3_out));
  nand nand_5 (nand_5_out, in_3, nand_3_out);
  nand nand_6 (nand_6_out, ~nand_3_out, in_3);  // NAND_Gate
  LED led_2 (.in(nand_7_out));
  nand nand_7 (nand_7_out, nand_5_out, nand_8_out);
  nand nand_8 (nand_8_out, nand_7_out, nand_6_out);
  nand nand_9 (nand_9_out, in_3, nand_7_out);
  nand nand_10 (nand_10_out, ~nand_7_out, in_3);  // NAND_Gate
  LED led_3 (.in(nand_11_out));
  nand nand_11 (nand_11_out, nand_9_out, nand_12_out);
  nand nand_12 (nand_12_out, nand_11_out, nand_10_out);
endmodule

module _2_4_decoder_ENABLE (
  input  s0,
  input  s1,
  input  enable,
  output _0,
  output _1,
  output _2,
  output _3
);

  wire not_1_out, not_2_out;

  not not_1 (not_1_out, s0);
  not not_2 (not_2_out, s1);
  and AND (_0, not_1_out, enable, not_2_out);
  and AND_2 (_1, s0, enable, not_2_out);
  and AND_3 (_2, not_1_out, enable, s1);
  and AND_4 (_3, s0, enable, s1);
endmodule

module _2_4_decoder (
  input  s0,
  input  s1,
  output _0,
  output _1,
  output _2,
  output _3
);

  wire not_1_out, not_2_out;

  not not_1 (not_1_out, s0);
  not not_2 (not_2_out, s1);
  and AND (_0, not_1_out, not_2_out);
  and AND_2 (_1, s0, not_2_out);
  and AND_3 (_2, not_1_out, s1);
  and AND_4 (_3, s0, s1);
endmodule

module _3_8_decoder (
  input  s0,
  input  s1,
  input  s2,
  output _0,
  output _1,
  output _2,
  output _3,
  output _4,
  output _5,
  output _6,
  output _7
);

  wire not_1_out, not_2_out, not_3_out;

  not not_1 (not_1_out, s0);
  not not_2 (not_2_out, s1);
  not not_3 (not_3_out, s2);
  and AND (_0, not_1_out, not_2_out, not_3_out);
  and AND_2 (_1, s0, not_2_out, not_3_out);
  and AND_3 (_2, not_1_out, s1, not_3_out);
  and AND_4 (_3, s0, s1, not_3_out);
  and AND_5 (_4, not_1_out, not_2_out, s2);
  and AND_6 (_5, s0, not_2_out, s2);
  and AND_7 (_6, not_1_out, s1, s2);
  and AND_8 (_7, s0, s1, s2);
endmodule

module _4_16_decoder (
  input  s0,
  input  s1,
  input  s2,
  input  s3,
  output out_5,
  output out_6,
  output out_7,
  output out_8,
  output out_9,
  output out_10,
  output out_11,
  output out_12,
  output out_13,
  output out_14,
  output out_15,
  output out_16,
  output out_17,
  output out_18,
  output out_19,
  output out_20
);

  wire n2_4_decoder_1__0, n2_4_decoder_1__1, n2_4_decoder_1__2, n2_4_decoder_1__3;

  _2_4_decoder u_2_4_decoder_1 (
    .s0(s2), .s1(s3), ._0(n2_4_decoder_1__0), ._1(n2_4_decoder_1__1), ._2(n2_4_decoder_1__2),
    ._3(n2_4_decoder_1__3));
  _2_4_decoder_ENABLE u_2_4_decoder_enable_1 (
    .s0(s0), .s1(s1), .enable(n2_4_decoder_1__0), ._0(out_5), ._1(out_6), ._2(out_7), ._3(out_8));
  _2_4_decoder_ENABLE u_2_4_decoder_enable_2 (
    .s0(s0), .s1(s1), .enable(n2_4_decoder_1__1), ._0(out_9), ._1(out_10), ._2(out_11), ._3(out_12));
  _2_4_decoder_ENABLE u_2_4_decoder_enable_3 (
    .s0(s0), .s1(s1), .enable(n2_4_decoder_1__2), ._0(out_13), ._1(out_14), ._2(out_15), ._3(out_16));
  _2_4_decoder_ENABLE u_2_4_decoder_enable_4 (
    .s0(s0), .s1(s1), .enable(n2_4_decoder_1__3), ._0(out_17), ._1(out_18), ._2(out_19), ._3(out_20));
endmodule

module program_counter_2byte_definitely_not_how_you_do_it (
  input  reset,
  input  clock,
  input  write_enable,
  output [15:0] PCout,
  output [15:0] PCin
);

  wire AND_out;
  wire [15:0] controlled_buffer_1_out, full_adder_d16_w1_1_a_b, multiplexer_1_out;

  Multiplexer #(.select(2), .width(16), .disabled(0), .enable("false")) multiplexer_1 (
    .in0(full_adder_d16_w1_1_a_b), .in1({16{1'b0}}), .out(multiplexer_1_out), .sel({2{reset}}));  // open: in2, in3
  _2byte_gatedSR_memory_d16_w1 u_2byte_gatedsr_memory_d16_w1_1 (
    .data_in(multiplexer_1_out), .write_enable(clock), .reset(reset), .data_out(PCout));
  and AND (AND_out, clock, ~write_enable);  // AND_Gate
  // Probe on multiplexer_1_out
  // Probe on PCout
  assign controlled_buffer_1_out = AND_out ? PCout : 16'bz;  // Controlled_Buffer controlled_buffer_1
  full_adder_d16_w1 full_adder_d16_w1_1 (
    ._2byteA(controlled_buffer_1_out), ._2byteB({16{1'b0}}), .cin(AND_out), .a_b(full_adder_d16_w1_1_a_b));  // open: cout

  // Notes on the sheet:
  //   PCout: pull=down
  //   PCin: pull=down
endmodule

module _4b_up_counter_synch (
  input  CLOCK,
  output QD,
  output QC,
  output QB,
  output QA
);

  wire AND_2_out, AND_out, j_k_ff_3_qn;

  // Probe on {QA, QB, QC, QD}
  Clock #(.highDuration(20), .lowDuration(20)) clock_1 ();  // open: out
  J_K_Flip_Flop j_k_ff_1 (.J(1'b1), .clk(CLOCK), .K(1'b1), .Q(QD));  // open: Qn, preset, en, reset
  J_K_Flip_Flop j_k_ff_2 (.J(QD), .clk(CLOCK), .K(QD), .Q(QC));  // open: Qn, preset, en, reset
  and AND (AND_out, QD, QC);
  J_K_Flip_Flop j_k_ff_3 (.J(AND_out), .clk(CLOCK), .K(AND_out), .Q(QB), .Qn(j_k_ff_3_qn));  // open: preset, en, reset
  and AND_2 (AND_2_out, QB, AND_out);
  J_K_Flip_Flop j_k_ff_4 (.J(AND_2_out), .clk(CLOCK), .K(AND_2_out), .Q(QA));  // open: Qn, preset, en, reset

  // Notes on the sheet:
  //   QB: pull=down
  //   QC: pull=down
  //   QA: pull=down
  //   QD: pull=down
endmodule

module alu (
  input  [15:0] value_in,
  input  [15:0] value_out
);
endmodule

module _4b_down_counter_synch (
  input  CLOCK,
  output QD,
  output QC,
  output QB,
  output QA
);

  wire AND_2_out, AND_out, j_k_ff_1_qn, j_k_ff_2_qn, j_k_ff_3_qn;

  J_K_Flip_Flop j_k_ff_1 (.J(1'b1), .clk(CLOCK), .K(1'b1), .Q(QD), .Qn(j_k_ff_1_qn));  // open: preset, en, reset
  J_K_Flip_Flop j_k_ff_2 (
    .J(j_k_ff_1_qn), .clk(CLOCK), .K(j_k_ff_1_qn), .Q(QC), .Qn(j_k_ff_2_qn));  // open: preset, en, reset
  and AND (AND_out, j_k_ff_2_qn, j_k_ff_1_qn);
  J_K_Flip_Flop j_k_ff_3 (.J(AND_out), .clk(CLOCK), .K(AND_out), .Q(QB), .Qn(j_k_ff_3_qn));  // open: preset, en, reset
  and AND_2 (AND_2_out, j_k_ff_3_qn, AND_out);
  J_K_Flip_Flop j_k_ff_4 (.J(AND_2_out), .clk(CLOCK), .K(AND_2_out), .Q(QA));  // open: Qn, preset, en, reset

  // Notes on the sheet:
  //   QA: pull=down
  //   QC: pull=down
  //   QB: pull=down
  //   QD: pull=down
endmodule

module _4b_u_d_counter_synch (
  input  CLOCK,
  input  up_down,
  output QA,
  output QD,
  output QC,
  output QB
);

  wire AND_2_out, AND_3_out, AND_4_out, AND_5_out, AND_6_out, AND_out, j_k_ff_1_qn, j_k_ff_2_qn, j_k_ff_3_qn,
       not_1_out, OR_2_out, OR_3_out, OR_out;

  // Probe on {QA, QB, QC, QD}
  not not_1 (not_1_out, up_down);
  J_K_Flip_Flop j_k_ff_1 (.J(1'b1), .clk(CLOCK), .K(1'b1), .Q(QD), .Qn(j_k_ff_1_qn));  // open: preset, en, reset
  and AND (AND_out, QD, up_down);
  and AND_2 (AND_2_out, j_k_ff_1_qn, not_1_out);
  or OR (OR_out, AND_out, AND_2_out);
  J_K_Flip_Flop j_k_ff_2 (.J(OR_out), .clk(CLOCK), .K(OR_out), .Q(QC), .Qn(j_k_ff_2_qn));  // open: preset, en, reset
  and AND_3 (AND_3_out, AND_out, QC);
  and AND_4 (AND_4_out, j_k_ff_2_qn, AND_2_out);
  or OR_2 (OR_2_out, AND_3_out, AND_4_out);
  and AND_5 (AND_5_out, AND_3_out, QB);
  J_K_Flip_Flop j_k_ff_3 (
    .J(OR_2_out), .clk(CLOCK), .K(OR_2_out), .Q(QB), .Qn(j_k_ff_3_qn));  // open: preset, en, reset
  and AND_6 (AND_6_out, j_k_ff_3_qn, AND_4_out);
  or OR_3 (OR_3_out, AND_5_out, AND_6_out);
  J_K_Flip_Flop j_k_ff_4 (.J(OR_3_out), .clk(CLOCK), .K(OR_3_out), .Q(QA));  // open: Qn, preset, en, reset

  // Other names for the same wires on the sheet: clk = CLOCK

  // Notes on the sheet:
  //   QC: pull=down
  //   QA: pull=down
  //   QD: pull=down
  //   QB: pull=down
endmodule

module _4b_u_d_counter_write_synch (
  input  CLOCK,
  input  up_down,
  input  write_enable,
  input  [3:0] value_in,
  output QA,
  output QD,
  output QC,
  output QB
);

  wire AND_2_out, AND_3_out, AND_4_out, AND_5_out, AND_6_out, AND_7_out, AND_8_out, AND_9_out, AND_10_out,
       AND_11_out, AND_12_out, AND_13_out, AND_14_out, AND_out, j_k_ff_1_qn, j_k_ff_2_qn, j_k_ff_3_qn,
       not_1_out, OR_2_out, OR_3_out, OR_out;

  // Probe on {QA, QB, QC, QD}
  not not_1 (not_1_out, up_down);
  J_K_Flip_Flop j_k_ff_1 (
    .J(1'b1), .clk(CLOCK), .K(1'b1), .Q(QD), .Qn(j_k_ff_1_qn), .preset(AND_2_out), .reset(AND_out));  // open: en
  and AND (AND_out, write_enable, ~value_in[0]);  // AND_Gate
  and AND_2 (AND_2_out, write_enable, value_in[0]);
  and AND_3 (AND_3_out, QD, up_down);
  and AND_4 (AND_4_out, j_k_ff_1_qn, not_1_out);
  or OR (OR_out, AND_3_out, AND_4_out);
  J_K_Flip_Flop j_k_ff_2 (
    .J(OR_out), .clk(CLOCK), .K(OR_out), .Q(QC), .Qn(j_k_ff_2_qn), .preset(AND_6_out), .reset(AND_5_out));  // open: en
  and AND_5 (AND_5_out, write_enable, ~value_in[1]);  // AND_Gate
  and AND_6 (AND_6_out, write_enable, value_in[1]);
  and AND_7 (AND_7_out, AND_3_out, QC);
  and AND_8 (AND_8_out, j_k_ff_2_qn, AND_4_out);
  or OR_2 (OR_2_out, AND_7_out, AND_8_out);
  J_K_Flip_Flop j_k_ff_3 (
    .J(OR_2_out), .clk(CLOCK), .K(OR_2_out), .Q(QB), .Qn(j_k_ff_3_qn), .preset(AND_9_out), .reset(AND_10_out));  // open: en
  and AND_9 (AND_9_out, write_enable, value_in[2]);
  and AND_10 (AND_10_out, write_enable, ~value_in[2]);  // AND_Gate
  and AND_11 (AND_11_out, AND_7_out, QB);
  and AND_12 (AND_12_out, j_k_ff_3_qn, AND_8_out);
  or OR_3 (OR_3_out, AND_11_out, AND_12_out);
  and AND_13 (AND_13_out, write_enable, value_in[3]);
  J_K_Flip_Flop j_k_ff_4 (
    .J(OR_3_out), .clk(CLOCK), .K(OR_3_out), .Q(QA), .preset(AND_13_out), .reset(AND_14_out));  // open: Qn, en
  and AND_14 (AND_14_out, write_enable, ~value_in[3]);  // AND_Gate

  // Other names for the same wires on the sheet: clk = CLOCK

  // Notes on the sheet:
  //   QD: pull=down
  //   QA: pull=down
  //   QC: pull=down
  //   QB: pull=down
endmodule

module _16b_u_d_counter_synch (
  input  CLOCK,
  input  up_down,
  input  write_enable,
  input  [15:0] value_in,
  output [15:0] out_5
);

  wire AND_2_out, AND_3_out, AND_4_out, AND_5_out, AND_6_out, AND_7_out, AND_8_out, AND_9_out, AND_10_out,
       AND_11_out, AND_12_out, AND_13_out, AND_14_out, AND_15_out, AND_16_out, AND_17_out, AND_18_out,
       AND_19_out, AND_20_out, AND_21_out, AND_22_out, AND_23_out, AND_24_out, AND_25_out, AND_26_out,
       AND_27_out, AND_28_out, AND_29_out, AND_30_out, AND_31_out, AND_32_out, AND_33_out, AND_34_out,
       AND_35_out, AND_36_out, AND_37_out, AND_38_out, AND_39_out, AND_40_out, AND_41_out, AND_42_out,
       AND_43_out, AND_44_out, AND_45_out, AND_46_out, AND_47_out, AND_48_out, AND_49_out, AND_50_out,
       AND_51_out, AND_52_out, AND_53_out, AND_54_out, AND_55_out, AND_56_out, AND_57_out, AND_58_out,
       AND_59_out, AND_60_out, AND_61_out, AND_62_out, AND_63_out, AND_64_out, AND_out, j_k_ff_1_qn,
       j_k_ff_2_qn, j_k_ff_3_qn, j_k_ff_4_qn, j_k_ff_5_qn, j_k_ff_6_qn, j_k_ff_7_qn, j_k_ff_8_qn,
       j_k_ff_9_qn, j_k_ff_10_qn, j_k_ff_11_qn, j_k_ff_12_qn, j_k_ff_13_qn, j_k_ff_14_qn, j_k_ff_15_qn,
       j_k_ff_16_qn, not_1_out, OR_2_out, OR_3_out, OR_4_out, OR_5_out, OR_6_out, OR_7_out, OR_8_out,
       OR_9_out, OR_10_out, OR_11_out, OR_12_out, OR_13_out, OR_14_out, OR_15_out, OR_out, undriven,
       undriven_2, undriven_3, undriven_4;

  // Probe on out_5
  not not_1 (not_1_out, up_down);
  and AND (AND_out, write_enable, value_in[0]);
  J_K_Flip_Flop j_k_ff_1 (
    .J(1'b1), .clk(CLOCK), .K(1'b1), .Q(out_5[0]), .Qn(j_k_ff_1_qn), .preset(AND_out), .reset(AND_2_out));  // open: en
  and AND_2 (AND_2_out, write_enable, ~value_in[0]);  // AND_Gate
  and AND_3 (AND_3_out, out_5[0], up_down);
  and AND_4 (AND_4_out, j_k_ff_1_qn, not_1_out);
  or OR (OR_out, AND_3_out, AND_4_out);
  and AND_5 (AND_5_out, write_enable, value_in[1]);
  J_K_Flip_Flop j_k_ff_2 (
    .J(OR_out), .clk(CLOCK), .K(OR_out), .Q(out_5[1]), .Qn(j_k_ff_2_qn), .preset(AND_5_out), .reset(AND_6_out));  // open: en
  and AND_6 (AND_6_out, write_enable, ~value_in[1]);  // AND_Gate
  and AND_7 (AND_7_out, AND_3_out, out_5[1]);
  and AND_8 (AND_8_out, j_k_ff_2_qn, AND_4_out);
  or OR_2 (OR_2_out, AND_7_out, AND_8_out);
  and AND_9 (AND_9_out, write_enable, value_in[2]);
  J_K_Flip_Flop j_k_ff_3 (
    .J(OR_2_out), .clk(CLOCK), .K(OR_2_out), .Q(out_5[2]), .Qn(j_k_ff_3_qn), .preset(AND_9_out),
    .reset(AND_10_out));  // open: en
  and AND_10 (AND_10_out, write_enable, ~value_in[2]);  // AND_Gate
  and AND_11 (AND_11_out, AND_7_out, out_5[2]);
  and AND_12 (AND_12_out, j_k_ff_3_qn, AND_8_out);
  or OR_3 (OR_3_out, AND_11_out, AND_12_out);
  and AND_13 (AND_13_out, write_enable, value_in[3]);
  J_K_Flip_Flop j_k_ff_4 (
    .J(OR_3_out), .clk(CLOCK), .K(OR_3_out), .Q(out_5[3]), .Qn(j_k_ff_4_qn), .preset(AND_13_out),
    .reset(AND_14_out));  // open: en
  and AND_14 (AND_14_out, write_enable, ~value_in[3]);  // AND_Gate
  and AND_15 (AND_15_out, AND_11_out, out_5[3]);
  and AND_16 (AND_16_out, j_k_ff_4_qn, AND_12_out);
  or OR_4 (OR_4_out, AND_15_out, AND_16_out);
  and AND_17 (AND_17_out, write_enable, value_in[4]);
  J_K_Flip_Flop j_k_ff_5 (
    .J(OR_4_out), .clk(CLOCK), .K(OR_4_out), .Q(out_5[4]), .Qn(j_k_ff_5_qn), .preset(AND_17_out),
    .reset(AND_18_out));  // open: en
  and AND_18 (AND_18_out, write_enable, ~value_in[4]);  // AND_Gate
  and AND_19 (AND_19_out, AND_15_out, out_5[4]);
  and AND_20 (AND_20_out, j_k_ff_5_qn, AND_16_out);
  or OR_5 (OR_5_out, AND_19_out, AND_20_out);
  and AND_21 (AND_21_out, write_enable, value_in[5]);
  J_K_Flip_Flop j_k_ff_6 (
    .J(OR_5_out), .clk(CLOCK), .K(OR_5_out), .Q(out_5[5]), .Qn(j_k_ff_6_qn), .preset(AND_21_out),
    .reset(AND_22_out));  // open: en
  and AND_22 (AND_22_out, write_enable, ~value_in[5]);  // AND_Gate
  and AND_23 (AND_23_out, AND_19_out, out_5[5]);
  and AND_24 (AND_24_out, j_k_ff_6_qn, AND_20_out);
  or OR_6 (OR_6_out, AND_23_out, AND_24_out);
  and AND_25 (AND_25_out, write_enable, value_in[6]);
  J_K_Flip_Flop j_k_ff_7 (
    .J(OR_6_out), .clk(CLOCK), .K(OR_6_out), .Q(out_5[6]), .Qn(j_k_ff_7_qn), .preset(AND_25_out),
    .reset(AND_26_out));  // open: en
  and AND_26 (AND_26_out, write_enable, ~value_in[6]);  // AND_Gate
  and AND_27 (AND_27_out, AND_23_out, out_5[6]);
  and AND_28 (AND_28_out, j_k_ff_7_qn, AND_24_out);
  or OR_7 (OR_7_out, AND_27_out, AND_28_out);
  and AND_29 (AND_29_out, write_enable, value_in[7]);
  J_K_Flip_Flop j_k_ff_8 (
    .J(OR_7_out), .clk(CLOCK), .K(OR_7_out), .Q(out_5[7]), .Qn(j_k_ff_8_qn), .preset(AND_29_out),
    .reset(AND_30_out));  // open: en
  and AND_30 (AND_30_out, write_enable, ~value_in[7]);  // AND_Gate
  and AND_31 (AND_31_out, AND_27_out, out_5[7]);
  and AND_32 (AND_32_out, j_k_ff_8_qn, AND_28_out);
  or OR_8 (OR_8_out, AND_31_out, AND_32_out);
  and AND_33 (AND_33_out, write_enable, value_in[8]);
  J_K_Flip_Flop j_k_ff_9 (
    .J(OR_8_out), .clk(CLOCK), .K(OR_8_out), .Q(out_5[8]), .Qn(j_k_ff_9_qn), .preset(AND_33_out),
    .reset(AND_34_out));  // open: en
  and AND_34 (AND_34_out, write_enable, ~value_in[8]);  // AND_Gate
  and AND_35 (AND_35_out, AND_31_out, out_5[8]);
  and AND_36 (AND_36_out, j_k_ff_9_qn, AND_32_out);
  or OR_9 (OR_9_out, AND_35_out, AND_36_out);
  and AND_37 (AND_37_out, write_enable, value_in[9]);
  J_K_Flip_Flop j_k_ff_10 (
    .J(OR_9_out), .clk(CLOCK), .K(OR_9_out), .Q(out_5[9]), .Qn(j_k_ff_10_qn), .preset(AND_37_out),
    .reset(AND_38_out));  // open: en
  and AND_38 (AND_38_out, write_enable, ~value_in[9]);  // AND_Gate
  and AND_39 (AND_39_out, AND_35_out, out_5[9]);
  and AND_40 (AND_40_out, j_k_ff_10_qn, AND_36_out);
  or OR_10 (OR_10_out, AND_39_out, AND_40_out);
  and AND_41 (AND_41_out, write_enable, value_in[10]);
  J_K_Flip_Flop j_k_ff_11 (
    .J(OR_10_out), .clk(CLOCK), .K(OR_10_out), .Q(out_5[10]), .Qn(j_k_ff_11_qn), .preset(AND_41_out),
    .reset(AND_42_out));  // open: en
  and AND_42 (AND_42_out, write_enable, ~value_in[10]);  // AND_Gate
  and AND_43 (AND_43_out, AND_39_out, out_5[10]);
  and AND_44 (AND_44_out, j_k_ff_11_qn, AND_40_out);
  or OR_11 (OR_11_out, AND_43_out, AND_44_out);
  and AND_45 (AND_45_out, write_enable, value_in[11]);
  J_K_Flip_Flop j_k_ff_12 (
    .J(OR_11_out), .clk(CLOCK), .K(OR_11_out), .Q(out_5[11]), .Qn(j_k_ff_12_qn), .preset(AND_45_out),
    .reset(AND_46_out));  // open: en
  and AND_46 (AND_46_out, write_enable, ~value_in[11]);  // AND_Gate
  and AND_47 (AND_47_out, AND_43_out, out_5[11]);
  and AND_48 (AND_48_out, j_k_ff_12_qn, AND_44_out);
  or OR_12 (OR_12_out, AND_47_out, AND_48_out);
  and AND_49 (AND_49_out, write_enable, undriven);
  J_K_Flip_Flop j_k_ff_13 (
    .J(OR_12_out), .clk(CLOCK), .K(OR_12_out), .Q(out_5[12]), .Qn(j_k_ff_13_qn), .preset(AND_49_out),
    .reset(AND_50_out));  // open: en
  and AND_50 (AND_50_out, write_enable, ~undriven);  // AND_Gate
  and AND_51 (AND_51_out, AND_47_out, out_5[12]);
  and AND_52 (AND_52_out, j_k_ff_13_qn, AND_48_out);
  or OR_13 (OR_13_out, AND_51_out, AND_52_out);
  and AND_53 (AND_53_out, write_enable, undriven_2);
  J_K_Flip_Flop j_k_ff_14 (
    .J(OR_13_out), .clk(CLOCK), .K(OR_13_out), .Q(out_5[13]), .Qn(j_k_ff_14_qn), .preset(AND_53_out),
    .reset(AND_54_out));  // open: en
  and AND_54 (AND_54_out, write_enable, ~undriven_2);  // AND_Gate
  and AND_55 (AND_55_out, AND_51_out, out_5[13]);
  and AND_56 (AND_56_out, j_k_ff_14_qn, AND_52_out);
  or OR_14 (OR_14_out, AND_55_out, AND_56_out);
  and AND_57 (AND_57_out, write_enable, undriven_3);
  J_K_Flip_Flop j_k_ff_15 (
    .J(OR_14_out), .clk(CLOCK), .K(OR_14_out), .Q(out_5[14]), .Qn(j_k_ff_15_qn), .preset(AND_57_out),
    .reset(AND_58_out));  // open: en
  and AND_58 (AND_58_out, write_enable, ~undriven_3);  // AND_Gate
  and AND_59 (AND_59_out, AND_55_out, out_5[14]);
  and AND_60 (AND_60_out, j_k_ff_15_qn, AND_56_out);
  or OR_15 (OR_15_out, AND_59_out, AND_60_out);
  and AND_61 (AND_61_out, write_enable, undriven_4);
  J_K_Flip_Flop j_k_ff_16 (
    .J(OR_15_out), .clk(CLOCK), .K(OR_15_out), .Q(out_5[15]), .Qn(j_k_ff_16_qn), .preset(AND_61_out),
    .reset(AND_62_out));  // open: en
  and AND_62 (AND_62_out, write_enable, ~undriven_4);  // AND_Gate
  and AND_63 (AND_63_out, AND_59_out, out_5[15]);
  and AND_64 (AND_64_out, j_k_ff_16_qn, AND_60_out);

  // Other names for the same wires on the sheet: clk = CLOCK
endmodule

module _4x4_LED_matrix (
  input  inA,
  input  inA_2,
  input  inB,
  input  inB_2
);

  wire AND_2_out, AND_3_out, AND_4_out, AND_5_out, AND_6_out, AND_7_out, AND_8_out, AND_9_out, AND_10_out,
       AND_11_out, AND_12_out, AND_13_out, AND_14_out, AND_15_out, AND_16_out, AND_out, n2_4_decoder_1__0,
       n2_4_decoder_1__1, n2_4_decoder_1__2, n2_4_decoder_1__3, n2_4_decoder_2__0, n2_4_decoder_2__1,
       n2_4_decoder_2__2, n2_4_decoder_2__3;

  _2_4_decoder u_2_4_decoder_1 (
    .s0(inA_2), .s1(inA), ._0(n2_4_decoder_1__0), ._1(n2_4_decoder_1__1), ._2(n2_4_decoder_1__2),
    ._3(n2_4_decoder_1__3));
  LED led_1 (.in(AND_out));
  and AND (AND_out, n2_4_decoder_1__0, n2_4_decoder_2__0);
  LED led_2 (.in(AND_2_out));
  and AND_2 (AND_2_out, n2_4_decoder_1__1, n2_4_decoder_2__0);
  LED led_3 (.in(AND_3_out));
  and AND_3 (AND_3_out, n2_4_decoder_1__2, n2_4_decoder_2__0);
  LED led_4 (.in(AND_4_out));
  and AND_4 (AND_4_out, n2_4_decoder_1__3, n2_4_decoder_2__0);
  LED led_5 (.in(AND_5_out));
  and AND_5 (AND_5_out, n2_4_decoder_1__0, n2_4_decoder_2__1);
  and AND_6 (AND_6_out, n2_4_decoder_1__1, n2_4_decoder_2__1);
  LED led_6 (.in(AND_6_out));
  LED led_7 (.in(AND_7_out));
  and AND_7 (AND_7_out, n2_4_decoder_1__2, n2_4_decoder_2__1);
  and AND_8 (AND_8_out, n2_4_decoder_1__3, n2_4_decoder_2__1);
  LED led_8 (.in(AND_8_out));
  _2_4_decoder u_2_4_decoder_2 (
    .s0(inB_2), .s1(inB), ._0(n2_4_decoder_2__0), ._1(n2_4_decoder_2__1), ._2(n2_4_decoder_2__2),
    ._3(n2_4_decoder_2__3));
  and AND_9 (AND_9_out, n2_4_decoder_1__0, n2_4_decoder_2__2);
  LED led_9 (.in(AND_9_out));
  LED led_10 (.in(AND_10_out));
  and AND_10 (AND_10_out, n2_4_decoder_1__1, n2_4_decoder_2__2);
  LED led_11 (.in(AND_11_out));
  and AND_11 (AND_11_out, n2_4_decoder_1__2, n2_4_decoder_2__2);
  and AND_12 (AND_12_out, n2_4_decoder_1__3, n2_4_decoder_2__2);
  LED led_12 (.in(AND_12_out));
  and AND_13 (AND_13_out, n2_4_decoder_1__0, n2_4_decoder_2__3);
  LED led_13 (.in(AND_13_out));
  and AND_14 (AND_14_out, n2_4_decoder_1__1, n2_4_decoder_2__3);
  LED led_14 (.in(AND_14_out));
  and AND_15 (AND_15_out, n2_4_decoder_1__2, n2_4_decoder_2__3);
  LED led_15 (.in(AND_15_out));
  and AND_16 (AND_16_out, n2_4_decoder_1__3, n2_4_decoder_2__3);
  LED led_16 (.in(AND_16_out));
endmodule

module max_wtf_circuit_1gate (
  input  CLOCK,
  input  RESET_HOLD,
  output CLOCK_2
);

  wire NOR_out;

  nor NOR (NOR_out, RESET_HOLD, NOR_out);
  xor XOR (CLOCK_2, CLOCK, NOR_out);
endmodule

module max_wtf_circuit_1byte (
  output clock,
  output [7:0] data_out,
  output [7:0] data_in
);

  wire clock_1_out;

  Clock clock_1 (.out(clock_1_out));
  max_wtf_circuit_1gate max_wtf_circuit_1gate_1 ();  // open: RESET_HOLD, CLOCK, CLOCK_2
  max_wtf_circuit_1gate max_wtf_circuit_1gate_2 ();  // open: RESET_HOLD, CLOCK, CLOCK_2
  max_wtf_circuit_1gate max_wtf_circuit_1gate_3 ();  // open: RESET_HOLD, CLOCK, CLOCK_2
  max_wtf_circuit_1gate max_wtf_circuit_1gate_4 ();  // open: RESET_HOLD, CLOCK, CLOCK_2
  max_wtf_circuit_1gate max_wtf_circuit_1gate_5 ();  // open: RESET_HOLD, CLOCK, CLOCK_2
  max_wtf_circuit_1gate max_wtf_circuit_1gate_6 ();  // open: RESET_HOLD, CLOCK, CLOCK_2
  max_wtf_circuit_1gate max_wtf_circuit_1gate_7 ();  // open: RESET_HOLD, CLOCK, CLOCK_2
  max_wtf_circuit_1gate max_wtf_circuit_1gate_8 ();  // open: RESET_HOLD, CLOCK, CLOCK_2
endmodule

module max_wtf_circuit_v2 (
  input  RESET_HOLD,
  input  RESET_HOLD_2,
  input  RESET_HOLD_3,
  input  RESET_HOLD_4,
  input  RESET_HOLD_5,
  output [3:0] out_6
);

  wire NOR_2_out, NOR_3_out, NOR_4_out, NOR_5_out, NOR_out;

  nor NOR (NOR_out, RESET_HOLD, NOR_out);
  nor NOR_2 (NOR_2_out, RESET_HOLD_2, NOR_2_out);
  nor NOR_3 (NOR_3_out, RESET_HOLD_3, NOR_3_out);
  nor NOR_4 (NOR_4_out, RESET_HOLD_4, NOR_4_out);
  nor NOR_5 (NOR_5_out, RESET_HOLD_5, NOR_5_out);
  xor XOR (out_6[3], NOR_out, NOR_2_out);
  xor XOR_2 (out_6[2], NOR_out, NOR_3_out);
  xor XOR_3 (out_6[1], NOR_out, NOR_4_out);
  xor XOR_4 (out_6[0], NOR_out, NOR_5_out);
  // Probe on out_6
endmodule

module max_wtf_circuit_v3 (
);

  wire max_wtf_circuit_1gate_8_p1, max_wtf_circuit_1gate_8_p2;
  wire [7:0] max_wtf_circuit_1gate_1_clock_2;

  max_wtf_circuit_1gate max_wtf_circuit_1gate_1 (
    .CLOCK(max_wtf_circuit_1gate_8_p2), .CLOCK_2(max_wtf_circuit_1gate_1_clock_2[0]));  // open: RESET_HOLD
  max_wtf_circuit_1gate max_wtf_circuit_1gate_2 (
    .CLOCK(max_wtf_circuit_1gate_8_p2), .CLOCK_2(max_wtf_circuit_1gate_1_clock_2[1]));  // open: RESET_HOLD
  max_wtf_circuit_1gate max_wtf_circuit_1gate_3 (
    .CLOCK(max_wtf_circuit_1gate_8_p2), .CLOCK_2(max_wtf_circuit_1gate_1_clock_2[2]));  // open: RESET_HOLD
  max_wtf_circuit_1gate max_wtf_circuit_1gate_4 (
    .CLOCK(max_wtf_circuit_1gate_8_p2), .CLOCK_2(max_wtf_circuit_1gate_1_clock_2[3]));  // open: RESET_HOLD
  max_wtf_circuit_1gate max_wtf_circuit_1gate_5 (
    .CLOCK(max_wtf_circuit_1gate_8_p2), .CLOCK_2(max_wtf_circuit_1gate_1_clock_2[4]));  // open: RESET_HOLD
  max_wtf_circuit_1gate max_wtf_circuit_1gate_6 (
    .CLOCK(max_wtf_circuit_1gate_8_p2), .CLOCK_2(max_wtf_circuit_1gate_1_clock_2[5]));  // open: RESET_HOLD
  max_wtf_circuit_1gate max_wtf_circuit_1gate_7 (
    .CLOCK(max_wtf_circuit_1gate_8_p2), .CLOCK_2(max_wtf_circuit_1gate_1_clock_2[6]));  // open: RESET_HOLD
  // max_wtf_circuit_1gate max_wtf_circuit_1gate_8: pin names not known; wires that end beside it: max_wtf_circuit_1gate_8_p1, max_wtf_circuit_1gate_8_p2, max_wtf_circuit_1gate_8_p1, max_wtf_circuit_1gate_1_clock_2[7]
endmodule

module _2_1_mux (
  input  select,
  input  inA,
  input  inB,
  output out
);

  wire AND_2_out, AND_out, not_1_out;

  not not_1 (not_1_out, select);
  and AND (AND_out, not_1_out, inA);
  and AND_2 (AND_2_out, select, inB);
  or or_1 (out, AND_out, AND_2_out);

  // Notes on the sheet:
  //   out: pull=down
endmodule

module _4_2_mux (
  input  s0,
  input  d0,
  input  d1,
  input  d2,
  input  d3,
  output out0,
  output out1
);

  _2_1_mux u_2_1_mux_1 (.inA(d0), .inB(d2), .select(s0), .out(out0));
  _2_1_mux u_2_1_mux_2 (.inA(d1), .inB(d3), .select(s0), .out(out1));
endmodule

module aaaaa (
  input  in_1,
  input  in_2,
  input  in_3,
  input  in_4,
  input  in_5,
  input  in_6
);

  wire AND_2_out, AND_3_out, AND_4_out, AND_5_out, AND_6_out, AND_7_out, AND_8_out, AND_out, or_1_out;

  and AND (AND_out, ~in_1, ~in_2);  // AND_Gate
  and AND_2 (AND_2_out, ~in_1, in_2);  // AND_Gate
  and AND_3 (AND_3_out, in_1, ~in_2);  // AND_Gate
  and AND_4 (AND_4_out, in_1, in_2);
  and AND_5 (AND_5_out, in_3, AND_out);
  and AND_6 (AND_6_out, in_4, AND_2_out);
  and AND_7 (AND_7_out, in_5, AND_3_out);
  and AND_8 (AND_8_out, in_6, AND_4_out);
  or or_1 (or_1_out, AND_5_out, AND_6_out, AND_7_out, AND_8_out);
endmodule

module dram (
  input  x0,
  input  x1,
  input  y0,
  input  y1
);

  wire n2_4_decoder_1__0, n2_4_decoder_1__1, n2_4_decoder_1__2, n2_4_decoder_1__3, n2_4_decoder_2__0,
       n2_4_decoder_2__1, n2_4_decoder_2__2, n2_4_decoder_2__3;

  _2_4_decoder u_2_4_decoder_1 (
    .s0(y0), .s1(y1), ._0(n2_4_decoder_1__0), ._1(n2_4_decoder_1__1), ._2(n2_4_decoder_1__2),
    ._3(n2_4_decoder_1__3));
  _2_4_decoder u_2_4_decoder_2 (
    .s0(x1), .s1(x0), ._0(n2_4_decoder_2__0), ._1(n2_4_decoder_2__1), ._2(n2_4_decoder_2__2),
    ._3(n2_4_decoder_2__3));
  LED led_1 ();  // open: in
  LED led_2 ();  // open: in
endmodule

module _3bit_addressable_memory (
  input  value_in,
  input  value_in_2,
  input  value_in_3,
  input  value_in_4,
  input  value_in_5,
  input  value_in_6,
  input  value_in_7,
  input  addr0,
  input  value_in_8,
  input  addr1,
  input  addr2
);

  wire n3_8_decoder_1__0;

  _3_8_decoder u_3_8_decoder_1 (._0(n3_8_decoder_1__0));  // open: s0, s1, s2, _1, _2, _3, _4, _5, _6, _7
  // Probe on {addr2, addr1, addr0}
  // AND_Gate AND has open pins: in0=n3_8_decoder_1__0, in1=value_in, out=open
  // AND_Gate AND_2 has open pins: in0=value_in, in1=value_in_2, out=open
endmodule

module test23 (
  input  a,
  input  b,
  input  c
);

  wire transistor_1_out, transistor_2_out, transistor_5_out, transistor_7_out;

  Transistor transistor_1 (.in(1'b0), .out(transistor_1_out), .gate(c));
  Transistor transistor_2 (.in(transistor_1_out), .out(transistor_2_out), .gate(a));
  Transistor #(.\type ("n")) transistor_3 (.in(transistor_5_out), .out(transistor_2_out), .gate(a));
  Transistor #(.\type ("n")) transistor_4 (.in(1'b1), .out(transistor_2_out), .gate(c));
  Transistor #(.\type ("n")) transistor_5 (.in(1'b1), .out(transistor_5_out), .gate(b));
  Transistor transistor_6 (.in(transistor_1_out), .out(transistor_2_out), .gate(b));
  Transistor transistor_7 (.in(1'b0), .out(transistor_7_out), .gate(transistor_2_out));
  Transistor #(.\type ("n")) transistor_8 (.in(1'b1), .out(transistor_7_out), .gate(transistor_2_out));
endmodule
