// Logisim project test.circ as structural Verilog: 1 circuit, main circuit 2scomplement
module _2scomplement (
  input  x1,
  input  x2,
  input  x3,
  input  x4,
  input  x5,
  input  x,
  input  x2_2,
  input  x3_2,
  input  x1_2,
  input  x4_2,
  input  x2_3,
  input  x5_2,
  input  x3_3,
  output y1,
  output y2,
  output y3,
  output y4,
  output y5,
  output y1_2,
  output y2_2,
  output y3_2,
  output y1_3,
  output y4_2,
  output y2_3,
  output y5_2,
  output y3_3
);

  wire not_1_out, not_2_out, not_3_out, not_4_out;

  not not_1 (not_1_out, x2);
  not not_2 (not_2_out, x3);
  not not_3 (not_3_out, x4);
  not not_4 (not_4_out, x5);
  Transistor #(.\type ("n")) transistor_1 (.in(not_1_out), .out(y2), .gate(x1));
  Transistor transistor_2 (.in(x2), .out(y2), .gate(x1));
  Transistor #(.\type ("n")) transistor_3 (.in(not_2_out), .out(y3), .gate(x1));
  Transistor transistor_4 (.in(x3), .out(y3), .gate(x1));
  Transistor #(.\type ("n")) transistor_5 (.in(not_3_out), .out(y4), .gate(x1));
  Transistor transistor_6 (.in(x4), .out(y4), .gate(x1));
  Transistor #(.\type ("n")) transistor_7 (.in(not_4_out), .out(y5), .gate(x1));
  Transistor transistor_8 (.in(x5), .out(y5), .gate(x1));

  assign y1 = x1;
  assign y1_2 = x;
  assign y2_2 = x2_2;
  assign y3_2 = x3_2;
  assign y4_2 = x4_2;
  assign y5_2 = x5_2;

  // Notes on the sheet:
  //   n-long 2's complement circuit
  //   n-long 2's complement circuit
  //   n-long 2's complement circuit
endmodule
