// Logisim project weird_latch.circ as structural Verilog: 5 circuits, main circuit weird_latch_thing
module weird_latch_thing (
  input  d,
  input  s,
  input  a,
  input  b,
  output q,
  output sum,
  output carry
);

  wire not_1_out, or_1_out, or_2_out, or_3_out, undriven;

  not not_1 (not_1_out, s);
  or or_1 (or_1_out, q, d);
  or or_2 (or_2_out, d, not_1_out);
  or or_3 (or_3_out, s, q);
  // Probe on q
  and and_1 (q, or_1_out, or_2_out, or_3_out);
  xor XOR (sum, b, a);
  and AND_2 (carry, a, b);
  half_adder half_adder_1 (.b1(undriven));  // open: b2, sum, carry
endmodule

module half_adder (
  input  b1,
  input  b2,
  output sum,
  output carry
);

  xor XOR (sum, b2, b1);
  and AND (carry, b1, b2);
endmodule

module full_adder (
  input  b1,
  input  b2,
  input  cin,
  output s,
  output cout
);

  wire AND_2_out, AND_out, XOR_out;

  xor XOR (XOR_out, b1, b2);
  and AND (AND_out, XOR_out, cin);
  and AND_2 (AND_2_out, b2, b1);
  xor XOR_2 (s, XOR_out, cin);
  or OR (cout, AND_out, AND_2_out);
endmodule

module byte_adder (
  input  cin,
  input  a1,
  input  b1,
  input  a2,
  input  b2,
  input  a3,
  input  b3,
  input  a4,
  input  b4,
  input  a5,
  input  b5,
  input  a6,
  input  b6,
  input  a7,
  input  b7,
  input  a8,
  input  b8,
  output c1,
  output c2,
  output c3,
  output c4,
  output c5,
  output c6,
  output c7,
  output c8,
  output ccout
);

  wire full_adder_1_cout, full_adder_2_cout, full_adder_3_cout, full_adder_4_cout, full_adder_5_cout,
       full_adder_6_cout, full_adder_7_cout;

  full_adder full_adder_1 (.b1(a1), .b2(b1), .cin(cin), .s(c1), .cout(full_adder_1_cout));
  full_adder full_adder_2 (.b1(a2), .b2(b2), .cin(full_adder_1_cout), .s(c2), .cout(full_adder_2_cout));
  full_adder full_adder_3 (.b1(a3), .b2(b3), .cin(full_adder_2_cout), .s(c3), .cout(full_adder_3_cout));
  full_adder full_adder_4 (.b1(a4), .b2(b4), .cin(full_adder_3_cout), .s(c4), .cout(full_adder_4_cout));
  full_adder full_adder_5 (.b1(a5), .b2(b5), .cin(full_adder_4_cout), .s(c5), .cout(full_adder_5_cout));
  full_adder full_adder_6 (.b1(a6), .b2(b6), .cin(full_adder_5_cout), .s(c6), .cout(full_adder_6_cout));
  full_adder full_adder_7 (.b1(a7), .b2(b7), .cin(full_adder_6_cout), .s(c7), .cout(full_adder_7_cout));
  full_adder full_adder_8 (.b1(a8), .b2(b8), .cin(full_adder_7_cout), .s(c8), .cout(ccout));
endmodule

module test (
);

  wire byte_adder_1_ccout, clock_1_out;
  wire [3:0] byte_adder_1_c1, byte_adder_1_c5;

  byte_adder byte_adder_1 (
    .cin(1'b1), .a1(1'b0), .b1(1'b1), .a2(1'b1), .b2(1'b1), .a3(1'b0), .b3(1'b0), .a4(1'b1), .b4(1'b0),
    .a5(1'b0), .b5(1'b1), .a6(1'b0), .b6(1'b1), .a7(1'b0), .b7(1'b1), .a8(1'b0), .b8(1'b1),
    .c1(byte_adder_1_c1[0]), .c2(byte_adder_1_c1[1]), .c3(byte_adder_1_c1[2]), .c4(byte_adder_1_c1[3]),
    .c5(byte_adder_1_c5[0]), .c6(byte_adder_1_c5[1]), .c7(byte_adder_1_c5[2]), .c8(byte_adder_1_c5[3]),
    .ccout(byte_adder_1_ccout));
  Hex_Digit_Display hex_digit_display_1 (.value(byte_adder_1_c1));  // open: dp
  Hex_Digit_Display hex_digit_display_2 (.value(byte_adder_1_c5));  // open: dp
  Clock clock_1 (.out(clock_1_out));
  full_adder full_adder_1 ();  // open: b1, b2, cin, s, cout
endmodule
